// Logisim project 3-YuhangChen1.circ as structural Verilog: 21 circuits, main circuit ◇单周期RISC-V
module \单周期RISC_V  (
  input  IR1,
  input  IR2,
  input  IR3,
  output RegWrite,
  output MemWrite,
  output [31:0] PC,
  output [31:0] IR,
  output [31:0] RDin,
  output [31:0] MDin,
  output [31:0] LedData
);

  wire and_1_out, and_3_out, and_4_out, and_5_out, and_7_out, Beq, bgue, Bne, CLK, clock_1_out,
       comparator_1_eq, comparator_2_eq, comparator_3_eq, comparator_3_lt, d_ff_1_q, ecall, equal, gequal,
       Go, halt, IR1_t, IR2_t, IR3_t, IRA, IRB, IRC, is_lb, JAL, JALR, keep, less, MemToReg, nand_1_out,
       not_1_out, not_2_out, not_3_out, or_1_out, or_5_out, register_1_q, riscv_probe_1_p2, RST, S_type, W1,
       W2, W3, \单周期硬布线控制器_1_alu_src ;
  wire [1:0] priority_encoder_1_out, priority_encoder_2_out;
  wire [3:0] \单周期硬布线控制器_1_alu_op ;
  wire [4:0] multiplexer_2_out, multiplexer_3_out;
  wire [7:0] multiplexer_7_out;
  wire [11:0] multiplexer_4_out;
  wire [12:0] CNT_num;
  wire [15:0] \总周期数 ;
  wire [31:0] Alu_out, Alu_out2, and_2_out, bit_extender_1_out, bit_extender_2_out, bit_extender_3_out,
       bit_extender_4_out, bout, jout, load, Mout, multiplexer_1_out, multiplexer_5_out, PC_4, R1,
       shifter_1_out, shifter_2_out;

  Button \u_继续运行  (.out(Go));
  Button _1 (.out(IRA));
  Button _2 (.out(IRB));
  Button _3 (.out(IRC));
  LED #(.active("true")) led_1 (.in(W1));
  LED #(.active("true")) led_2 (.in(W2));
  LED #(.active("true")) led_3 (.in(W3));
  and and_1 (and_1_out, gequal, bgue);
  assign and_2_out = Alu_out & 32'hfffffffe;  // AND_Gate and_2, 32 bits wide
  Hex_Digit_Display hex_digit_display_1 (.value(LedData[31:28]));  // open: dp
  not not_1 (not_1_out, equal);
  and and_3 (and_3_out, not_1_out, Bne);
  and and_4 (and_4_out, Beq, equal);
  or or_1 (or_1_out, and_1_out, and_4_out, and_3_out);
  Priority_Encoder #(.select(2), .disabled("Z")) priority_encoder_1 (
    .in0(1'b1), .in1(or_1_out), .in2(JAL), .in3(JALR), .out(priority_encoder_1_out));  // open: gs, en_out, en_in
  Multiplexer #(.select(2), .width(32), .disabled("Z"), .enable("false")) multiplexer_1 (
    .in0(PC_4), .in1(bout), .in2(jout), .in3(and_2_out), .out(multiplexer_1_out), .sel(priority_encoder_1_out));
  not not_2 (not_2_out, halt);
  Hex_Digit_Display hex_digit_display_2 (.value(LedData[27:24]));  // open: dp
  Hex_Digit_Display hex_digit_display_3 (.value(LedData[23:20]));  // open: dp
  Register #(.width(32), .trigger("rising"), .Select("low")) u_PC (
    .D(multiplexer_1_out), .en(not_2_out), .Q(PC), .clk(CLK), .clr(RST));
  Hex_Digit_Display hex_digit_display_4 (.value(LedData[19:16]));  // open: dp
  Hex_Digit_Display hex_digit_display_5 (.value(LedData[15:12]));  // open: dp
  Hex_Digit_Display hex_digit_display_6 (.value(LedData[11:8]));  // open: dp
  Hex_Digit_Display hex_digit_display_7 (.value(LedData[7:4]));  // open: dp
  // Probe on \总周期数 
  Adder #(.width(32)) adder_1 (.a(PC), .b(32'h4), .out(PC_4));  // open: cin, cout
  Hex_Digit_Display hex_digit_display_8 (.value(LedData[3:0]));  // open: dp
  // RiscV_Probe riscv_probe_1: pin names not known; wires that end beside it: IR, riscv_probe_1_p2
  ROM #(.addrWidth(10), .dataWidth(32), .Select("high")) rom_1 (.addr(PC[11:2]), .data(IR));
  or or_2 (IR1_t, IR1, IRA);
  Comparator #(.width(32), .mode("twosComplement")) comparator_1 (
    .a(R1), .b(32'h22), .eq(comparator_1_eq));  // open: gt, lt
  Comparator #(.width(32), .mode("twosComplement")) comparator_2 (
    .a(R1), .b(32'h22), .eq(comparator_2_eq));  // open: gt, lt
  Register #(.width(1), .trigger("falling"), .Select("low")) register_1 (
    .D(1'b0), .Q(register_1_q), .clk(keep), .preset(Go));  // open: en, clr, cs
  or or_3 (IR2_t, IR2, IRB);
  \单周期硬布线控制器  \u_单周期硬布线控制器_1  (
    .Funct({IR[30], IR[25], IR[14:12]}), .OP(IR[6:2]), .ALU_OP(\单周期硬布线控制器_1_alu_op ), .MemToReg(MemToReg),
    .MemWrite(MemWrite), .ALU_SRC(\单周期硬布线控制器_1_alu_src ), .RegWrite(RegWrite), .ecall(ecall),
    .S_type(S_type), .Jalr(JALR), .Beq(Beq), .JAL(JAL), .Bne(Bne), .in_3(IR[21]), .uret(riscv_probe_1_p2),
    .is_lb(is_lb), .bgue(bgue));  // open: rs1_used, rs2_used
  Multiplexer #(.select(1), .width(5), .disabled("Z"), .enable("false")) multiplexer_2 (
    .in0(IR[19:15]), .in1(5'b10001), .out(multiplexer_2_out), .sel(ecall));
  Multiplexer #(.select(1), .width(5), .disabled("Z"), .enable("false")) multiplexer_3 (
    .in0(IR[24:20]), .in1(5'b01010), .out(multiplexer_3_out), .sel(ecall));
  Multiplexer #(.select(1), .width(12), .disabled("Z"), .enable("false")) multiplexer_4 (
    .in0(IR[31:20]), .in1({IR[31:25], IR[11:7]}), .out(multiplexer_4_out), .sel(S_type));
  and and_5 (and_5_out, ecall, comparator_1_eq);
  and and_6 (keep, ecall, not_3_out);
  not not_3 (not_3_out, comparator_2_eq);
  and and_7 (and_7_out, ~register_1_q, keep);  // AND_Gate
  assign bit_extender_1_out = {{20{IR[31]}}, {IR[31], IR[7], IR[30:25], IR[11:8]}};  // Bit_Extender bit_extender_1
  assign bit_extender_2_out = {{12{IR[31]}}, {IR[31], IR[19:12], IR[20], IR[30:21]}};  // Bit_Extender bit_extender_2
  Register #(.width(32), .trigger("rising"), .Select("low")) register_2 (
    .D(MDin), .en(and_5_out), .Q(LedData), .clk(CLK));  // open: clr
  Register #(.width(1), .trigger("falling"), .Select("low")) register_3 (
    .D(and_7_out), .Q(halt), .clk(CLK));  // open: en, clr
  or or_4 (IR3_t, IR3, IRC);
  assign bit_extender_3_out = {{20{multiplexer_4_out[11]}}, multiplexer_4_out};  // Bit_Extender bit_extender_3
  Shifter #(.width(32), .shift("ll")) shifter_1 (.in(bit_extender_1_out), .\dist (5'b00001), .out(shifter_1_out));
  Shifter #(.width(32), .shift("ll")) shifter_2 (.in(bit_extender_2_out), .\dist (5'b00001), .out(shifter_2_out));
  Regifile regifile_1 (
    .Din(RDin), .Clk(CLK), .R1(R1), .R2(MDin), .WE(RegWrite), .W_num(IR[11:7]), .R1_num(multiplexer_2_out),
    .R2_num(multiplexer_3_out));
  Adder #(.width(32)) adder_2 (.a(shifter_1_out), .b(PC), .out(bout));  // open: cin, cout
  Adder #(.width(32)) adder_3 (.a(shifter_2_out), .b(PC), .out(jout));  // open: cin, cout
  Multiplexer #(.select(1), .width(32), .disabled("Z"), .enable("false")) multiplexer_5 (
    .in0(MDin), .in1(bit_extender_3_out), .out(multiplexer_5_out), .sel(\单周期硬布线控制器_1_alu_src ));
  ALU alu_1 (
    .X(R1), .Y(multiplexer_5_out), .AluOP(\单周期硬布线控制器_1_alu_op ), .Equal(equal), .Result(Alu_out),
    .Result_2(Alu_out2), .out_4(gequal), .out_6(less));
  or or_5 (or_5_out, JAL, JALR);
  Priority_Encoder #(.select(2), .disabled("Z")) priority_encoder_2 (
    .in0(1'b1), .in1(or_5_out), .in2(MemToReg), .in3(1'b0), .out(priority_encoder_2_out));  // open: gs, en_out, en_in
  D_Flip_Flop #(.trigger("high"), .Pre_Clr_Positions("LEGACY"), .NegatePresetClear("false"), .enable("true"), .NewFFLayout("false")) d_ff_1 (.Q(d_ff_1_q));  // open: clk, D, Qn, preset, en, reset
  // Probe on 13'h123
  Comparator #(.width(13), .mode("twosComplement")) comparator_3 (
    .a(CNT_num), .b(13'h123), .eq(comparator_3_eq), .lt(comparator_3_lt));  // open: gt
  Clock #(.highDuration(1), .lowDuration(1)) clock_1 (.out(clock_1_out));
  RAM #(.addrWidth(10), .dataWidth(32), .bus("separate"), .Select("high")) ram_1 (
    .addr(Alu_out[11:2]), .din(MDin), .data(Mout), .str(MemWrite), .sel(1'b1), .clk(CLK), .ld(MemToReg),
    .clr(1'b0));
  Counter #(.width(13), .max('h1fff), .ongoal("stay"), .trigger("rising"), .behavior("old")) counter_1 (
    .count(comparator_3_lt), .Q(CNT_num), .clk(clock_1_out));  // open: load, D, carry, clr, preset
  Multiplexer #(.select(2), .width(32), .disabled("Z"), .enable("false")) multiplexer_6 (
    .in0(Alu_out), .in1(PC_4), .in2(load), .out(RDin), .sel(priority_encoder_2_out));  // open: in3
  nand nand_1 (nand_1_out, d_ff_1_q, comparator_3_eq);
  assign CLK = nand_1_out ? clock_1_out : 1'bz;  // Controlled_Buffer controlled_buffer_1
  Pull_Resistor #(.pull(1)) pull_resistor_1 (.node(CLK));
  Multiplexer #(.select(2), .width(8), .disabled("Z"), .enable("false")) multiplexer_7 (
    .in0(Mout[7:0]), .in1(Mout[15:8]), .in2(Mout[23:16]), .in3(Mout[31:24]), .out(multiplexer_7_out),
    .sel(Alu_out[1:0]));
  assign bit_extender_4_out = {{24{multiplexer_7_out[7]}}, multiplexer_7_out};  // Bit_Extender bit_extender_4
  Multiplexer #(.select(1), .width(32), .disabled("Z"), .enable("false")) multiplexer_8 (
    .in0(Mout), .in1(bit_extender_4_out), .out(load), .sel(is_lb));

  // Other names for the same wires on the sheet: R2[31:0] = MDin

  // Notes on the sheet:
  //   中断源
  //   中断等待指示
  //   数码管输出
  //   数码管输出应该用寄存器锁存，否则显示数据只能一闪而过
  //   指令存储器
  //   指令探针
  //   contents of rom_1 (hex, n*v repeats v):
  //   100493 100006f 100493 200913 300993 100006f 100493 200913 300993 100006f 100493 200913 300993
  //   100006f 100493 200913 300993 29c000ef 100413 100493 1f49493 900533 2200893 73 24d493 48463 fedff06f
  //   900533 2200893 73 100493 249493 900533 2200893 73 48463 fedff06f 100493 1f49493 900533 2200893 73
  //   4034d493 900533 2200893 73 4044d493 900533 2200893 73 4044d493 900533 2200893 73 4044d493 900533
  //   2200893 73 4044d493 900533 2200893 73 4044d493 900533 2200893 73 4044d493 900533 2200893 73 4044d493
  //   900533 2200893 73 100413 1f41993 41f9d993 433 c00913 300b13 140413 f47413 800293 100313 499993
  //   89e9b3 1300533 2200893 73 406282b3 fe0294e3 140413 f00f93 1f47433 1c41413 800293 100313 49d993
  //   89e9b3 1300533 2200893 73 406282b3 fe0294e3 1c45413 406b0b33 b0463 f95ff06f 2b3 fff2c293 829293
  //   ff2e293 500533 2200893 73 fff00413 493 84a023 140413 448493 84a023 140413 448493 84a023 140413
  //   448493 84a023 140413 448493 84a023 140413 448493 84a023 140413 448493 84a023 140413 448493 84a023
  //   140413 448493 84a023 140413 448493 84a023 140413 448493 84a023 140413 448493 84a023 140413 448493
  //   84a023 140413 448493 84a023 140413 448493 84a023 140413 448493 84a023 140413 448493 140413 433
  //   3c00493 42983 4aa03 149a2b3 28663 134a023 1442023 ffc48493 fe9412e3 800533 2200893 73 440413 3c00493
  //   fc9416e3 a00893 73 413 140413 800533 2200893 73 240413 800533 2200893 73 340413 800533 2200893 73
  //   440413 800533 2200893 73 540413 800533 2200893 73 640413 800533 2200893 73 740413 800533 2200893 73
  //   840413 800533 2200893 2200893 73 8067
  //   keep信号为1表示暂停
  //   JAL
  //   JALR
  //   指令字
  //   b型
  //   j型
  //   Led显示，注意我们需要锁存，且我们在a7！=34的时候要暂停
  //   由于会出现毛刺问题，我们需要用寄存器以及
  //   Beq
  //   Bne
  //   URET
  //   MemToReg
  //   MemWrite
  //   AluOP
  //   AluSrcB
  //   RegWrite
  //   0是正常1是暂停（因为我们后面有一个非门）
  //   jal和jalr传给pc的值不一样
  //   为方便自动评测，需要输出PC，IR，寄存器堆写如数据RDin
  //   RAM写使能MemWrite、RAM写入数据MDin等信号
  //   处理sw，写入Mdatain
  //   控制位
  //   暂停节拍，不能为0
  //   戳工具置1进入计数暂停模式，ctrl+k时钟自动运行到对应节拍暂停
  //   ctrl+k关闭时钟连续运行，将控制位置零，进入单步调试模式调试
  //   用这个时钟源需要去掉电路中的其他时钟源
  //   数据存储器
  //   可计数暂停的时钟源
  //   rdin分三种情况，正常r型指令要aluout，j型要pc4，最后是lw和lb
  //   区分lb和lw，写入寄存器
endmodule

// 单周期硬布线控制器
module \单周期硬布线控制器  (
  input  [4:0] OP,
  input  [4:0] Funct,
  input  in_3,
  output [3:0] ALU_OP,
  output uret,
  output rs2_used,
  output rs1_used,
  output MemToReg,
  output ecall,
  output MemWrite,
  output ALU_SRC,
  output is_lb,
  output RegWrite,
  output S_type,
  output Beq,
  output Bne,
  output Jalr,
  output JAL,
  output bgue
);

  wire \控制信号自动生成_1_ecall ;

  \运算控制器自动生成  \u_运算控制器自动生成_1  (
    .OP2(OP[0]), .OP3(OP[1]), .OP4(OP[2]), .OP5(OP[3]), .OP6(OP[4]), .F12(Funct[0]), .F13(Funct[1]),
    .F14(Funct[2]), .F25(Funct[3]), .F30(Funct[4]), .S0(ALU_OP[0]), .S1(ALU_OP[1]), .S2(ALU_OP[2]),
    .S3(ALU_OP[3]));
  \控制信号自动生成  \u_控制信号自动生成_1  (
    .OP2(OP[0]), .OP3(OP[1]), .OP4(OP[2]), .OP5(OP[3]), .MemToReg(MemToReg), .OP6(OP[4]), .F12(Funct[0]),
    .F13(Funct[1]), .F14(Funct[2]), .F25(Funct[3]), .F30(Funct[4]), .MemWrite(MemWrite), .ALU_SRC(ALU_SRC),
    .is_lb(is_lb), .RegWrite(RegWrite), .ecall(\控制信号自动生成_1_ecall ), .S_Type(S_type), .BEQ(Beq), .BNE(Bne),
    .JALR(Jalr), .JAL(JAL), .bgeu(bgue), .rs1_used(rs1_used), .rs2_used(rs2_used));
  and and_1 (uret, in_3, \控制信号自动生成_1_ecall );
  and and_2 (ecall, ~in_3, \控制信号自动生成_1_ecall );  // AND_Gate

  // Other names for the same wires on the sheet: IR21 = in_3; OP_CODE[4:0] = OP

  // Notes on the sheet:
  //   运算器控制器，根据指令生成运算器功能选择信号
  //   控制信号生成，产生数据通路需要的其他控制信号
endmodule

// 运算器控制器
module \运算控制器自动生成  (
  input  OP2,
  input  OP3,
  input  OP4,
  input  OP5,
  input  OP6,
  input  F12,
  input  F13,
  input  F14,
  input  F25,
  input  F30,
  output S0,
  output S1,
  output S2,
  output S3
);

  wire and_1_out, and_2_out, and_3_out, and_4_out, and_5_out, and_6_out, and_7_out, and_8_out, and_9_out,
       and_10_out, and_11_out, and_12_out, and_13_out, and_14_out, and_15_out, and_16_out, and_17_out,
       and_18_out, and_19_out, and_20_out, and_21_out, and_22_out, and_23_out, and_24_out, and_25_out,
       and_26_out, and_27_out, and_28_out, and_29_out, and_30_out, and_31_out, and_32_out, and_33_out,
       and_34_out, and_35_out, and_36_out, and_37_out, and_38_out, and_39_out, and_40_out, and_41_out,
       and_42_out, and_43_out, and_44_out, and_45_out, and_46_out, not_1_out, not_2_out, not_3_out,
       not_4_out, not_5_out, not_6_out, not_7_out, not_8_out, not_9_out, not_10_out, not_11_out, not_12_out,
       not_13_out, not_14_out, not_15_out, not_16_out, not_17_out, not_18_out, not_19_out, not_20_out,
       not_21_out, not_22_out, not_23_out, not_24_out, not_25_out, not_26_out, not_27_out, not_28_out,
       not_29_out, not_30_out, not_31_out, not_32_out, not_33_out, not_34_out, not_35_out, not_36_out,
       not_37_out, not_38_out, not_39_out, not_40_out, not_41_out, not_42_out, not_43_out, not_44_out,
       not_45_out, not_46_out, not_47_out, not_48_out, not_49_out, not_50_out, not_51_out, not_52_out,
       not_53_out, not_54_out, not_55_out, not_56_out, not_57_out, not_58_out, not_59_out, not_60_out,
       not_61_out, not_62_out, not_63_out, not_64_out, not_65_out, not_66_out, not_67_out, not_68_out,
       not_69_out, not_70_out, not_71_out, not_72_out, not_73_out, not_74_out, not_75_out, not_76_out,
       not_77_out, not_78_out, not_79_out, not_80_out, not_81_out, not_82_out, not_83_out, not_84_out,
       not_85_out, not_86_out, not_87_out, not_88_out, not_89_out, not_90_out, not_91_out, not_92_out,
       not_93_out, not_94_out, not_95_out, not_96_out, not_97_out, not_98_out, not_99_out, not_100_out,
       not_101_out, not_102_out, not_103_out, not_104_out, not_105_out, not_106_out, not_107_out,
       not_108_out, not_109_out, not_110_out, not_111_out, not_112_out, not_113_out, not_114_out,
       not_115_out, not_116_out, not_117_out, not_118_out, not_119_out, not_120_out, not_121_out,
       not_122_out, not_123_out, not_124_out, not_125_out, not_126_out, not_127_out, not_128_out,
       not_129_out, not_130_out, not_131_out, not_132_out, not_133_out, not_134_out, not_135_out,
       not_136_out, not_137_out, not_138_out, not_139_out, not_140_out, not_141_out, not_142_out,
       not_143_out, not_144_out, not_145_out, not_146_out, not_147_out, not_148_out, not_149_out,
       not_150_out, not_151_out, not_152_out, not_153_out, not_154_out, not_155_out, not_156_out,
       not_157_out, not_158_out, not_159_out, not_160_out, not_161_out, not_162_out, not_163_out,
       not_164_out, not_165_out, not_166_out, not_167_out, not_168_out, not_169_out, not_170_out,
       not_171_out, not_172_out, not_173_out, not_174_out, not_175_out, not_176_out, not_177_out,
       not_178_out, not_179_out, not_180_out, not_181_out, not_182_out, not_183_out, not_184_out,
       not_185_out, not_186_out, not_187_out, not_188_out, not_189_out, not_190_out, not_191_out,
       not_192_out, not_193_out, not_194_out, not_195_out, not_196_out, not_197_out, not_198_out,
       not_199_out, not_200_out, not_201_out, not_202_out, not_203_out, not_204_out, not_205_out,
       not_206_out, not_207_out, not_208_out, not_209_out, not_210_out, not_211_out, not_212_out,
       not_213_out, not_214_out, not_215_out, not_216_out, not_217_out, not_218_out, not_219_out,
       not_220_out, not_221_out, not_222_out, not_223_out, not_224_out, not_225_out, not_226_out,
       not_227_out, not_228_out, not_229_out, not_230_out, not_231_out, not_232_out, not_233_out,
       not_234_out, not_235_out, not_236_out, not_237_out, not_238_out, not_239_out, not_240_out,
       not_241_out, not_242_out, not_243_out, not_244_out, not_245_out, not_246_out, not_247_out,
       not_248_out, not_249_out, not_250_out, not_251_out;

  not not_1 (not_1_out, F30);
  not not_2 (not_2_out, F25);
  not not_3 (not_3_out, F14);
  not not_4 (not_4_out, F13);
  not not_5 (not_5_out, F12);
  not not_6 (not_6_out, OP6);
  not not_7 (not_7_out, OP3);
  not not_8 (not_8_out, OP2);
  not not_9 (not_9_out, F30);
  not not_10 (not_10_out, F25);
  not not_11 (not_11_out, OP6);
  not not_12 (not_12_out, OP3);
  not not_13 (not_13_out, OP2);
  not not_14 (not_14_out, F30);
  not not_15 (not_15_out, F25);
  not not_16 (not_16_out, F14);
  not not_17 (not_17_out, F12);
  not not_18 (not_18_out, OP6);
  not not_19 (not_19_out, OP3);
  not not_20 (not_20_out, OP2);
  not not_21 (not_21_out, F14);
  not not_22 (not_22_out, F13);
  not not_23 (not_23_out, F12);
  not not_24 (not_24_out, OP6);
  not not_25 (not_25_out, OP5);
  not not_26 (not_26_out, OP3);
  not not_27 (not_27_out, OP2);
  not not_28 (not_28_out, OP6);
  not not_29 (not_29_out, OP5);
  not not_30 (not_30_out, OP3);
  not not_31 (not_31_out, OP2);
  not not_32 (not_32_out, F13);
  not not_33 (not_33_out, F12);
  not not_34 (not_34_out, OP6);
  not not_35 (not_35_out, OP5);
  not not_36 (not_36_out, OP3);
  not not_37 (not_37_out, OP2);
  not not_38 (not_38_out, F14);
  not not_39 (not_39_out, F12);
  not not_40 (not_40_out, OP6);
  not not_41 (not_41_out, OP5);
  not not_42 (not_42_out, OP3);
  not not_43 (not_43_out, OP2);
  not not_44 (not_44_out, F25);
  not not_45 (not_45_out, F13);
  not not_46 (not_46_out, OP6);
  not not_47 (not_47_out, OP5);
  not not_48 (not_48_out, OP3);
  not not_49 (not_49_out, OP2);
  not not_50 (not_50_out, F14);
  not not_51 (not_51_out, F12);
  not not_52 (not_52_out, OP6);
  not not_53 (not_53_out, OP5);
  not not_54 (not_54_out, OP4);
  not not_55 (not_55_out, OP3);
  not not_56 (not_56_out, OP2);
  not not_57 (not_57_out, F14);
  not not_58 (not_58_out, F12);
  not not_59 (not_59_out, OP6);
  not not_60 (not_60_out, OP4);
  not not_61 (not_61_out, OP3);
  not not_62 (not_62_out, OP2);
  not not_63 (not_63_out, OP4);
  not not_64 (not_64_out, F14);
  not not_65 (not_65_out, F13);
  not not_66 (not_66_out, F12);
  not not_67 (not_67_out, OP4);
  not not_68 (not_68_out, OP3);
  not not_69 (not_69_out, OP3);
  not not_70 (not_70_out, OP2);
  not not_71 (not_71_out, F30);
  not not_72 (not_72_out, F25);
  not not_73 (not_73_out, F13);
  not not_74 (not_74_out, F12);
  not not_75 (not_75_out, OP6);
  not not_76 (not_76_out, OP3);
  not not_77 (not_77_out, OP2);
  not not_78 (not_78_out, F14);
  not not_79 (not_79_out, F13);
  not not_80 (not_80_out, F12);
  not not_81 (not_81_out, OP6);
  not not_82 (not_82_out, OP5);
  not not_83 (not_83_out, OP4);
  not not_84 (not_84_out, OP3);
  not not_85 (not_85_out, OP2);
  not not_86 (not_86_out, F25);
  not not_87 (not_87_out, F14);
  not not_88 (not_88_out, F13);
  not not_89 (not_89_out, F12);
  not not_90 (not_90_out, OP6);
  not not_91 (not_91_out, OP3);
  not not_92 (not_92_out, OP2);
  not not_93 (not_93_out, F30);
  not not_94 (not_94_out, F25);
  not not_95 (not_95_out, OP6);
  not not_96 (not_96_out, OP3);
  not not_97 (not_97_out, OP2);
  not not_98 (not_98_out, F30);
  not not_99 (not_99_out, F25);
  not not_100 (not_100_out, F14);
  not not_101 (not_101_out, F12);
  not not_102 (not_102_out, OP6);
  not not_103 (not_103_out, OP3);
  not not_104 (not_104_out, OP2);
  not not_105 (not_105_out, OP6);
  not not_106 (not_106_out, OP5);
  not not_107 (not_107_out, OP3);
  not not_108 (not_108_out, OP2);
  not not_109 (not_109_out, F14);
  not not_110 (not_110_out, F12);
  not not_111 (not_111_out, OP6);
  not not_112 (not_112_out, OP5);
  not not_113 (not_113_out, OP3);
  not not_114 (not_114_out, OP2);
  not not_115 (not_115_out, F30);
  not not_116 (not_116_out, F25);
  not not_117 (not_117_out, F13);
  not not_118 (not_118_out, OP6);
  not not_119 (not_119_out, OP5);
  not not_120 (not_120_out, OP3);
  not not_121 (not_121_out, OP2);
  not not_122 (not_122_out, OP3);
  not not_123 (not_123_out, OP2);
  not not_124 (not_124_out, F30);
  not not_125 (not_125_out, F25);
  not not_126 (not_126_out, F14);
  not not_127 (not_127_out, F13);
  not not_128 (not_128_out, F12);
  not not_129 (not_129_out, OP6);
  not not_130 (not_130_out, OP3);
  not not_131 (not_131_out, OP2);
  not not_132 (not_132_out, F25);
  not not_133 (not_133_out, F14);
  not not_134 (not_134_out, F13);
  not not_135 (not_135_out, F12);
  not not_136 (not_136_out, OP6);
  not not_137 (not_137_out, OP3);
  not not_138 (not_138_out, OP2);
  not not_139 (not_139_out, F30);
  not not_140 (not_140_out, F25);
  not not_141 (not_141_out, OP6);
  not not_142 (not_142_out, OP3);
  not not_143 (not_143_out, OP2);
  not not_144 (not_144_out, F30);
  not not_145 (not_145_out, F25);
  not not_146 (not_146_out, F14);
  not not_147 (not_147_out, OP6);
  not not_148 (not_148_out, OP3);
  not not_149 (not_149_out, OP2);
  not not_150 (not_150_out, F14);
  not not_151 (not_151_out, F13);
  not not_152 (not_152_out, F12);
  not not_153 (not_153_out, OP6);
  not not_154 (not_154_out, OP5);
  not not_155 (not_155_out, OP3);
  not not_156 (not_156_out, OP2);
  not not_157 (not_157_out, OP6);
  not not_158 (not_158_out, OP5);
  not not_159 (not_159_out, OP3);
  not not_160 (not_160_out, OP2);
  not not_161 (not_161_out, F14);
  not not_162 (not_162_out, F12);
  not not_163 (not_163_out, OP6);
  not not_164 (not_164_out, OP5);
  not not_165 (not_165_out, OP4);
  not not_166 (not_166_out, OP3);
  not not_167 (not_167_out, OP2);
  not not_168 (not_168_out, F14);
  not not_169 (not_169_out, F12);
  not not_170 (not_170_out, OP6);
  not not_171 (not_171_out, OP4);
  not not_172 (not_172_out, OP3);
  not not_173 (not_173_out, OP2);
  not not_174 (not_174_out, OP4);
  not not_175 (not_175_out, F14);
  not not_176 (not_176_out, F13);
  not not_177 (not_177_out, F12);
  not not_178 (not_178_out, OP4);
  not not_179 (not_179_out, OP3);
  not not_180 (not_180_out, OP3);
  not not_181 (not_181_out, OP2);
  not not_182 (not_182_out, F14);
  not not_183 (not_183_out, OP6);
  not not_184 (not_184_out, OP5);
  not not_185 (not_185_out, OP3);
  not not_186 (not_186_out, OP2);
  not not_187 (not_187_out, F14);
  not not_188 (not_188_out, F13);
  not not_189 (not_189_out, F12);
  not not_190 (not_190_out, OP6);
  not not_191 (not_191_out, OP5);
  not not_192 (not_192_out, OP4);
  not not_193 (not_193_out, OP3);
  not not_194 (not_194_out, OP2);
  not not_195 (not_195_out, OP4);
  not not_196 (not_196_out, OP3);
  not not_197 (not_197_out, OP2);
  not not_198 (not_198_out, F30);
  not not_199 (not_199_out, F25);
  not not_200 (not_200_out, F12);
  not not_201 (not_201_out, OP6);
  not not_202 (not_202_out, OP3);
  not not_203 (not_203_out, OP2);
  not not_204 (not_204_out, F30);
  not not_205 (not_205_out, F25);
  not not_206 (not_206_out, F14);
  not not_207 (not_207_out, F12);
  not not_208 (not_208_out, OP6);
  not not_209 (not_209_out, OP3);
  not not_210 (not_210_out, OP2);
  not not_211 (not_211_out, F30);
  not not_212 (not_212_out, F25);
  not not_213 (not_213_out, F14);
  not not_214 (not_214_out, OP6);
  not not_215 (not_215_out, OP3);
  not not_216 (not_216_out, OP2);
  not not_217 (not_217_out, F12);
  not not_218 (not_218_out, OP6);
  not not_219 (not_219_out, OP5);
  not not_220 (not_220_out, OP3);
  not not_221 (not_221_out, OP2);
  not not_222 (not_222_out, F13);
  not not_223 (not_223_out, F12);
  not not_224 (not_224_out, OP6);
  not not_225 (not_225_out, OP5);
  not not_226 (not_226_out, OP3);
  not not_227 (not_227_out, OP2);
  not not_228 (not_228_out, F14);
  not not_229 (not_229_out, F12);
  not not_230 (not_230_out, OP6);
  not not_231 (not_231_out, OP5);
  not not_232 (not_232_out, OP3);
  not not_233 (not_233_out, OP2);
  not not_234 (not_234_out, F12);
  not not_235 (not_235_out, OP3);
  not not_236 (not_236_out, OP2);
  not not_237 (not_237_out, F30);
  not not_238 (not_238_out, F25);
  not not_239 (not_239_out, F13);
  not not_240 (not_240_out, F12);
  not not_241 (not_241_out, OP6);
  not not_242 (not_242_out, OP3);
  not not_243 (not_243_out, OP2);
  not not_244 (not_244_out, F14);
  not not_245 (not_245_out, OP6);
  not not_246 (not_246_out, OP5);
  not not_247 (not_247_out, OP3);
  not not_248 (not_248_out, OP2);
  not not_249 (not_249_out, OP4);
  not not_250 (not_250_out, OP3);
  not not_251 (not_251_out, OP2);
  and and_1 (and_1_out, not_1_out, not_2_out, not_3_out, not_4_out, not_5_out, not_6_out, OP5, OP4, not_7_out, not_8_out);
  and and_2 (and_2_out, not_9_out, not_10_out, F14, F13, F12, not_11_out, OP5, OP4, not_12_out, not_13_out);
  and and_3 (and_3_out, not_14_out, not_15_out, not_16_out, F13, not_17_out, not_18_out, OP5, OP4, not_19_out, not_20_out);
  and and_4 (and_4_out, not_21_out, not_22_out, not_23_out, not_24_out, not_25_out, OP4, not_26_out, not_27_out);
  and and_5 (and_5_out, F14, F13, F12, not_28_out, not_29_out, OP4, not_30_out, not_31_out);
  and and_6 (and_6_out, F14, not_32_out, not_33_out, not_34_out, not_35_out, OP4, not_36_out, not_37_out);
  and and_7 (and_7_out, not_38_out, F13, not_39_out, not_40_out, not_41_out, OP4, not_42_out, not_43_out);
  and and_8 (and_8_out, F30, not_44_out, F14, not_45_out, F12, not_46_out, not_47_out, OP4, not_48_out, not_49_out);
  and and_9 (and_9_out, not_50_out, F13, not_51_out, not_52_out, not_53_out, not_54_out, not_55_out, not_56_out);
  and and_10 (and_10_out, not_57_out, F13, not_58_out, not_59_out, OP5, not_60_out, not_61_out, not_62_out);
  and and_11 (and_11_out, OP6, OP5, not_63_out, OP3, OP2);
  and and_12 (and_12_out, not_64_out, not_65_out, not_66_out, OP6, OP5, not_67_out, not_68_out, OP2);
  and and_13 (and_13_out, F14, F13, F12, OP6, OP5, OP4, not_69_out, not_70_out);
  and and_14 (and_14_out, not_71_out, not_72_out, F14, not_73_out, not_74_out, not_75_out, OP5, OP4, not_76_out, not_77_out);
  and and_15 (and_15_out, not_78_out, not_79_out, not_80_out, not_81_out, not_82_out, not_83_out, not_84_out, not_85_out);
  and and_16 (and_16_out, F30, not_86_out, not_87_out, not_88_out, not_89_out, not_90_out, OP5, OP4, not_91_out, not_92_out);
  and and_17 (and_17_out, not_93_out, not_94_out, F14, F13, F12, not_95_out, OP5, OP4, not_96_out, not_97_out);
  and and_18 (and_18_out, not_98_out, not_99_out, not_100_out, F13, not_101_out, not_102_out, OP5, OP4, not_103_out, not_104_out);
  and and_19 (and_19_out, F14, F13, F12, not_105_out, not_106_out, OP4, not_107_out, not_108_out);
  and and_20 (and_20_out, not_109_out, F13, not_110_out, not_111_out, not_112_out, OP4, not_113_out, not_114_out);
  and and_21 (and_21_out, not_115_out, not_116_out, F14, not_117_out, F12, not_118_out, not_119_out, OP4, not_120_out, not_121_out);
  and and_22 (and_22_out, F14, F13, F12, OP6, OP5, OP4, not_122_out, not_123_out);
  and and_23 (and_23_out, not_124_out, not_125_out, not_126_out, not_127_out, not_128_out, not_129_out, OP5, OP4, not_130_out, not_131_out);
  and and_24 (and_24_out, F30, not_132_out, not_133_out, not_134_out, not_135_out, not_136_out, OP5, OP4, not_137_out, not_138_out);
  and and_25 (and_25_out, not_139_out, not_140_out, F14, F13, F12, not_141_out, OP5, OP4, not_142_out, not_143_out);
  and and_26 (and_26_out, not_144_out, not_145_out, not_146_out, F13, F12, not_147_out, OP5, OP4, not_148_out, not_149_out);
  and and_27 (and_27_out, not_150_out, not_151_out, not_152_out, not_153_out, not_154_out, OP4, not_155_out, not_156_out);
  and and_28 (and_28_out, F14, F13, F12, not_157_out, not_158_out, OP4, not_159_out, not_160_out);
  and and_29 (and_29_out, not_161_out, F13, not_162_out, not_163_out, not_164_out, not_165_out, not_166_out, not_167_out);
  and and_30 (and_30_out, not_168_out, F13, not_169_out, not_170_out, OP5, not_171_out, not_172_out, not_173_out);
  and and_31 (and_31_out, OP6, OP5, not_174_out, OP3, OP2);
  and and_32 (and_32_out, not_175_out, not_176_out, not_177_out, OP6, OP5, not_178_out, not_179_out, OP2);
  and and_33 (and_33_out, F14, F13, F12, OP6, OP5, OP4, not_180_out, not_181_out);
  and and_34 (and_34_out, not_182_out, F13, F12, not_183_out, not_184_out, OP4, not_185_out, not_186_out);
  and and_35 (and_35_out, not_187_out, not_188_out, not_189_out, not_190_out, not_191_out, not_192_out, not_193_out, not_194_out);
  and and_36 (and_36_out, F14, F13, F12, OP6, OP5, not_195_out, not_196_out, not_197_out);
  and and_37 (and_37_out, not_198_out, not_199_out, F14, F13, not_200_out, not_201_out, OP5, OP4, not_202_out, not_203_out);
  and and_38 (and_38_out, not_204_out, not_205_out, not_206_out, F13, not_207_out, not_208_out, OP5, OP4, not_209_out, not_210_out);
  and and_39 (and_39_out, not_211_out, not_212_out, not_213_out, F13, F12, not_214_out, OP5, OP4, not_215_out, not_216_out);
  and and_40 (and_40_out, F14, F13, not_217_out, not_218_out, not_219_out, OP4, not_220_out, not_221_out);
  and and_41 (and_41_out, F14, not_222_out, not_223_out, not_224_out, not_225_out, OP4, not_226_out, not_227_out);
  and and_42 (and_42_out, not_228_out, F13, not_229_out, not_230_out, not_231_out, OP4, not_232_out, not_233_out);
  and and_43 (and_43_out, F14, F13, not_234_out, OP6, OP5, OP4, not_235_out, not_236_out);
  and and_44 (and_44_out, not_237_out, not_238_out, F14, not_239_out, not_240_out, not_241_out, OP5, OP4, not_242_out, not_243_out);
  and and_45 (and_45_out, not_244_out, F13, F12, not_245_out, not_246_out, OP4, not_247_out, not_248_out);
  and and_46 (and_46_out, F14, F13, F12, OP6, OP5, not_249_out, not_250_out, not_251_out);
  or or_1 (S0, and_1_out, and_2_out, and_3_out, and_4_out, and_5_out, and_6_out, and_7_out, and_8_out, and_9_out, and_10_out, and_11_out, and_12_out, and_13_out, and_14_out, and_15_out);
  or or_2 (S1, and_16_out, and_17_out, and_18_out, and_19_out, and_20_out, and_21_out, and_22_out);
  or or_3 (S2, and_23_out, and_24_out, and_25_out, and_26_out, and_27_out, and_28_out, and_29_out, and_30_out, and_31_out, and_32_out, and_33_out, and_34_out, and_35_out, and_36_out);
  or or_4 (S3, and_37_out, and_38_out, and_39_out, and_40_out, and_41_out, and_42_out, and_43_out, and_44_out, and_45_out, and_46_out);
endmodule

// 控制信号生成
module \控制信号自动生成  (
  input  OP2,
  input  OP3,
  input  OP4,
  input  OP5,
  input  OP6,
  input  F12,
  input  F13,
  input  F14,
  input  F25,
  input  F30,
  output MemToReg,
  output MemWrite,
  output ALU_SRC,
  output is_lb,
  output RegWrite,
  output ecall,
  output S_Type,
  output BEQ,
  output BNE,
  output JALR,
  output JAL,
  output bgeu,
  output rs1_used,
  output rs2_used
);

  wire and_1_out, and_2_out, and_4_out, and_5_out, and_6_out, and_7_out, and_8_out, and_9_out, and_10_out,
       and_11_out, and_12_out, and_13_out, and_14_out, and_15_out, and_16_out, and_17_out, and_19_out,
       and_20_out, and_21_out, and_22_out, and_23_out, and_24_out, and_25_out, and_26_out, and_27_out,
       and_28_out, and_29_out, and_30_out, and_31_out, and_32_out, and_33_out, and_34_out, and_35_out,
       and_36_out, and_37_out, and_38_out, and_46_out, and_47_out, and_48_out, and_49_out, and_50_out,
       and_51_out, and_52_out, and_53_out, and_54_out, and_55_out, and_56_out, and_57_out, and_58_out,
       and_59_out, and_60_out, and_61_out, and_62_out, and_63_out, and_64_out, and_65_out, and_66_out,
       and_67_out, and_68_out, and_69_out, and_70_out, and_71_out, and_72_out, and_73_out, and_74_out,
       and_75_out, and_76_out, and_77_out, and_78_out, and_79_out, and_80_out, and_81_out, not_1_out,
       not_2_out, not_3_out, not_4_out, not_5_out, not_6_out, not_7_out, not_8_out, not_9_out, not_10_out,
       not_11_out, not_12_out, not_13_out, not_14_out, not_15_out, not_16_out, not_17_out, not_18_out,
       not_19_out, not_20_out, not_21_out, not_22_out, not_23_out, not_24_out, not_25_out, not_26_out,
       not_27_out, not_28_out, not_29_out, not_30_out, not_31_out, not_32_out, not_33_out, not_34_out,
       not_35_out, not_36_out, not_37_out, not_38_out, not_39_out, not_40_out, not_41_out, not_42_out,
       not_43_out, not_44_out, not_45_out, not_46_out, not_47_out, not_48_out, not_49_out, not_50_out,
       not_51_out, not_52_out, not_53_out, not_54_out, not_55_out, not_56_out, not_57_out, not_58_out,
       not_59_out, not_60_out, not_61_out, not_62_out, not_63_out, not_64_out, not_65_out, not_66_out,
       not_67_out, not_68_out, not_69_out, not_70_out, not_71_out, not_72_out, not_73_out, not_74_out,
       not_75_out, not_76_out, not_77_out, not_78_out, not_79_out, not_80_out, not_81_out, not_82_out,
       not_83_out, not_84_out, not_85_out, not_86_out, not_87_out, not_88_out, not_89_out, not_90_out,
       not_91_out, not_92_out, not_93_out, not_94_out, not_95_out, not_96_out, not_97_out, not_98_out,
       not_99_out, not_100_out, not_101_out, not_102_out, not_103_out, not_104_out, not_105_out, not_106_out,
       not_107_out, not_108_out, not_109_out, not_110_out, not_111_out, not_112_out, not_113_out,
       not_114_out, not_115_out, not_116_out, not_117_out, not_118_out, not_119_out, not_120_out,
       not_121_out, not_122_out, not_123_out, not_124_out, not_125_out, not_126_out, not_127_out,
       not_128_out, not_129_out, not_130_out, not_131_out, not_132_out, not_133_out, not_134_out,
       not_135_out, not_136_out, not_137_out, not_138_out, not_139_out, not_140_out, not_141_out,
       not_142_out, not_143_out, not_144_out, not_145_out, not_146_out, not_147_out, not_148_out,
       not_149_out, not_150_out, not_151_out, not_152_out, not_153_out, not_154_out, not_155_out,
       not_156_out, not_157_out, not_158_out, not_159_out, not_160_out, not_161_out, not_162_out,
       not_163_out, not_164_out, not_165_out, not_166_out, not_167_out, not_168_out, not_169_out,
       not_170_out, not_171_out, not_172_out, not_173_out, not_174_out, not_175_out, not_176_out,
       not_177_out, not_178_out, not_179_out, not_180_out, not_181_out, not_182_out, not_183_out,
       not_184_out, not_185_out, not_186_out, not_187_out, not_188_out, not_189_out, not_190_out,
       not_191_out, not_192_out, not_193_out, not_194_out, not_195_out, not_196_out, not_197_out,
       not_198_out, not_199_out, not_200_out, not_201_out, not_202_out, not_203_out, not_204_out,
       not_205_out, not_206_out, not_207_out, not_208_out, not_209_out, not_210_out, not_211_out,
       not_212_out, not_213_out, not_214_out, not_215_out, not_216_out, not_217_out, not_218_out,
       not_219_out, not_220_out, not_221_out, not_222_out, not_223_out, not_224_out, not_225_out,
       not_226_out, not_227_out, not_228_out, not_229_out, not_230_out, not_231_out, not_232_out,
       not_233_out, not_234_out, not_235_out, not_236_out, not_237_out, not_238_out, not_239_out,
       not_240_out, not_241_out, not_242_out, not_243_out, not_244_out, not_245_out, not_246_out,
       not_247_out, not_248_out, not_249_out, not_250_out, not_251_out, not_252_out, not_253_out,
       not_254_out, not_255_out, not_256_out, not_257_out, not_258_out, not_259_out, not_260_out,
       not_261_out, not_262_out, not_263_out, not_264_out, not_265_out, not_266_out, not_267_out,
       not_268_out, not_269_out, not_270_out, not_271_out, not_272_out, not_273_out, not_274_out,
       not_275_out, not_276_out, not_277_out, not_278_out, not_279_out, not_280_out, not_281_out,
       not_282_out, not_283_out, not_284_out, not_285_out, not_286_out, not_287_out, not_288_out,
       not_289_out, not_290_out, not_291_out, not_292_out, not_293_out, not_294_out, not_295_out,
       not_296_out, not_297_out, not_298_out, not_299_out, not_300_out, not_301_out, not_302_out,
       not_303_out, not_304_out, not_305_out, not_306_out, not_307_out, not_308_out, not_309_out,
       not_310_out, not_311_out, not_312_out, not_313_out, not_314_out, not_315_out, not_316_out,
       not_317_out, not_318_out, not_319_out, not_320_out, not_321_out, not_322_out, not_323_out,
       not_324_out, not_325_out, not_326_out, not_327_out, not_328_out, not_329_out, not_330_out,
       not_331_out, not_332_out, not_333_out, not_334_out, not_335_out, not_336_out, not_337_out,
       not_338_out, not_339_out, not_340_out, not_341_out, not_342_out, not_343_out, not_344_out,
       not_345_out, not_346_out, not_347_out, not_348_out, not_349_out, not_350_out, not_351_out,
       not_352_out, not_353_out, not_354_out, not_355_out, not_356_out, not_357_out, not_358_out,
       not_359_out, not_360_out, not_361_out, not_362_out, not_363_out, not_364_out, not_365_out,
       not_366_out, not_367_out, not_368_out, not_369_out, not_370_out, not_371_out, not_372_out,
       not_373_out, not_374_out, not_375_out, not_376_out, not_377_out, not_378_out, not_379_out,
       not_380_out, not_381_out, not_382_out, not_383_out, not_384_out, not_385_out, not_386_out,
       not_387_out, not_388_out, not_389_out, not_390_out, not_391_out, not_392_out, not_393_out,
       not_394_out, not_395_out, not_396_out, not_397_out, not_398_out, not_399_out, not_400_out,
       not_401_out, not_402_out, not_403_out, not_404_out, not_405_out, not_406_out, not_407_out,
       not_408_out, not_409_out, not_410_out, not_411_out, not_412_out, not_413_out, not_414_out,
       not_415_out, not_416_out, not_417_out, not_418_out, not_419_out, not_420_out, not_421_out,
       not_422_out, not_423_out, not_424_out, not_425_out, not_426_out, not_427_out, not_428_out,
       not_429_out, not_430_out, not_431_out, not_432_out, not_433_out, not_434_out, not_435_out,
       not_436_out, not_437_out, not_438_out, not_439_out, not_440_out, not_441_out, not_442_out,
       not_443_out, not_444_out, not_445_out, not_446_out, not_447_out, not_448_out, not_449_out,
       not_450_out, not_451_out, not_452_out, not_453_out, not_454_out, not_455_out, not_456_out,
       not_457_out, not_458_out, not_459_out, not_460_out, not_461_out, not_462_out, not_463_out,
       not_464_out, not_465_out, not_466_out, not_467_out, not_468_out, not_469_out, not_470_out,
       not_471_out, not_472_out, not_473_out, not_474_out, not_475_out, not_476_out, not_477_out,
       not_478_out, not_479_out, not_480_out, not_481_out, not_482_out, not_483_out, not_484_out,
       not_485_out, not_486_out, not_487_out, not_488_out, not_489_out, not_490_out;

  not not_1 (not_1_out, F14);
  not not_2 (not_2_out, F12);
  not not_3 (not_3_out, OP6);
  not not_4 (not_4_out, OP5);
  not not_5 (not_5_out, OP4);
  not not_6 (not_6_out, OP3);
  not not_7 (not_7_out, OP2);
  not not_8 (not_8_out, F14);
  not not_9 (not_9_out, F13);
  not not_10 (not_10_out, F12);
  not not_11 (not_11_out, OP6);
  not not_12 (not_12_out, OP5);
  not not_13 (not_13_out, OP4);
  not not_14 (not_14_out, OP3);
  not not_15 (not_15_out, OP2);
  not not_16 (not_16_out, F14);
  not not_17 (not_17_out, F12);
  not not_18 (not_18_out, OP6);
  not not_19 (not_19_out, OP4);
  not not_20 (not_20_out, OP3);
  not not_21 (not_21_out, OP2);
  not not_22 (not_22_out, F14);
  not not_23 (not_23_out, F13);
  not not_24 (not_24_out, F12);
  not not_25 (not_25_out, OP6);
  not not_26 (not_26_out, OP5);
  not not_27 (not_27_out, OP3);
  not not_28 (not_28_out, OP2);
  not not_29 (not_29_out, OP6);
  not not_30 (not_30_out, OP5);
  not not_31 (not_31_out, OP3);
  not not_32 (not_32_out, OP2);
  not not_33 (not_33_out, F12);
  not not_34 (not_34_out, OP6);
  not not_35 (not_35_out, OP5);
  not not_36 (not_36_out, OP3);
  not not_37 (not_37_out, OP2);
  not not_38 (not_38_out, F13);
  not not_39 (not_39_out, F12);
  not not_40 (not_40_out, OP6);
  not not_41 (not_41_out, OP5);
  not not_42 (not_42_out, OP3);
  not not_43 (not_43_out, OP2);
  not not_44 (not_44_out, F14);
  not not_45 (not_45_out, F12);
  not not_46 (not_46_out, OP6);
  not not_47 (not_47_out, OP5);
  not not_48 (not_48_out, OP3);
  not not_49 (not_49_out, OP2);
  not not_50 (not_50_out, F30);
  not not_51 (not_51_out, F25);
  not not_52 (not_52_out, F14);
  not not_53 (not_53_out, F13);
  not not_54 (not_54_out, OP6);
  not not_55 (not_55_out, OP5);
  not not_56 (not_56_out, OP3);
  not not_57 (not_57_out, OP2);
  not not_58 (not_58_out, F30);
  not not_59 (not_59_out, F25);
  not not_60 (not_60_out, F13);
  not not_61 (not_61_out, OP6);
  not not_62 (not_62_out, OP5);
  not not_63 (not_63_out, OP3);
  not not_64 (not_64_out, OP2);
  not not_65 (not_65_out, F25);
  not not_66 (not_66_out, F13);
  not not_67 (not_67_out, OP6);
  not not_68 (not_68_out, OP5);
  not not_69 (not_69_out, OP3);
  not not_70 (not_70_out, OP2);
  not not_71 (not_71_out, F14);
  not not_72 (not_72_out, F12);
  not not_73 (not_73_out, OP6);
  not not_74 (not_74_out, OP5);
  not not_75 (not_75_out, OP4);
  not not_76 (not_76_out, OP3);
  not not_77 (not_77_out, OP2);
  not not_78 (not_78_out, F14);
  not not_79 (not_79_out, F12);
  not not_80 (not_80_out, OP6);
  not not_81 (not_81_out, OP4);
  not not_82 (not_82_out, OP3);
  not not_83 (not_83_out, OP2);
  not not_84 (not_84_out, F30);
  not not_85 (not_85_out, F25);
  not not_86 (not_86_out, F14);
  not not_87 (not_87_out, F13);
  not not_88 (not_88_out, F12);
  not not_89 (not_89_out, OP3);
  not not_90 (not_90_out, OP2);
  not not_91 (not_91_out, F14);
  not not_92 (not_92_out, F13);
  not not_93 (not_93_out, F12);
  not not_94 (not_94_out, OP4);
  not not_95 (not_95_out, OP3);
  not not_96 (not_96_out, F14);
  not not_97 (not_97_out, OP6);
  not not_98 (not_98_out, OP5);
  not not_99 (not_99_out, OP3);
  not not_100 (not_100_out, OP2);
  not not_101 (not_101_out, F14);
  not not_102 (not_102_out, F13);
  not not_103 (not_103_out, F12);
  not not_104 (not_104_out, OP6);
  not not_105 (not_105_out, OP5);
  not not_106 (not_106_out, OP4);
  not not_107 (not_107_out, OP3);
  not not_108 (not_108_out, OP2);
  not not_109 (not_109_out, F14);
  not not_110 (not_110_out, F13);
  not not_111 (not_111_out, F12);
  not not_112 (not_112_out, OP6);
  not not_113 (not_113_out, OP5);
  not not_114 (not_114_out, OP4);
  not not_115 (not_115_out, OP3);
  not not_116 (not_116_out, OP2);
  not not_117 (not_117_out, F30);
  not not_118 (not_118_out, F25);
  not not_119 (not_119_out, F14);
  not not_120 (not_120_out, F13);
  not not_121 (not_121_out, F12);
  not not_122 (not_122_out, OP6);
  not not_123 (not_123_out, OP3);
  not not_124 (not_124_out, OP2);
  not not_125 (not_125_out, F25);
  not not_126 (not_126_out, F14);
  not not_127 (not_127_out, F13);
  not not_128 (not_128_out, F12);
  not not_129 (not_129_out, OP6);
  not not_130 (not_130_out, OP3);
  not not_131 (not_131_out, OP2);
  not not_132 (not_132_out, F30);
  not not_133 (not_133_out, F25);
  not not_134 (not_134_out, OP6);
  not not_135 (not_135_out, OP3);
  not not_136 (not_136_out, OP2);
  not not_137 (not_137_out, F30);
  not not_138 (not_138_out, F25);
  not not_139 (not_139_out, F12);
  not not_140 (not_140_out, OP6);
  not not_141 (not_141_out, OP3);
  not not_142 (not_142_out, OP2);
  not not_143 (not_143_out, F30);
  not not_144 (not_144_out, F25);
  not not_145 (not_145_out, F14);
  not not_146 (not_146_out, F12);
  not not_147 (not_147_out, OP6);
  not not_148 (not_148_out, OP3);
  not not_149 (not_149_out, OP2);
  not not_150 (not_150_out, F30);
  not not_151 (not_151_out, F25);
  not not_152 (not_152_out, F14);
  not not_153 (not_153_out, OP6);
  not not_154 (not_154_out, OP3);
  not not_155 (not_155_out, OP2);
  not not_156 (not_156_out, F14);
  not not_157 (not_157_out, F13);
  not not_158 (not_158_out, F12);
  not not_159 (not_159_out, OP6);
  not not_160 (not_160_out, OP5);
  not not_161 (not_161_out, OP3);
  not not_162 (not_162_out, OP2);
  not not_163 (not_163_out, OP6);
  not not_164 (not_164_out, OP5);
  not not_165 (not_165_out, OP3);
  not not_166 (not_166_out, OP2);
  not not_167 (not_167_out, F12);
  not not_168 (not_168_out, OP6);
  not not_169 (not_169_out, OP5);
  not not_170 (not_170_out, OP3);
  not not_171 (not_171_out, OP2);
  not not_172 (not_172_out, F13);
  not not_173 (not_173_out, F12);
  not not_174 (not_174_out, OP6);
  not not_175 (not_175_out, OP5);
  not not_176 (not_176_out, OP3);
  not not_177 (not_177_out, OP2);
  not not_178 (not_178_out, F14);
  not not_179 (not_179_out, F12);
  not not_180 (not_180_out, OP6);
  not not_181 (not_181_out, OP5);
  not not_182 (not_182_out, OP3);
  not not_183 (not_183_out, OP2);
  not not_184 (not_184_out, F30);
  not not_185 (not_185_out, F25);
  not not_186 (not_186_out, F14);
  not not_187 (not_187_out, F13);
  not not_188 (not_188_out, OP6);
  not not_189 (not_189_out, OP5);
  not not_190 (not_190_out, OP3);
  not not_191 (not_191_out, OP2);
  not not_192 (not_192_out, F30);
  not not_193 (not_193_out, F25);
  not not_194 (not_194_out, F13);
  not not_195 (not_195_out, OP6);
  not not_196 (not_196_out, OP5);
  not not_197 (not_197_out, OP3);
  not not_198 (not_198_out, OP2);
  not not_199 (not_199_out, F25);
  not not_200 (not_200_out, F13);
  not not_201 (not_201_out, OP6);
  not not_202 (not_202_out, OP5);
  not not_203 (not_203_out, OP3);
  not not_204 (not_204_out, OP2);
  not not_205 (not_205_out, F14);
  not not_206 (not_206_out, F12);
  not not_207 (not_207_out, OP6);
  not not_208 (not_208_out, OP5);
  not not_209 (not_209_out, OP4);
  not not_210 (not_210_out, OP3);
  not not_211 (not_211_out, OP2);
  not not_212 (not_212_out, OP4);
  not not_213 (not_213_out, F14);
  not not_214 (not_214_out, F13);
  not not_215 (not_215_out, F12);
  not not_216 (not_216_out, OP4);
  not not_217 (not_217_out, OP3);
  not not_218 (not_218_out, F30);
  not not_219 (not_219_out, F25);
  not not_220 (not_220_out, F13);
  not not_221 (not_221_out, F12);
  not not_222 (not_222_out, OP6);
  not not_223 (not_223_out, OP3);
  not not_224 (not_224_out, OP2);
  not not_225 (not_225_out, F14);
  not not_226 (not_226_out, OP6);
  not not_227 (not_227_out, OP5);
  not not_228 (not_228_out, OP3);
  not not_229 (not_229_out, OP2);
  not not_230 (not_230_out, F14);
  not not_231 (not_231_out, F13);
  not not_232 (not_232_out, F12);
  not not_233 (not_233_out, OP6);
  not not_234 (not_234_out, OP5);
  not not_235 (not_235_out, OP4);
  not not_236 (not_236_out, OP3);
  not not_237 (not_237_out, OP2);
  not not_238 (not_238_out, F30);
  not not_239 (not_239_out, F25);
  not not_240 (not_240_out, F14);
  not not_241 (not_241_out, F13);
  not not_242 (not_242_out, F12);
  not not_243 (not_243_out, OP3);
  not not_244 (not_244_out, OP2);
  not not_245 (not_245_out, F14);
  not not_246 (not_246_out, F12);
  not not_247 (not_247_out, OP6);
  not not_248 (not_248_out, OP4);
  not not_249 (not_249_out, OP3);
  not not_250 (not_250_out, OP2);
  not not_251 (not_251_out, F14);
  not not_252 (not_252_out, F13);
  not not_253 (not_253_out, F12);
  not not_254 (not_254_out, OP4);
  not not_255 (not_255_out, OP3);
  not not_256 (not_256_out, OP2);
  not not_257 (not_257_out, F14);
  not not_258 (not_258_out, F13);
  not not_259 (not_259_out, OP4);
  not not_260 (not_260_out, OP3);
  not not_261 (not_261_out, OP2);
  not not_262 (not_262_out, F14);
  not not_263 (not_263_out, F13);
  not not_264 (not_264_out, F12);
  not not_265 (not_265_out, OP4);
  not not_266 (not_266_out, OP3);
  not not_267 (not_267_out, OP4);
  not not_268 (not_268_out, OP4);
  not not_269 (not_269_out, OP3);
  not not_270 (not_270_out, OP2);
  not not_271 (not_271_out, F30);
  not not_272 (not_272_out, F25);
  not not_273 (not_273_out, F14);
  not not_274 (not_274_out, F13);
  not not_275 (not_275_out, F12);
  not not_276 (not_276_out, OP6);
  not not_277 (not_277_out, OP3);
  not not_278 (not_278_out, OP2);
  not not_279 (not_279_out, F25);
  not not_280 (not_280_out, F14);
  not not_281 (not_281_out, F13);
  not not_282 (not_282_out, F12);
  not not_283 (not_283_out, OP6);
  not not_284 (not_284_out, OP3);
  not not_285 (not_285_out, OP2);
  not not_286 (not_286_out, F30);
  not not_287 (not_287_out, F25);
  not not_288 (not_288_out, OP6);
  not not_289 (not_289_out, OP3);
  not not_290 (not_290_out, OP2);
  not not_291 (not_291_out, F30);
  not not_292 (not_292_out, F25);
  not not_293 (not_293_out, F12);
  not not_294 (not_294_out, OP6);
  not not_295 (not_295_out, OP3);
  not not_296 (not_296_out, OP2);
  not not_297 (not_297_out, F30);
  not not_298 (not_298_out, F25);
  not not_299 (not_299_out, F14);
  not not_300 (not_300_out, F12);
  not not_301 (not_301_out, OP6);
  not not_302 (not_302_out, OP3);
  not not_303 (not_303_out, OP2);
  not not_304 (not_304_out, F30);
  not not_305 (not_305_out, F25);
  not not_306 (not_306_out, F14);
  not not_307 (not_307_out, OP6);
  not not_308 (not_308_out, OP3);
  not not_309 (not_309_out, OP2);
  not not_310 (not_310_out, F14);
  not not_311 (not_311_out, F13);
  not not_312 (not_312_out, F12);
  not not_313 (not_313_out, OP6);
  not not_314 (not_314_out, OP5);
  not not_315 (not_315_out, OP3);
  not not_316 (not_316_out, OP2);
  not not_317 (not_317_out, OP6);
  not not_318 (not_318_out, OP5);
  not not_319 (not_319_out, OP3);
  not not_320 (not_320_out, OP2);
  not not_321 (not_321_out, F12);
  not not_322 (not_322_out, OP6);
  not not_323 (not_323_out, OP5);
  not not_324 (not_324_out, OP3);
  not not_325 (not_325_out, OP2);
  not not_326 (not_326_out, F13);
  not not_327 (not_327_out, F12);
  not not_328 (not_328_out, OP6);
  not not_329 (not_329_out, OP5);
  not not_330 (not_330_out, OP3);
  not not_331 (not_331_out, OP2);
  not not_332 (not_332_out, F14);
  not not_333 (not_333_out, F12);
  not not_334 (not_334_out, OP6);
  not not_335 (not_335_out, OP5);
  not not_336 (not_336_out, OP3);
  not not_337 (not_337_out, OP2);
  not not_338 (not_338_out, F30);
  not not_339 (not_339_out, F25);
  not not_340 (not_340_out, F14);
  not not_341 (not_341_out, F13);
  not not_342 (not_342_out, OP6);
  not not_343 (not_343_out, OP5);
  not not_344 (not_344_out, OP3);
  not not_345 (not_345_out, OP2);
  not not_346 (not_346_out, F30);
  not not_347 (not_347_out, F25);
  not not_348 (not_348_out, F13);
  not not_349 (not_349_out, OP6);
  not not_350 (not_350_out, OP5);
  not not_351 (not_351_out, OP3);
  not not_352 (not_352_out, OP2);
  not not_353 (not_353_out, F25);
  not not_354 (not_354_out, F13);
  not not_355 (not_355_out, OP6);
  not not_356 (not_356_out, OP5);
  not not_357 (not_357_out, OP3);
  not not_358 (not_358_out, OP2);
  not not_359 (not_359_out, F14);
  not not_360 (not_360_out, F12);
  not not_361 (not_361_out, OP6);
  not not_362 (not_362_out, OP5);
  not not_363 (not_363_out, OP4);
  not not_364 (not_364_out, OP3);
  not not_365 (not_365_out, OP2);
  not not_366 (not_366_out, F14);
  not not_367 (not_367_out, F12);
  not not_368 (not_368_out, OP6);
  not not_369 (not_369_out, OP4);
  not not_370 (not_370_out, OP3);
  not not_371 (not_371_out, OP2);
  not not_372 (not_372_out, F30);
  not not_373 (not_373_out, F25);
  not not_374 (not_374_out, F14);
  not not_375 (not_375_out, F13);
  not not_376 (not_376_out, F12);
  not not_377 (not_377_out, OP3);
  not not_378 (not_378_out, OP2);
  not not_379 (not_379_out, F14);
  not not_380 (not_380_out, F13);
  not not_381 (not_381_out, F12);
  not not_382 (not_382_out, OP4);
  not not_383 (not_383_out, OP3);
  not not_384 (not_384_out, OP2);
  not not_385 (not_385_out, F14);
  not not_386 (not_386_out, F13);
  not not_387 (not_387_out, OP4);
  not not_388 (not_388_out, OP3);
  not not_389 (not_389_out, OP2);
  not not_390 (not_390_out, F14);
  not not_391 (not_391_out, F13);
  not not_392 (not_392_out, F12);
  not not_393 (not_393_out, OP4);
  not not_394 (not_394_out, OP3);
  not not_395 (not_395_out, F30);
  not not_396 (not_396_out, F25);
  not not_397 (not_397_out, F13);
  not not_398 (not_398_out, F12);
  not not_399 (not_399_out, OP6);
  not not_400 (not_400_out, OP3);
  not not_401 (not_401_out, OP2);
  not not_402 (not_402_out, F14);
  not not_403 (not_403_out, OP6);
  not not_404 (not_404_out, OP5);
  not not_405 (not_405_out, OP3);
  not not_406 (not_406_out, OP2);
  not not_407 (not_407_out, F14);
  not not_408 (not_408_out, F13);
  not not_409 (not_409_out, F12);
  not not_410 (not_410_out, OP6);
  not not_411 (not_411_out, OP5);
  not not_412 (not_412_out, OP4);
  not not_413 (not_413_out, OP3);
  not not_414 (not_414_out, OP2);
  not not_415 (not_415_out, OP4);
  not not_416 (not_416_out, OP3);
  not not_417 (not_417_out, OP2);
  not not_418 (not_418_out, F30);
  not not_419 (not_419_out, F25);
  not not_420 (not_420_out, F14);
  not not_421 (not_421_out, F13);
  not not_422 (not_422_out, F12);
  not not_423 (not_423_out, OP6);
  not not_424 (not_424_out, OP3);
  not not_425 (not_425_out, OP2);
  not not_426 (not_426_out, F25);
  not not_427 (not_427_out, F14);
  not not_428 (not_428_out, F13);
  not not_429 (not_429_out, F12);
  not not_430 (not_430_out, OP6);
  not not_431 (not_431_out, OP3);
  not not_432 (not_432_out, OP2);
  not not_433 (not_433_out, F30);
  not not_434 (not_434_out, F25);
  not not_435 (not_435_out, OP6);
  not not_436 (not_436_out, OP3);
  not not_437 (not_437_out, OP2);
  not not_438 (not_438_out, F30);
  not not_439 (not_439_out, F25);
  not not_440 (not_440_out, F12);
  not not_441 (not_441_out, OP6);
  not not_442 (not_442_out, OP3);
  not not_443 (not_443_out, OP2);
  not not_444 (not_444_out, F30);
  not not_445 (not_445_out, F25);
  not not_446 (not_446_out, F14);
  not not_447 (not_447_out, F12);
  not not_448 (not_448_out, OP6);
  not not_449 (not_449_out, OP3);
  not not_450 (not_450_out, OP2);
  not not_451 (not_451_out, F30);
  not not_452 (not_452_out, F25);
  not not_453 (not_453_out, F14);
  not not_454 (not_454_out, OP6);
  not not_455 (not_455_out, OP3);
  not not_456 (not_456_out, OP2);
  not not_457 (not_457_out, F14);
  not not_458 (not_458_out, F12);
  not not_459 (not_459_out, OP6);
  not not_460 (not_460_out, OP4);
  not not_461 (not_461_out, OP3);
  not not_462 (not_462_out, OP2);
  not not_463 (not_463_out, F30);
  not not_464 (not_464_out, F25);
  not not_465 (not_465_out, F14);
  not not_466 (not_466_out, F13);
  not not_467 (not_467_out, F12);
  not not_468 (not_468_out, OP3);
  not not_469 (not_469_out, OP2);
  not not_470 (not_470_out, F14);
  not not_471 (not_471_out, F13);
  not not_472 (not_472_out, F12);
  not not_473 (not_473_out, OP4);
  not not_474 (not_474_out, OP3);
  not not_475 (not_475_out, OP2);
  not not_476 (not_476_out, F14);
  not not_477 (not_477_out, F13);
  not not_478 (not_478_out, OP4);
  not not_479 (not_479_out, OP3);
  not not_480 (not_480_out, OP2);
  not not_481 (not_481_out, F30);
  not not_482 (not_482_out, F25);
  not not_483 (not_483_out, F13);
  not not_484 (not_484_out, F12);
  not not_485 (not_485_out, OP6);
  not not_486 (not_486_out, OP3);
  not not_487 (not_487_out, OP2);
  not not_488 (not_488_out, OP4);
  not not_489 (not_489_out, OP3);
  not not_490 (not_490_out, OP2);
  and and_1 (and_1_out, not_1_out, F13, not_2_out, not_3_out, not_4_out, not_5_out, not_6_out, not_7_out);
  and and_2 (and_2_out, not_8_out, not_9_out, not_10_out, not_11_out, not_12_out, not_13_out, not_14_out, not_15_out);
  and and_3 (MemWrite, not_16_out, F13, not_17_out, not_18_out, OP5, not_19_out, not_20_out, not_21_out);
  and and_4 (and_4_out, not_22_out, not_23_out, not_24_out, not_25_out, not_26_out, OP4, not_27_out, not_28_out);
  and and_5 (and_5_out, F14, F13, F12, not_29_out, not_30_out, OP4, not_31_out, not_32_out);
  and and_6 (and_6_out, F14, F13, not_33_out, not_34_out, not_35_out, OP4, not_36_out, not_37_out);
  and and_7 (and_7_out, F14, not_38_out, not_39_out, not_40_out, not_41_out, OP4, not_42_out, not_43_out);
  and and_8 (and_8_out, not_44_out, F13, not_45_out, not_46_out, not_47_out, OP4, not_48_out, not_49_out);
  and and_9 (and_9_out, not_50_out, not_51_out, not_52_out, not_53_out, F12, not_54_out, not_55_out, OP4, not_56_out, not_57_out);
  and and_10 (and_10_out, not_58_out, not_59_out, F14, not_60_out, F12, not_61_out, not_62_out, OP4, not_63_out, not_64_out);
  and and_11 (and_11_out, F30, not_65_out, F14, not_66_out, F12, not_67_out, not_68_out, OP4, not_69_out, not_70_out);
  and and_12 (and_12_out, not_71_out, F13, not_72_out, not_73_out, not_74_out, not_75_out, not_76_out, not_77_out);
  and and_13 (and_13_out, not_78_out, F13, not_79_out, not_80_out, OP5, not_81_out, not_82_out, not_83_out);
  and and_14 (and_14_out, not_84_out, not_85_out, not_86_out, not_87_out, not_88_out, OP6, OP5, OP4, not_89_out, not_90_out);
  and and_15 (and_15_out, not_91_out, not_92_out, not_93_out, OP6, OP5, not_94_out, not_95_out, OP2);
  and and_16 (and_16_out, not_96_out, F13, F12, not_97_out, not_98_out, OP4, not_99_out, not_100_out);
  and and_17 (and_17_out, not_101_out, not_102_out, not_103_out, not_104_out, not_105_out, not_106_out, not_107_out, not_108_out);
  and and_18 (is_lb, not_109_out, not_110_out, not_111_out, not_112_out, not_113_out, not_114_out, not_115_out, not_116_out);
  and and_19 (and_19_out, not_117_out, not_118_out, not_119_out, not_120_out, not_121_out, not_122_out, OP5, OP4, not_123_out, not_124_out);
  and and_20 (and_20_out, F30, not_125_out, not_126_out, not_127_out, not_128_out, not_129_out, OP5, OP4, not_130_out, not_131_out);
  and and_21 (and_21_out, not_132_out, not_133_out, F14, F13, F12, not_134_out, OP5, OP4, not_135_out, not_136_out);
  and and_22 (and_22_out, not_137_out, not_138_out, F14, F13, not_139_out, not_140_out, OP5, OP4, not_141_out, not_142_out);
  and and_23 (and_23_out, not_143_out, not_144_out, not_145_out, F13, not_146_out, not_147_out, OP5, OP4, not_148_out, not_149_out);
  and and_24 (and_24_out, not_150_out, not_151_out, not_152_out, F13, F12, not_153_out, OP5, OP4, not_154_out, not_155_out);
  and and_25 (and_25_out, not_156_out, not_157_out, not_158_out, not_159_out, not_160_out, OP4, not_161_out, not_162_out);
  and and_26 (and_26_out, F14, F13, F12, not_163_out, not_164_out, OP4, not_165_out, not_166_out);
  and and_27 (and_27_out, F14, F13, not_167_out, not_168_out, not_169_out, OP4, not_170_out, not_171_out);
  and and_28 (and_28_out, F14, not_172_out, not_173_out, not_174_out, not_175_out, OP4, not_176_out, not_177_out);
  and and_29 (and_29_out, not_178_out, F13, not_179_out, not_180_out, not_181_out, OP4, not_182_out, not_183_out);
  and and_30 (and_30_out, not_184_out, not_185_out, not_186_out, not_187_out, F12, not_188_out, not_189_out, OP4, not_190_out, not_191_out);
  and and_31 (and_31_out, not_192_out, not_193_out, F14, not_194_out, F12, not_195_out, not_196_out, OP4, not_197_out, not_198_out);
  and and_32 (and_32_out, F30, not_199_out, F14, not_200_out, F12, not_201_out, not_202_out, OP4, not_203_out, not_204_out);
  and and_33 (and_33_out, not_205_out, F13, not_206_out, not_207_out, not_208_out, not_209_out, not_210_out, not_211_out);
  and and_34 (and_34_out, OP6, OP5, not_212_out, OP3, OP2);
  and and_35 (and_35_out, not_213_out, not_214_out, not_215_out, OP6, OP5, not_216_out, not_217_out, OP2);
  and and_36 (and_36_out, not_218_out, not_219_out, F14, not_220_out, not_221_out, not_222_out, OP5, OP4, not_223_out, not_224_out);
  and and_37 (and_37_out, not_225_out, F13, F12, not_226_out, not_227_out, OP4, not_228_out, not_229_out);
  and and_38 (and_38_out, not_230_out, not_231_out, not_232_out, not_233_out, not_234_out, not_235_out, not_236_out, not_237_out);
  and and_39 (ecall, not_238_out, not_239_out, not_240_out, not_241_out, not_242_out, OP6, OP5, OP4, not_243_out, not_244_out);
  and and_40 (S_Type, not_245_out, F13, not_246_out, not_247_out, OP5, not_248_out, not_249_out, not_250_out);
  and and_41 (BEQ, not_251_out, not_252_out, not_253_out, OP6, OP5, not_254_out, not_255_out, not_256_out);
  and and_42 (BNE, not_257_out, not_258_out, F12, OP6, OP5, not_259_out, not_260_out, not_261_out);
  and and_43 (JALR, not_262_out, not_263_out, not_264_out, OP6, OP5, not_265_out, not_266_out, OP2);
  and and_44 (JAL, OP6, OP5, not_267_out, OP3, OP2);
  and and_45 (bgeu, F14, F13, F12, OP6, OP5, not_268_out, not_269_out, not_270_out);
  and and_46 (and_46_out, not_271_out, not_272_out, not_273_out, not_274_out, not_275_out, not_276_out, OP5, OP4, not_277_out, not_278_out);
  and and_47 (and_47_out, F30, not_279_out, not_280_out, not_281_out, not_282_out, not_283_out, OP5, OP4, not_284_out, not_285_out);
  and and_48 (and_48_out, not_286_out, not_287_out, F14, F13, F12, not_288_out, OP5, OP4, not_289_out, not_290_out);
  and and_49 (and_49_out, not_291_out, not_292_out, F14, F13, not_293_out, not_294_out, OP5, OP4, not_295_out, not_296_out);
  and and_50 (and_50_out, not_297_out, not_298_out, not_299_out, F13, not_300_out, not_301_out, OP5, OP4, not_302_out, not_303_out);
  and and_51 (and_51_out, not_304_out, not_305_out, not_306_out, F13, F12, not_307_out, OP5, OP4, not_308_out, not_309_out);
  and and_52 (and_52_out, not_310_out, not_311_out, not_312_out, not_313_out, not_314_out, OP4, not_315_out, not_316_out);
  and and_53 (and_53_out, F14, F13, F12, not_317_out, not_318_out, OP4, not_319_out, not_320_out);
  and and_54 (and_54_out, F14, F13, not_321_out, not_322_out, not_323_out, OP4, not_324_out, not_325_out);
  and and_55 (and_55_out, F14, not_326_out, not_327_out, not_328_out, not_329_out, OP4, not_330_out, not_331_out);
  and and_56 (and_56_out, not_332_out, F13, not_333_out, not_334_out, not_335_out, OP4, not_336_out, not_337_out);
  and and_57 (and_57_out, not_338_out, not_339_out, not_340_out, not_341_out, F12, not_342_out, not_343_out, OP4, not_344_out, not_345_out);
  and and_58 (and_58_out, not_346_out, not_347_out, F14, not_348_out, F12, not_349_out, not_350_out, OP4, not_351_out, not_352_out);
  and and_59 (and_59_out, F30, not_353_out, F14, not_354_out, F12, not_355_out, not_356_out, OP4, not_357_out, not_358_out);
  and and_60 (and_60_out, not_359_out, F13, not_360_out, not_361_out, not_362_out, not_363_out, not_364_out, not_365_out);
  and and_61 (and_61_out, not_366_out, F13, not_367_out, not_368_out, OP5, not_369_out, not_370_out, not_371_out);
  and and_62 (and_62_out, not_372_out, not_373_out, not_374_out, not_375_out, not_376_out, OP6, OP5, OP4, not_377_out, not_378_out);
  and and_63 (and_63_out, not_379_out, not_380_out, not_381_out, OP6, OP5, not_382_out, not_383_out, not_384_out);
  and and_64 (and_64_out, not_385_out, not_386_out, F12, OP6, OP5, not_387_out, not_388_out, not_389_out);
  and and_65 (and_65_out, not_390_out, not_391_out, not_392_out, OP6, OP5, not_393_out, not_394_out, OP2);
  and and_66 (and_66_out, not_395_out, not_396_out, F14, not_397_out, not_398_out, not_399_out, OP5, OP4, not_400_out, not_401_out);
  and and_67 (and_67_out, not_402_out, F13, F12, not_403_out, not_404_out, OP4, not_405_out, not_406_out);
  and and_68 (and_68_out, not_407_out, not_408_out, not_409_out, not_410_out, not_411_out, not_412_out, not_413_out, not_414_out);
  and and_69 (and_69_out, F14, F13, F12, OP6, OP5, not_415_out, not_416_out, not_417_out);
  and and_70 (and_70_out, not_418_out, not_419_out, not_420_out, not_421_out, not_422_out, not_423_out, OP5, OP4, not_424_out, not_425_out);
  and and_71 (and_71_out, F30, not_426_out, not_427_out, not_428_out, not_429_out, not_430_out, OP5, OP4, not_431_out, not_432_out);
  and and_72 (and_72_out, not_433_out, not_434_out, F14, F13, F12, not_435_out, OP5, OP4, not_436_out, not_437_out);
  and and_73 (and_73_out, not_438_out, not_439_out, F14, F13, not_440_out, not_441_out, OP5, OP4, not_442_out, not_443_out);
  and and_74 (and_74_out, not_444_out, not_445_out, not_446_out, F13, not_447_out, not_448_out, OP5, OP4, not_449_out, not_450_out);
  and and_75 (and_75_out, not_451_out, not_452_out, not_453_out, F13, F12, not_454_out, OP5, OP4, not_455_out, not_456_out);
  and and_76 (and_76_out, not_457_out, F13, not_458_out, not_459_out, OP5, not_460_out, not_461_out, not_462_out);
  and and_77 (and_77_out, not_463_out, not_464_out, not_465_out, not_466_out, not_467_out, OP6, OP5, OP4, not_468_out, not_469_out);
  and and_78 (and_78_out, not_470_out, not_471_out, not_472_out, OP6, OP5, not_473_out, not_474_out, not_475_out);
  and and_79 (and_79_out, not_476_out, not_477_out, F12, OP6, OP5, not_478_out, not_479_out, not_480_out);
  and and_80 (and_80_out, not_481_out, not_482_out, F14, not_483_out, not_484_out, not_485_out, OP5, OP4, not_486_out, not_487_out);
  and and_81 (and_81_out, F14, F13, F12, OP6, OP5, not_488_out, not_489_out, not_490_out);
  or or_1 (MemToReg, and_1_out, and_2_out);
  or or_2 (ALU_SRC, and_4_out, and_5_out, and_6_out, and_7_out, and_8_out, and_9_out, and_10_out, and_11_out, and_12_out, and_13_out, and_14_out, and_15_out, and_16_out, and_17_out);
  or or_3 (RegWrite, and_19_out, and_20_out, and_21_out, and_22_out, and_23_out, and_24_out, and_25_out, and_26_out, and_27_out, and_28_out, and_29_out, and_30_out, and_31_out, and_32_out, and_33_out, and_34_out, and_35_out, and_36_out, and_37_out, and_38_out);
  or or_4 (rs2_used, and_70_out, and_71_out, and_72_out, and_73_out, and_74_out, and_75_out, and_76_out, and_77_out, and_78_out, and_79_out, and_80_out, and_81_out);
  or or_5 (rs1_used, and_46_out, and_47_out, and_48_out, and_49_out, and_50_out, and_51_out, and_52_out, and_53_out, and_54_out, and_55_out, and_56_out, and_57_out, and_58_out, and_59_out, and_60_out, and_61_out, and_62_out, and_63_out, and_64_out, and_65_out, and_66_out, and_67_out, and_68_out, and_69_out);
endmodule

// ALU
module ALU (
  input  [31:0] X,
  input  [31:0] Y,
  input  [3:0] AluOP,
  output out_4,
  output Equal,
  output out_6,
  output [31:0] Result,
  output [31:0] Result_2
);

  wire [0:0] comparator_1_lt, comparator_2_lt;
  wire [31:0] adder_1_out, AND_out, divider_1_out, divider_1_rem, multiplier_1_cout, multiplier_1_out,
       NOR_out, OR_out, shifter_1_out, shifter_2_out, shifter_3_out, subtractor_1_out, XOR_out;

  assign AND_out = X & Y;  // AND_Gate AND, 32 bits wide
  assign OR_out = X | Y;  // OR_Gate OR, 32 bits wide
  Shifter #(.width(32), .shift("ll")) shifter_1 (.in(X), .\dist (Y[4:0]), .out(shifter_1_out));
  Shifter #(.width(32), .shift("ar")) shifter_2 (.in(X), .\dist (Y[4:0]), .out(shifter_2_out));
  Shifter #(.width(32), .shift("lr")) shifter_3 (.in(X), .\dist (Y[4:0]), .out(shifter_3_out));
  Multiplier #(.width(32)) multiplier_1 (.a(X), .b(Y), .out(multiplier_1_out), .cout(multiplier_1_cout));  // open: cin
  Divider #(.width(32)) divider_1 (.a(X), .b(Y), .out(divider_1_out), .rem(divider_1_rem));  // open: upper
  Adder #(.width(32)) adder_1 (.a(X), .b(Y), .out(adder_1_out));  // open: cin, cout
  Subtractor #(.width(32)) subtractor_1 (.a(X), .b(Y), .out(subtractor_1_out));  // open: bin, bout
  assign XOR_out = X ^ Y;  // XOR_Gate XOR, 32 bits wide
  assign NOR_out = ~(X | Y);  // NOR_Gate NOR, 32 bits wide
  Comparator #(.width(32), .mode("twosComplement")) comparator_1 (
    .a(X), .b(Y), .eq(Equal), .lt(comparator_1_lt[0]));  // open: gt
  Comparator #(.width(32), .mode("unsigned")) comparator_2 (.a(X), .b(Y), .lt(comparator_2_lt[0]));  // open: gt, eq
  Multiplexer #(.select(4), .width(32), .disabled("Z"), .enable("false")) multiplexer_1 (
    .in0(shifter_1_out), .in1(shifter_2_out), .in2(shifter_3_out), .in3(multiplier_1_out),
    .in4(divider_1_out), .in5(adder_1_out), .in6(subtractor_1_out), .in7(AND_out), .in8(OR_out),
    .in9(XOR_out), .in10(NOR_out), .in11({{31{1'b0}}, comparator_1_lt[0]}),
    .in12({{31{1'b0}}, comparator_2_lt[0]}), .in13({32{1'b0}}), .in14({32{1'b0}}), .in15({32{1'b0}}),
    .out(Result), .sel(AluOP));
  Multiplexer #(.select(4), .width(32), .disabled("Z"), .enable("false")) multiplexer_2 (
    .in0({32{1'b0}}), .in1({32{1'b0}}), .in2({32{1'b0}}), .in3(multiplier_1_cout), .in4(divider_1_rem),
    .in5({32{1'b0}}), .in6({32{1'b0}}), .in7({32{1'b0}}), .in8({32{1'b0}}), .in9({32{1'b0}}),
    .in10({32{1'b0}}), .in11({32{1'b0}}), .in12({32{1'b0}}), .in13({32{1'b0}}), .in14({32{1'b0}}),
    .in15({32{1'b0}}), .out(Result_2), .sel(AluOP));
  Multiplexer #(.select(4), .width(1), .disabled("Z"), .enable("false")) multiplexer_3 (
    .in0(1'b0), .in1(1'b0), .in2(1'b0), .in3(1'b0), .in4(1'b0), .in5(1'b0), .in6(1'b0), .in7(1'b0),
    .in8(1'b0), .in9(1'b0), .in10(1'b0), .in11(comparator_1_lt[0]), .in12(comparator_2_lt[0]), .in13(1'b0),
    .in14(1'b0), .in15(1'b0), .out(out_6), .sel(AluOP));
  not not_1 (out_4, out_6);

  // Other names for the same wires on the sheet: Result2[31:0] = Result_2; S[3:0] = AluOP; tunnel = out_6;
  //   tunnel_t = out_4

  // Notes on the sheet:
  //   不要改变此引脚区域内容，也不要改变ALU封装形式
  //   输入引脚
  //   输出引脚
endmodule

module Regifile (
  input  [31:0] Din,
  input  Clk,
  input  WE,
  input  [4:0] R1_num,
  input  [4:0] W_num,
  input  [4:0] R2_num,
  output [31:0] R1,
  output [31:0] R2
);

  // RegisterFile registerfile_1: pin names not known; wires that end beside it: Din, Clk, WE, W_num, R1_num, R2_num, R1, R2
endmodule

module \理想流水线  (
  output RegWrite,
  output MemWrite,
  output [31:0] IF_PC,
  output [31:0] ID_PC,
  output [31:0] EX_PC,
  output [31:0] M_PC,
  output [31:0] WB_PC,
  output [31:0] RDin,
  output [31:0] MDin,
  output [31:0] LedData
);

  wire alu_1_equal, alu_1_out_4, and_1_out, and_3_out, and_4_out, and_5_out, and_6_out, and_7_out, bgue, CLK,
       clock_1_out, comparator_1_eq, comparator_1_lt, comparator_2_eq, comparator_3_eq, d_ff_1_q, ecall, Go,
       halt, IR1, IR2, IR3, is_lb, JAL, JALR, less, multiplexer_2_out, nand_1_out, not_1_out, not_2_out,
       not_3_out, not_4_out, not_5_out, or_1_out, or_2_out, or_3_out, register_2_q, RST, S_type, W1, W2, W3,
       \单周期硬布线控制器_1_alu_src , \单周期硬布线控制器_1_beq , \单周期硬布线控制器_1_bne , \单周期硬布线控制器_1_memtoreg ,
       \单周期硬布线控制器_1_memwrite , \单周期硬布线控制器_1_regwrite , \单周期硬布线控制器_1_uret , \流水器器件_1_valid_2 ,
       \流水器器件_2_alusrcb_2 , \流水器器件_2_begue_2 , \流水器器件_2_beq_2 , \流水器器件_2_bne_2 , \流水器器件_2_ecall_2 ,
       \流水器器件_2_is_lb_2 , \流水器器件_2_jal_2 , \流水器器件_2_jalr_2 , \流水器器件_2_memtoreg_2 , \流水器器件_2_memwrite_2 ,
       \流水器器件_2_regwrite_2 , \流水器器件_2_valid_2 , \流水器器件_3_halt_3 , \流水器器件_3_is_lb_2 , \流水器器件_3_jal_2 ,
       \流水器器件_3_jalr_2 , \流水器器件_3_memtoreg_2 , \流水器器件_3_regwrite_2 , \流水器器件_3_valid_2 , \流水器器件_4_halt_3 ;
  wire [1:0] priority_encoder_1_out, priority_encoder_2_out;
  wire [3:0] \单周期硬布线控制器_1_alu_op , \流水器器件_2_aluop_2 ;
  wire [4:0] multiplexer_3_out, multiplexer_4_out, \流水器器件_2_rd_2 , \流水器器件_3_rd_2 , \流水器器件_4_rd_2 ;
  wire [11:0] multiplexer_5_out;
  wire [12:0] CNT_num;
  wire [15:0] \LoadUse次数 , \总周期数 , \插入气泡数 , \无条件分支数 , \条件分支成功数 ;
  wire [31:0] adder_1_out, alu_1_result, Alu_out2, and_2_out, bit_extender_1_out, bit_extender_2_out,
       bit_extender_3_out, bit_extender_4_out, bout, EX_IR, ID_IR, IF_IR, IR, jout, MEM_IR,
       multiplexer_1_out, multiplexer_6_out, multiplexer_7_out, multiplexer_8_out, PC_4id, R1, ram_1_data,
       regifile_1_r2, rom_1_data, shifter_1_out, shifter_2_out, WB_IR, \流水器器件_2_imm_b_2 , \流水器器件_2_imm_j_2 ,
       \流水器器件_2_imm_si_2 , \流水器器件_2_pc_4_2 , \流水器器件_2_r1_2 , \流水器器件_2_r2_2 , \流水器器件_3_imm_si_2 ,
       \流水器器件_3_pc_4_2 ;

  Button \u_总复位  (.out(RST));
  Button _1 (.out(IR1));
  Button _2 (.out(IR2));
  Button _3 (.out(IR3));
  // Probe on \总周期数 
  // Probe on \总周期数 
  Button \u_继续运行  (.out(Go));
  LED #(.active("true")) led_1 (.in(W1));
  LED #(.active("true")) led_2 (.in(W2));
  LED #(.active("true")) led_3 (.in(W3));
  Hex_Digit_Display hex_digit_display_1 (.value(LedData[31:28]));  // open: dp
  // Probe on IF_PC[19:0]
  // RiscV_Probe riscv_probe_1: pin names not known; wires that end beside it: IF_IR
  Hex_Digit_Display hex_digit_display_2 (.value(LedData[23:20]));  // open: dp
  Hex_Digit_Display hex_digit_display_3 (.value(LedData[27:24]));  // open: dp
  // Probe on ID_PC[19:0]
  // RiscV_Probe riscv_probe_2: pin names not known; wires that end beside it: ID_IR
  Hex_Digit_Display hex_digit_display_4 (.value(LedData[19:16]));  // open: dp
  Hex_Digit_Display hex_digit_display_5 (.value(LedData[15:12]));  // open: dp
  Hex_Digit_Display hex_digit_display_6 (.value(LedData[7:4]));  // open: dp
  Hex_Digit_Display hex_digit_display_7 (.value(LedData[11:8]));  // open: dp
  // Probe on EX_PC[19:0]
  // RiscV_Probe riscv_probe_3: pin names not known; wires that end beside it: EX_IR
  and and_1 (and_1_out, alu_1_out_4, \流水器器件_2_begue_2 );
  assign and_2_out = 32'hfffffffe & alu_1_result;  // AND_Gate and_2, 32 bits wide
  Hex_Digit_Display hex_digit_display_8 (.value(LedData[3:0]));  // open: dp
  not not_1 (not_1_out, alu_1_equal);
  and and_3 (and_3_out, \流水器器件_2_beq_2 , alu_1_equal);
  and and_4 (and_4_out, not_1_out, \流水器器件_2_bne_2 );
  or or_1 (or_1_out, and_1_out, and_3_out, and_4_out);
  Priority_Encoder #(.select(2), .disabled("Z")) priority_encoder_1 (
    .in0(1'b1), .in1(or_1_out), .in2(\流水器器件_2_jal_2 ), .in3(\流水器器件_2_jalr_2 ), .out(priority_encoder_1_out));  // open: gs, en_out, en_in
  Multiplexer #(.select(2), .width(32), .disabled("Z"), .enable("false")) multiplexer_1 (
    .in0(adder_1_out), .in1(\流水器器件_2_imm_b_2 ), .in2(\流水器器件_2_imm_j_2 ), .in3(and_2_out),
    .out(multiplexer_1_out), .sel(priority_encoder_1_out));
  // Probe on \总周期数 
  // Probe on M_PC[19:0]
  // RiscV_Probe riscv_probe_4: pin names not known; wires that end beside it: MEM_IR
  Register #(.width(32), .trigger("rising"), .Select("low")) PC (
    .D(multiplexer_1_out), .en(not_2_out), .Q(IF_PC), .clk(CLK), .clr(RST));
  not not_2 (not_2_out, halt);
  // Probe on \总周期数 
  // Probe on \无条件分支数 
  // Probe on \条件分支成功数 
  // Probe on \插入气泡数 
  // Probe on \LoadUse次数 
  // Probe on IF_PC[11:0]
  // Probe on WB_PC[19:0]
  // RiscV_Probe riscv_probe_5: pin names not known; wires that end beside it: WB_IR
  Adder #(.width(32)) adder_1 (.a(IF_PC), .b(32'h4), .out(adder_1_out));  // open: cin, cout
  // Probe on EX_PC[11:0]
  // Probe on ID_PC[11:0]
  Multiplexer #(.select(1), .width(1), .disabled("Z"), .enable("false")) multiplexer_2 (
    .in0(1'b1), .in1(1'b0), .out(multiplexer_2_out), .sel(halt));
  ROM #(.addrWidth(10), .dataWidth(32), .Select("high")) rom_1 (.addr(IF_PC[11:2]), .data(rom_1_data));
  // Probe on M_PC[11:0]
  D_Flip_Flop #(.trigger("high"), .Pre_Clr_Positions("LEGACY"), .NegatePresetClear("false"), .enable("true"), .NewFFLayout("false")) d_ff_1 (.Q(d_ff_1_q));  // open: clk, D, Qn, preset, en, reset
  // Probe on {13{1'b1}}
  // RiscV_Probe riscv_probe_6: pin names not known; wires that end beside it: rom_1_data
  // Probe on WB_PC[11:0]
  Comparator #(.width(13), .mode("twosComplement")) comparator_1 (
    .a(CNT_num), .b({13{1'b1}}), .eq(comparator_1_eq), .lt(comparator_1_lt));  // open: gt
  Clock #(.highDuration(1), .lowDuration(1)) clock_1 (.out(clock_1_out));
  \流水器器件  \u_流水器器件_1  (
    .PC(IF_PC), .PC_4(adder_1_out), .IR(rom_1_data), .PC_2(ID_PC), .PC_4_2(PC_4id), .IR_2(IR), .reset(1'b0),
    .refresh(or_2_out), .Halt_2(halt), .clk(CLK), .valid(multiplexer_2_out), .valid_2(\流水器器件_1_valid_2 ));  // open: JAL, JALR, is_lb, begue, Beq, Bne, MemToReg, MemWrite, AluSrcB, RegWrite, S_type, ecall, halt, AluOp, rd, R1, R2, imm_si, imm_b, imm_j, JAL_2, JALR_2, is_lb_2, begue_2, Beq_2, Bne_2, MemToReg_2, MemWrite_2, AluSrcB_2, RegWrite_2, S_type_2, ecall_2, halt_3, Aluop_2, rd_2, R1_2, R2_2, imm_si_2, imm_b_2, imm_j_2, predict, predict_2
  nand nand_1 (nand_1_out, d_ff_1_q, comparator_1_eq);
  Counter #(.width(13), .max('h1fff), .ongoal("stay"), .trigger("rising"), .behavior("old")) counter_1 (
    .count(comparator_1_lt), .Q(CNT_num), .clk(clock_1_out));  // open: load, D, carry, clr, preset
  assign CLK = nand_1_out ? clock_1_out : 1'bz;  // Controlled_Buffer controlled_buffer_1
  Pull_Resistor #(.pull(1)) pull_resistor_1 (.node(CLK));
  Multiplexer #(.select(1), .width(5), .disabled("Z"), .enable("false")) multiplexer_3 (
    .in0(IR[19:15]), .in1(5'b10001), .out(multiplexer_3_out), .sel(ecall));
  Multiplexer #(.select(1), .width(5), .disabled("Z"), .enable("false")) multiplexer_4 (
    .in0(IR[24:20]), .in1(5'b01010), .out(multiplexer_4_out), .sel(ecall));
  \单周期硬布线控制器  \u_单周期硬布线控制器_1  (
    .Funct({IR[30], IR[25], IR[14:12]}), .OP(IR[6:2]), .ALU_OP(\单周期硬布线控制器_1_alu_op ),
    .MemToReg(\单周期硬布线控制器_1_memtoreg ), .MemWrite(\单周期硬布线控制器_1_memwrite ), .ALU_SRC(\单周期硬布线控制器_1_alu_src ),
    .RegWrite(\单周期硬布线控制器_1_regwrite ), .ecall(ecall), .S_type(S_type), .Jalr(JALR), .Beq(\单周期硬布线控制器_1_beq ),
    .JAL(JAL), .Bne(\单周期硬布线控制器_1_bne ), .in_3(IR[21]), .uret(\单周期硬布线控制器_1_uret ), .is_lb(is_lb), .bgue(bgue));  // open: rs1_used, rs2_used
  Multiplexer #(.select(1), .width(12), .disabled("Z"), .enable("false")) multiplexer_5 (
    .in0(IR[31:20]), .in1({IR[31:25], IR[11:7]}), .out(multiplexer_5_out), .sel(S_type));
  assign bit_extender_1_out = {{20{IR[31]}}, {IR[31], IR[7], IR[30:25], IR[11:8]}};  // Bit_Extender bit_extender_1
  assign bit_extender_2_out = {{12{IR[31]}}, {IR[31], IR[19:12], IR[20], IR[30:21]}};  // Bit_Extender bit_extender_2
  assign bit_extender_3_out = {{20{multiplexer_5_out[11]}}, multiplexer_5_out};  // Bit_Extender bit_extender_3
  Shifter #(.width(32), .shift("ll")) shifter_1 (.in(bit_extender_1_out), .\dist (5'b00001), .out(shifter_1_out));
  Regifile regifile_1 (
    .Din(RDin), .Clk(CLK), .R1(R1), .R2(regifile_1_r2), .WE(RegWrite), .W_num(\流水器器件_4_rd_2 ),
    .R1_num(multiplexer_3_out), .R2_num(multiplexer_4_out));
  Shifter #(.width(32), .shift("ll")) shifter_2 (.in(bit_extender_2_out), .\dist (5'b00001), .out(shifter_2_out));
  Adder #(.width(32)) adder_2 (.a(shifter_1_out), .b(ID_PC), .out(bout));  // open: cin, cout
  Adder #(.width(32)) adder_3 (.a(shifter_2_out), .b(ID_PC), .out(jout));  // open: cin, cout
  or or_2 (or_2_out, priority_encoder_1_out[0], priority_encoder_1_out[1]);
  not not_3 (not_3_out, \流水器器件_1_valid_2 );
  \流水器器件  \u_流水器器件_2  (
    .JAL(JAL), .JALR(JALR), .is_lb(is_lb), .begue(bgue), .Beq(\单周期硬布线控制器_1_beq ), .Bne(\单周期硬布线控制器_1_bne ),
    .MemToReg(\单周期硬布线控制器_1_memtoreg ), .MemWrite(\单周期硬布线控制器_1_memwrite ), .AluSrcB(\单周期硬布线控制器_1_alu_src ),
    .RegWrite(\单周期硬布线控制器_1_regwrite ), .S_type(S_type), .ecall(ecall), .AluOp(\单周期硬布线控制器_1_alu_op ),
    .rd(IR[11:7]), .R1(R1), .R2(regifile_1_r2), .PC(ID_PC), .PC_4(PC_4id), .imm_si(bit_extender_3_out),
    .imm_b(bout), .imm_j(jout), .JAL_2(\流水器器件_2_jal_2 ), .JALR_2(\流水器器件_2_jalr_2 ),
    .is_lb_2(\流水器器件_2_is_lb_2 ), .begue_2(\流水器器件_2_begue_2 ), .Beq_2(\流水器器件_2_beq_2 ),
    .Bne_2(\流水器器件_2_bne_2 ), .MemToReg_2(\流水器器件_2_memtoreg_2 ), .MemWrite_2(\流水器器件_2_memwrite_2 ),
    .AluSrcB_2(\流水器器件_2_alusrcb_2 ), .RegWrite_2(\流水器器件_2_regwrite_2 ), .ecall_2(\流水器器件_2_ecall_2 ),
    .Aluop_2(\流水器器件_2_aluop_2 ), .rd_2(\流水器器件_2_rd_2 ), .R1_2(\流水器器件_2_r1_2 ), .R2_2(\流水器器件_2_r2_2 ),
    .PC_2(EX_PC), .PC_4_2(\流水器器件_2_pc_4_2 ), .imm_si_2(\流水器器件_2_imm_si_2 ), .imm_b_2(\流水器器件_2_imm_b_2 ),
    .imm_j_2(\流水器器件_2_imm_j_2 ), .reset(not_3_out), .refresh(or_2_out), .Halt_2(halt), .clk(CLK),
    .valid(\流水器器件_1_valid_2 ), .valid_2(\流水器器件_2_valid_2 ));  // open: halt, IR, S_type_2, halt_3, IR_2, predict, predict_2
  Multiplexer #(.select(1), .width(32), .disabled("Z"), .enable("false")) multiplexer_6 (
    .in0(\流水器器件_2_r2_2 ), .in1(\流水器器件_2_imm_si_2 ), .out(multiplexer_6_out), .sel(\流水器器件_2_alusrcb_2 ));
  Comparator #(.width(32), .mode("twosComplement")) comparator_2 (
    .a(\流水器器件_2_r1_2 ), .b(32'h22), .eq(comparator_2_eq));  // open: gt, lt
  Comparator #(.width(32), .mode("twosComplement")) comparator_3 (
    .a(\流水器器件_2_r1_2 ), .b(32'h22), .eq(comparator_3_eq));  // open: gt, lt
  and and_5 (and_5_out, ~comparator_3_eq, \流水器器件_2_ecall_2 );  // AND_Gate
  ALU alu_1 (
    .X(\流水器器件_2_r1_2 ), .Y(multiplexer_6_out), .AluOP(\流水器器件_2_aluop_2 ), .Equal(alu_1_equal),
    .Result(alu_1_result), .Result_2(Alu_out2), .out_4(alu_1_out_4), .out_6(less));
  and and_6 (and_6_out, \流水器器件_2_ecall_2 , comparator_2_eq);
  Register #(.width(32), .trigger("rising"), .Select("low")) register_1 (
    .D(\流水器器件_2_r2_2 ), .en(and_6_out), .Q(LedData), .clk(CLK));  // open: clr
  not not_4 (not_4_out, \流水器器件_2_valid_2 );
  \流水器器件  \u_流水器器件_3  (
    .JAL(\流水器器件_2_jal_2 ), .JALR(\流水器器件_2_jalr_2 ), .is_lb(\流水器器件_2_is_lb_2 ),
    .MemToReg(\流水器器件_2_memtoreg_2 ), .MemWrite(\流水器器件_2_memwrite_2 ), .RegWrite(\流水器器件_2_regwrite_2 ),
    .halt(and_5_out), .rd(\流水器器件_2_rd_2 ), .R2(\流水器器件_2_r2_2 ), .PC(EX_PC), .PC_4(\流水器器件_2_pc_4_2 ),
    .imm_si(alu_1_result), .JAL_2(\流水器器件_3_jal_2 ), .JALR_2(\流水器器件_3_jalr_2 ), .is_lb_2(\流水器器件_3_is_lb_2 ),
    .MemToReg_2(\流水器器件_3_memtoreg_2 ), .MemWrite_2(MemWrite), .RegWrite_2(\流水器器件_3_regwrite_2 ),
    .halt_3(\流水器器件_3_halt_3 ), .rd_2(\流水器器件_3_rd_2 ), .R2_2(MDin), .PC_2(M_PC), .PC_4_2(\流水器器件_3_pc_4_2 ),
    .imm_si_2(\流水器器件_3_imm_si_2 ), .reset(not_4_out), .refresh(1'b0), .Halt_2(halt), .clk(CLK),
    .valid(\流水器器件_2_valid_2 ), .valid_2(\流水器器件_3_valid_2 ));  // open: begue, Beq, Bne, AluSrcB, S_type, ecall, AluOp, R1, imm_b, imm_j, IR, begue_2, Beq_2, Bne_2, AluSrcB_2, S_type_2, ecall_2, Aluop_2, R1_2, imm_b_2, imm_j_2, IR_2, predict, predict_2
  or or_3 (or_3_out, \流水器器件_3_jal_2 , \流水器器件_3_jalr_2 );
  Priority_Encoder #(.select(2), .disabled("Z")) priority_encoder_2 (
    .in0(1'b1), .in1(or_3_out), .in2(\流水器器件_3_memtoreg_2 ), .in3(1'b0), .out(priority_encoder_2_out));  // open: gs, en_out, en_in
  RAM #(.addrWidth(10), .dataWidth(32), .bus("separate"), .Select("high")) ram_1 (
    .addr(\流水器器件_3_imm_si_2 [11:2]), .din(MDin), .data(ram_1_data), .str(MemWrite), .sel(1'b1), .clk(CLK),
    .ld(\流水器器件_3_memtoreg_2 ), .clr(1'b0));
  Multiplexer #(.select(1), .width(32), .disabled("Z"), .enable("false")) multiplexer_7 (
    .in0(ram_1_data), .in1(bit_extender_4_out), .out(multiplexer_7_out), .sel(\流水器器件_3_is_lb_2 ));
  assign bit_extender_4_out = {{24{ram_1_data[7]}}, ram_1_data[7:0]};  // Bit_Extender bit_extender_4
  Multiplexer #(.select(2), .width(32), .disabled("Z"), .enable("false")) multiplexer_8 (
    .in0(\流水器器件_3_imm_si_2 ), .in1(\流水器器件_3_pc_4_2 ), .in2(multiplexer_7_out), .out(multiplexer_8_out),
    .sel(priority_encoder_2_out));  // open: in3
  not not_5 (not_5_out, \流水器器件_3_valid_2 );
  \流水器器件  \u_流水器器件_4  (
    .RegWrite(\流水器器件_3_regwrite_2 ), .halt(\流水器器件_3_halt_3 ), .rd(\流水器器件_3_rd_2 ), .PC(M_PC),
    .imm_si(\流水器器件_3_imm_si_2 ), .IR(multiplexer_8_out), .RegWrite_2(RegWrite), .halt_3(\流水器器件_4_halt_3 ),
    .rd_2(\流水器器件_4_rd_2 ), .PC_2(WB_PC), .IR_2(RDin), .reset(not_5_out), .refresh(1'b0), .Halt_2(halt),
    .clk(CLK), .valid(\流水器器件_3_valid_2 ));  // open: JAL, JALR, is_lb, begue, Beq, Bne, MemToReg, MemWrite, AluSrcB, S_type, ecall, AluOp, R1, R2, PC_4, imm_b, imm_j, JAL_2, JALR_2, is_lb_2, begue_2, Beq_2, Bne_2, MemToReg_2, MemWrite_2, AluSrcB_2, S_type_2, ecall_2, Aluop_2, R1_2, R2_2, PC_4_2, imm_si_2, imm_b_2, imm_j_2, valid_2, predict, predict_2
  Register #(.width(1), .trigger("falling"), .Select("low")) register_2 (
    .D(1'b0), .Q(register_2_q), .clk(\流水器器件_4_halt_3 ), .preset(Go));  // open: en, clr, cs
  and and_7 (and_7_out, ~register_2_q, \流水器器件_4_halt_3 );  // AND_Gate
  Register #(.width(1), .trigger("falling"), .Select("low")) register_3 (
    .D(and_7_out), .Q(halt), .clk(CLK));  // open: en, clr

  // Other names for the same wires on the sheet: rd[4:0] = IR[11:7]; MEM_PC[31:0] = M_PC; PC[31:0] = IF_PC;
  //   PCid[31:0] = ID_PC

  // Notes on the sheet:
  //   中断源
  //   时空图监测，可删除
  //   中断等待指示
  //   数码管输出
  //   指令存储器
  //   控制位
  //   指令探针
  //   contents of rom_1 (hex, n*v repeats v):
  //   413 493 913 993 46413 14e493 296913 39e993 842023 942223 1242423 1342623 a00893 493 913 993 73
  //   流水调试日志用
  //   暂停节拍，不能为0
  //   戳工具置1进入计数暂停模式，ctrl+k时钟自动运行到对应节拍暂停
  //   ctrl+k关闭时钟连续运行，将控制位置零，进入单步调试模式调试
  //   用这个时钟源需要去掉电路中的其他时钟源
  //   可计数暂停的时钟源
  //   指令字
  //   b型
  //   j型
  //   JALR
  //   URET
  //   Beq
  //   Bne
  //   MemToReg
  //   MemWrite
  //   AluOP
  //   AluSrcB
  //   RegWrite
  //   为方便自动评测，需要输出流水线各段保存的PC值，注意是PC不是PC+4，另外ID段寄存器写入信息，Mem段内存写入信息也要输出
  //   R2
  //   aluop
  //   rd
  //   JAL
  //   JALR
  //   PC_4
  //   Aluout
  //   MemtoReg
  //   is_lb
  //   MemWrite
  //   处理sw
  //   数据存储器
  //   写回寄存器有四种情况，R型，jalrjal，lb
  //   R地址
  //   Rdata
  //   Aluout
  //   写回data
endmodule
module \气泡流水线  (
  output RegWrite,
  output MemWrite,
  output [31:0] IF_PC,
  output [31:0] ID_PC,
  output [31:0] EX_PC,
  output [31:0] M_PC,
  output [31:0] WB_PC,
  output [31:0] RDin,
  output [31:0] MDin,
  output [31:0] LedData
);

  wire alu_1_equal, alu_1_out_4, and_1_out, and_3_out, and_4_out, and_5_out, and_6_out, and_7_out, bgue, CLK,
       clock_1_out, comparator_1_eq, comparator_1_lt, comparator_2_eq, comparator_3_eq, d_ff_1_q, ecall, Go,
       halt, IR1, IR2, IR3, is_lb, JAL, JALR, less, multiplexer_2_out, nand_1_out, not_1_out, not_2_out,
       not_3_out, not_4_out, not_5_out, not_6_out, or_1_out, or_2_out, or_3_out, or_4_out, or_5_out,
       register_2_q, riscv_probe_7_p2, RST, S_type, W1, W2, W3, \单周期硬布线控制器_1_alu_src , \单周期硬布线控制器_1_beq ,
       \单周期硬布线控制器_1_bne , \单周期硬布线控制器_1_memtoreg , \单周期硬布线控制器_1_memwrite , \单周期硬布线控制器_1_regwrite ,
       \单周期硬布线控制器_1_rs1_used , \单周期硬布线控制器_1_rs2_used , \流水器器件_1_valid_2 , \流水器器件_2_alusrcb_2 ,
       \流水器器件_2_begue_2 , \流水器器件_2_beq_2 , \流水器器件_2_bne_2 , \流水器器件_2_ecall_2 , \流水器器件_2_is_lb_2 ,
       \流水器器件_2_jal_2 , \流水器器件_2_jalr_2 , \流水器器件_2_memtoreg_2 , \流水器器件_2_memwrite_2 , \流水器器件_2_regwrite_2 ,
       \流水器器件_2_valid_2 , \流水器器件_3_halt_3 , \流水器器件_3_is_lb_2 , \流水器器件_3_jal_2 , \流水器器件_3_jalr_2 ,
       \流水器器件_3_memtoreg_2 , \流水器器件_3_regwrite_2 , \流水器器件_3_valid_2 , \流水器器件_4_halt_3 , \清空 , \阻塞 ;
  wire [1:0] priority_encoder_1_out, priority_encoder_2_out;
  wire [3:0] \单周期硬布线控制器_1_alu_op , \流水器器件_2_aluop_2 ;
  wire [4:0] multiplexer_3_out, multiplexer_4_out, \流水器器件_2_rd_2 , \流水器器件_3_rd_2 , \流水器器件_4_rd_2 ;
  wire [7:0] multiplexer_8_out;
  wire [11:0] multiplexer_5_out;
  wire [12:0] CNT_num;
  wire [15:0] \LoadUse次数 , \总周期数 , \插入气泡数 , \无条件分支数 , \条件分支成功数 ;
  wire [31:0] adder_1_out, alu_1_result, Alu_out, Alu_out2, and_2_out, bit_extender_1_out,
       bit_extender_2_out, bit_extender_3_out, bit_extender_4_out, bout, EX_IR, ID_IR, IF_IR, IR, jout,
       MEM_IR, multiplexer_1_out, multiplexer_6_out, multiplexer_7_out, multiplexer_9_out, PC_4id, R1,
       ram_1_data, regifile_1_r2, rom_1_data, shifter_1_out, shifter_2_out, WB_IR, \流水器器件_2_imm_b_2 ,
       \流水器器件_2_imm_j_2 , \流水器器件_2_imm_si_2 , \流水器器件_2_pc_4_2 , \流水器器件_2_r1_2 , \流水器器件_2_r2_2 ,
       \流水器器件_3_pc_4_2 ;

  Button \u_总复位  (.out(RST));
  Button _1 (.out(IR1));
  Button _2 (.out(IR2));
  Button _3 (.out(IR3));
  // Probe on \总周期数 
  // Probe on \总周期数 
  Button \u_继续运行  (.out(Go));
  LED #(.active("true")) led_1 (.in(W1));
  LED #(.active("true")) led_2 (.in(W2));
  LED #(.active("true")) led_3 (.in(W3));
  Hex_Digit_Display hex_digit_display_1 (.value(LedData[31:28]));  // open: dp
  // Probe on IF_PC[19:0]
  // RiscV_Probe riscv_probe_1: pin names not known; wires that end beside it: IF_IR
  Hex_Digit_Display hex_digit_display_2 (.value(LedData[27:24]));  // open: dp
  Hex_Digit_Display hex_digit_display_3 (.value(LedData[23:20]));  // open: dp
  // Probe on ID_PC[19:0]
  // RiscV_Probe riscv_probe_2: pin names not known; wires that end beside it: ID_IR
  Hex_Digit_Display hex_digit_display_4 (.value(LedData[19:16]));  // open: dp
  Hex_Digit_Display hex_digit_display_5 (.value(LedData[15:12]));  // open: dp
  Hex_Digit_Display hex_digit_display_6 (.value(LedData[11:8]));  // open: dp
  Hex_Digit_Display hex_digit_display_7 (.value(LedData[7:4]));  // open: dp
  // Probe on EX_PC[19:0]
  // RiscV_Probe riscv_probe_3: pin names not known; wires that end beside it: EX_IR
  and and_1 (and_1_out, alu_1_out_4, \流水器器件_2_begue_2 );
  assign and_2_out = 32'hfffffffe & alu_1_result;  // AND_Gate and_2, 32 bits wide
  Hex_Digit_Display hex_digit_display_8 (.value(LedData[3:0]));  // open: dp
  not not_1 (not_1_out, alu_1_equal);
  and and_3 (and_3_out, \流水器器件_2_beq_2 , alu_1_equal);
  and and_4 (and_4_out, not_1_out, \流水器器件_2_bne_2 );
  or or_1 (or_1_out, and_1_out, and_3_out, and_4_out);
  Priority_Encoder #(.select(2), .disabled("Z")) priority_encoder_1 (
    .in0(1'b1), .in1(or_1_out), .in2(\流水器器件_2_jal_2 ), .in3(\流水器器件_2_jalr_2 ), .out(priority_encoder_1_out));  // open: gs, en_out, en_in
  Multiplexer #(.select(2), .width(32), .disabled("Z"), .enable("false")) multiplexer_1 (
    .in0(adder_1_out), .in1(\流水器器件_2_imm_b_2 ), .in2(\流水器器件_2_imm_j_2 ), .in3(and_2_out),
    .out(multiplexer_1_out), .sel(priority_encoder_1_out));
  // Probe on \总周期数 
  // Probe on M_PC[19:0]
  // RiscV_Probe riscv_probe_4: pin names not known; wires that end beside it: MEM_IR
  Register #(.width(32), .trigger("rising"), .Select("low")) PC (
    .D(multiplexer_1_out), .en(not_2_out), .Q(IF_PC), .clk(CLK), .clr(RST));
  not not_2 (not_2_out, or_2_out);
  or or_2 (or_2_out, \阻塞 , halt);
  // Probe on \总周期数 
  // Probe on \无条件分支数 
  // Probe on \条件分支成功数 
  // Probe on \插入气泡数 
  // Probe on \LoadUse次数 
  // Probe on IF_PC[11:0]
  // Probe on WB_PC[19:0]
  // RiscV_Probe riscv_probe_5: pin names not known; wires that end beside it: WB_IR
  Adder #(.width(32)) adder_1 (.a(IF_PC), .b(32'h4), .out(adder_1_out));  // open: cin, cout
  // Probe on EX_PC[11:0]
  // Probe on ID_PC[11:0]
  Multiplexer #(.select(1), .width(1), .disabled("Z"), .enable("false")) multiplexer_2 (
    .in0(1'b1), .in1(1'b0), .out(multiplexer_2_out), .sel(halt));
  ROM #(.addrWidth(10), .dataWidth(32), .Select("high")) rom_1 (.addr(IF_PC[11:2]), .data(rom_1_data));
  // Probe on M_PC[11:0]
  D_Flip_Flop #(.trigger("high"), .Pre_Clr_Positions("LEGACY"), .NegatePresetClear("false"), .enable("true"), .NewFFLayout("false")) d_ff_1 (.Q(d_ff_1_q));  // open: clk, D, Qn, preset, en, reset
  // Probe on 13'h19
  // RiscV_Probe riscv_probe_6: pin names not known; wires that end beside it: rom_1_data
  // Probe on WB_PC[11:0]
  Comparator #(.width(13), .mode("twosComplement")) comparator_1 (
    .a(CNT_num), .b(13'h19), .eq(comparator_1_eq), .lt(comparator_1_lt));  // open: gt
  Clock #(.highDuration(1), .lowDuration(1)) clock_1 (.out(clock_1_out));
  \流水器器件  \u_流水器器件_1  (
    .PC(IF_PC), .PC_4(adder_1_out), .IR(rom_1_data), .PC_2(ID_PC), .PC_4_2(PC_4id), .IR_2(IR), .reset(1'b0),
    .refresh(\清空 ), .Halt_2(\阻塞 ), .clk(CLK), .valid(multiplexer_2_out), .valid_2(\流水器器件_1_valid_2 ));  // open: JAL, JALR, is_lb, begue, Beq, Bne, MemToReg, MemWrite, AluSrcB, RegWrite, S_type, ecall, halt, AluOp, rd, R1, R2, imm_si, imm_b, imm_j, JAL_2, JALR_2, is_lb_2, begue_2, Beq_2, Bne_2, MemToReg_2, MemWrite_2, AluSrcB_2, RegWrite_2, S_type_2, ecall_2, halt_3, Aluop_2, rd_2, R1_2, R2_2, imm_si_2, imm_b_2, imm_j_2, predict, predict_2
  nand nand_1 (nand_1_out, d_ff_1_q, comparator_1_eq);
  Counter #(.width(13), .max('h1fff), .ongoal("stay"), .trigger("rising"), .behavior("old")) counter_1 (
    .count(comparator_1_lt), .Q(CNT_num), .clk(clock_1_out));  // open: load, D, carry, clr, preset
  or or_3 (or_3_out, \清空 , \阻塞 );
  // RiscV_Probe riscv_probe_7: pin names not known; wires that end beside it: IR, riscv_probe_7_p2
  assign CLK = nand_1_out ? clock_1_out : 1'bz;  // Controlled_Buffer controlled_buffer_1
  Pull_Resistor #(.pull(1)) pull_resistor_1 (.node(CLK));
  Multiplexer #(.select(1), .width(5), .disabled("Z"), .enable("false")) multiplexer_3 (
    .in0(IR[19:15]), .in1(5'b10001), .out(multiplexer_3_out), .sel(ecall));
  Multiplexer #(.select(1), .width(5), .disabled("Z"), .enable("false")) multiplexer_4 (
    .in0(IR[24:20]), .in1(5'b01010), .out(multiplexer_4_out), .sel(ecall));
  \气泡器件  \u_气泡器件_1  (
    .rs1(multiplexer_3_out), .BranchTaken(or_4_out), .rs2(multiplexer_4_out),
    .rs1_used(\单周期硬布线控制器_1_rs1_used ), .rs2_used(\单周期硬布线控制器_1_rs2_used ), .ex_WriteReg(\流水器器件_2_rd_2 ),
    .ex_RegWrite(\流水器器件_2_regwrite_2 ), .Mem_WriteReg(\流水器器件_3_rd_2 ), .Mem_RegWrite(\流水器器件_3_regwrite_2 ),
    .\清空 (\清空 ), .\阻塞 (\阻塞 ));
  \单周期硬布线控制器  \u_单周期硬布线控制器_1  (
    .Funct({IR[30], IR[25], IR[14:12]}), .OP(IR[6:2]), .ALU_OP(\单周期硬布线控制器_1_alu_op ),
    .MemToReg(\单周期硬布线控制器_1_memtoreg ), .MemWrite(\单周期硬布线控制器_1_memwrite ), .ALU_SRC(\单周期硬布线控制器_1_alu_src ),
    .RegWrite(\单周期硬布线控制器_1_regwrite ), .ecall(ecall), .S_type(S_type), .Jalr(JALR), .Beq(\单周期硬布线控制器_1_beq ),
    .JAL(JAL), .Bne(\单周期硬布线控制器_1_bne ), .in_3(IR[21]), .uret(riscv_probe_7_p2), .is_lb(is_lb), .bgue(bgue),
    .rs1_used(\单周期硬布线控制器_1_rs1_used ), .rs2_used(\单周期硬布线控制器_1_rs2_used ));
  Multiplexer #(.select(1), .width(12), .disabled("Z"), .enable("false")) multiplexer_5 (
    .in0(IR[31:20]), .in1({IR[31:25], IR[11:7]}), .out(multiplexer_5_out), .sel(S_type));
  assign bit_extender_1_out = {{20{IR[31]}}, {IR[31], IR[7], IR[30:25], IR[11:8]}};  // Bit_Extender bit_extender_1
  assign bit_extender_2_out = {{12{IR[31]}}, {IR[31], IR[19:12], IR[20], IR[30:21]}};  // Bit_Extender bit_extender_2
  assign bit_extender_3_out = {{20{multiplexer_5_out[11]}}, multiplexer_5_out};  // Bit_Extender bit_extender_3
  Shifter #(.width(32), .shift("ll")) shifter_1 (.in(bit_extender_1_out), .\dist (5'b00001), .out(shifter_1_out));
  not not_3 (not_3_out, CLK);
  Regifile regifile_1 (
    .Din(RDin), .Clk(not_3_out), .R1(R1), .R2(regifile_1_r2), .WE(RegWrite), .W_num(\流水器器件_4_rd_2 ),
    .R1_num(multiplexer_3_out), .R2_num(multiplexer_4_out));
  Shifter #(.width(32), .shift("ll")) shifter_2 (.in(bit_extender_2_out), .\dist (5'b00001), .out(shifter_2_out));
  or or_4 (or_4_out, priority_encoder_1_out[0], priority_encoder_1_out[1]);
  Adder #(.width(32)) adder_2 (.a(shifter_1_out), .b(ID_PC), .out(bout));  // open: cin, cout
  Adder #(.width(32)) adder_3 (.a(shifter_2_out), .b(ID_PC), .out(jout));  // open: cin, cout
  not not_4 (not_4_out, \流水器器件_1_valid_2 );
  \流水器器件  \u_流水器器件_2  (
    .JAL(JAL), .JALR(JALR), .is_lb(is_lb), .begue(bgue), .Beq(\单周期硬布线控制器_1_beq ), .Bne(\单周期硬布线控制器_1_bne ),
    .MemToReg(\单周期硬布线控制器_1_memtoreg ), .MemWrite(\单周期硬布线控制器_1_memwrite ), .AluSrcB(\单周期硬布线控制器_1_alu_src ),
    .RegWrite(\单周期硬布线控制器_1_regwrite ), .S_type(S_type), .ecall(ecall), .AluOp(\单周期硬布线控制器_1_alu_op ),
    .rd(IR[11:7]), .R1(R1), .R2(regifile_1_r2), .PC(ID_PC), .PC_4(PC_4id), .imm_si(bit_extender_3_out),
    .imm_b(bout), .imm_j(jout), .JAL_2(\流水器器件_2_jal_2 ), .JALR_2(\流水器器件_2_jalr_2 ),
    .is_lb_2(\流水器器件_2_is_lb_2 ), .begue_2(\流水器器件_2_begue_2 ), .Beq_2(\流水器器件_2_beq_2 ),
    .Bne_2(\流水器器件_2_bne_2 ), .MemToReg_2(\流水器器件_2_memtoreg_2 ), .MemWrite_2(\流水器器件_2_memwrite_2 ),
    .AluSrcB_2(\流水器器件_2_alusrcb_2 ), .RegWrite_2(\流水器器件_2_regwrite_2 ), .ecall_2(\流水器器件_2_ecall_2 ),
    .Aluop_2(\流水器器件_2_aluop_2 ), .rd_2(\流水器器件_2_rd_2 ), .R1_2(\流水器器件_2_r1_2 ), .R2_2(\流水器器件_2_r2_2 ),
    .PC_2(EX_PC), .PC_4_2(\流水器器件_2_pc_4_2 ), .imm_si_2(\流水器器件_2_imm_si_2 ), .imm_b_2(\流水器器件_2_imm_b_2 ),
    .imm_j_2(\流水器器件_2_imm_j_2 ), .reset(not_4_out), .refresh(or_3_out), .Halt_2(halt), .clk(CLK),
    .valid(\流水器器件_1_valid_2 ), .valid_2(\流水器器件_2_valid_2 ));  // open: halt, IR, S_type_2, halt_3, IR_2, predict, predict_2
  Multiplexer #(.select(1), .width(32), .disabled("Z"), .enable("false")) multiplexer_6 (
    .in0(\流水器器件_2_r2_2 ), .in1(\流水器器件_2_imm_si_2 ), .out(multiplexer_6_out), .sel(\流水器器件_2_alusrcb_2 ));
  Comparator #(.width(32), .mode("twosComplement")) comparator_2 (
    .a(\流水器器件_2_r1_2 ), .b(32'h22), .eq(comparator_2_eq));  // open: gt, lt
  Comparator #(.width(32), .mode("twosComplement")) comparator_3 (
    .a(\流水器器件_2_r1_2 ), .b(32'h22), .eq(comparator_3_eq));  // open: gt, lt
  and and_5 (and_5_out, ~comparator_3_eq, \流水器器件_2_ecall_2 );  // AND_Gate
  ALU alu_1 (
    .X(\流水器器件_2_r1_2 ), .Y(multiplexer_6_out), .AluOP(\流水器器件_2_aluop_2 ), .Equal(alu_1_equal),
    .Result(alu_1_result), .Result_2(Alu_out2), .out_4(alu_1_out_4), .out_6(less));
  and and_6 (and_6_out, \流水器器件_2_ecall_2 , comparator_2_eq);
  Register #(.width(32), .trigger("rising"), .Select("low")) register_1 (
    .D(\流水器器件_2_r2_2 ), .en(and_6_out), .Q(LedData), .clk(CLK));  // open: clr
  not not_5 (not_5_out, \流水器器件_2_valid_2 );
  \流水器器件  \u_流水器器件_3  (
    .JAL(\流水器器件_2_jal_2 ), .JALR(\流水器器件_2_jalr_2 ), .is_lb(\流水器器件_2_is_lb_2 ),
    .MemToReg(\流水器器件_2_memtoreg_2 ), .MemWrite(\流水器器件_2_memwrite_2 ), .RegWrite(\流水器器件_2_regwrite_2 ),
    .halt(and_5_out), .rd(\流水器器件_2_rd_2 ), .R2(\流水器器件_2_r2_2 ), .PC(EX_PC), .PC_4(\流水器器件_2_pc_4_2 ),
    .imm_si(alu_1_result), .JAL_2(\流水器器件_3_jal_2 ), .JALR_2(\流水器器件_3_jalr_2 ), .is_lb_2(\流水器器件_3_is_lb_2 ),
    .MemToReg_2(\流水器器件_3_memtoreg_2 ), .MemWrite_2(MemWrite), .RegWrite_2(\流水器器件_3_regwrite_2 ),
    .halt_3(\流水器器件_3_halt_3 ), .rd_2(\流水器器件_3_rd_2 ), .R2_2(MDin), .PC_2(M_PC), .PC_4_2(\流水器器件_3_pc_4_2 ),
    .imm_si_2(Alu_out), .reset(not_5_out), .refresh(1'b0), .Halt_2(halt), .clk(CLK),
    .valid(\流水器器件_2_valid_2 ), .valid_2(\流水器器件_3_valid_2 ));  // open: begue, Beq, Bne, AluSrcB, S_type, ecall, AluOp, R1, imm_b, imm_j, IR, begue_2, Beq_2, Bne_2, AluSrcB_2, S_type_2, ecall_2, Aluop_2, R1_2, imm_b_2, imm_j_2, IR_2, predict, predict_2
  or or_5 (or_5_out, \流水器器件_3_jal_2 , \流水器器件_3_jalr_2 );
  Priority_Encoder #(.select(2), .disabled("Z")) priority_encoder_2 (
    .in0(1'b1), .in1(or_5_out), .in2(\流水器器件_3_memtoreg_2 ), .in3(1'b0), .out(priority_encoder_2_out));  // open: gs, en_out, en_in
  RAM #(.addrWidth(10), .dataWidth(32), .bus("separate"), .Select("high")) ram_1 (
    .addr(Alu_out[11:2]), .din(MDin), .data(ram_1_data), .str(MemWrite), .sel(1'b1), .clk(CLK),
    .ld(\流水器器件_3_memtoreg_2 ), .clr(1'b0));
  Multiplexer #(.select(1), .width(32), .disabled("Z"), .enable("false")) multiplexer_7 (
    .in0(ram_1_data), .in1(bit_extender_4_out), .out(multiplexer_7_out), .sel(\流水器器件_3_is_lb_2 ));
  Multiplexer #(.select(2), .width(8), .disabled("Z"), .enable("false")) multiplexer_8 (
    .in0(ram_1_data[7:0]), .in1(ram_1_data[15:8]), .in2(ram_1_data[23:16]), .in3(ram_1_data[31:24]),
    .out(multiplexer_8_out), .sel(Alu_out[1:0]));
  assign bit_extender_4_out = {{24{multiplexer_8_out[7]}}, multiplexer_8_out};  // Bit_Extender bit_extender_4
  Multiplexer #(.select(2), .width(32), .disabled("Z"), .enable("false")) multiplexer_9 (
    .in0(Alu_out), .in1(\流水器器件_3_pc_4_2 ), .in2(multiplexer_7_out), .out(multiplexer_9_out),
    .sel(priority_encoder_2_out));  // open: in3
  not not_6 (not_6_out, \流水器器件_3_valid_2 );
  \流水器器件  \u_流水器器件_4  (
    .RegWrite(\流水器器件_3_regwrite_2 ), .halt(\流水器器件_3_halt_3 ), .rd(\流水器器件_3_rd_2 ), .PC(M_PC),
    .imm_si(Alu_out), .IR(multiplexer_9_out), .RegWrite_2(RegWrite), .halt_3(\流水器器件_4_halt_3 ),
    .rd_2(\流水器器件_4_rd_2 ), .PC_2(WB_PC), .IR_2(RDin), .reset(not_6_out), .refresh(1'b0), .Halt_2(halt),
    .clk(CLK), .valid(\流水器器件_3_valid_2 ));  // open: JAL, JALR, is_lb, begue, Beq, Bne, MemToReg, MemWrite, AluSrcB, S_type, ecall, AluOp, R1, R2, PC_4, imm_b, imm_j, JAL_2, JALR_2, is_lb_2, begue_2, Beq_2, Bne_2, MemToReg_2, MemWrite_2, AluSrcB_2, S_type_2, ecall_2, Aluop_2, R1_2, R2_2, PC_4_2, imm_si_2, imm_b_2, imm_j_2, valid_2, predict, predict_2
  Register #(.width(1), .trigger("falling"), .Select("low")) register_2 (
    .D(1'b0), .Q(register_2_q), .clk(\流水器器件_4_halt_3 ), .preset(Go));  // open: en, clr, cs
  and and_7 (and_7_out, ~register_2_q, \流水器器件_4_halt_3 );  // AND_Gate
  Register #(.width(1), .trigger("falling"), .Select("low")) register_3 (
    .D(and_7_out), .Q(halt), .clk(CLK));  // open: en, clr

  // Other names for the same wires on the sheet: rd[4:0] = IR[11:7]; MEM_PC[31:0] = M_PC; PC[31:0] = IF_PC;
  //   PCid[31:0] = ID_PC

  // Notes on the sheet:
  //   中断源
  //   时空图监测，可删除
  //   中断等待指示
  //   数码管输出
  //   指令存储器
  //   控制位
  //   指令探针
  //   contents of rom_1 (hex, n*v repeats v):
  //   100493 100006f 100493 200913 300993 100006f 100493 200913 300993 100006f 100493 200913 300993
  //   100006f 100493 200913 300993 29c000ef 100413 100493 1f49493 900533 2200893 73 24d493 48463 fedff06f
  //   900533 2200893 73 100493 249493 900533 2200893 73 48463 fedff06f 100493 1f49493 900533 2200893 73
  //   4034d493 900533 2200893 73 4044d493 900533 2200893 73 4044d493 900533 2200893 73 4044d493 900533
  //   2200893 73 4044d493 900533 2200893 73 4044d493 900533 2200893 73 4044d493 900533 2200893 73 4044d493
  //   900533 2200893 73 100413 1f41993 41f9d993 433 c00913 300b13 140413 f47413 800293 100313 499993
  //   89e9b3 1300533 2200893 73 406282b3 fe0294e3 140413 f00f93 1f47433 1c41413 800293 100313 49d993
  //   89e9b3 1300533 2200893 73 406282b3 fe0294e3 1c45413 406b0b33 b0463 f95ff06f 2b3 fff2c293 829293
  //   ff2e293 500533 2200893 73 fff00413 493 84a023 140413 448493 84a023 140413 448493 84a023 140413
  //   448493 84a023 140413 448493 84a023 140413 448493 84a023 140413 448493 84a023 140413 448493 84a023
  //   140413 448493 84a023 140413 448493 84a023 140413 448493 84a023 140413 448493 84a023 140413 448493
  //   84a023 140413 448493 84a023 140413 448493 84a023 140413 448493 84a023 140413 448493 140413 433
  //   3c00493 42983 4aa03 149a2b3 28663 134a023 1442023 ffc48493 fe9412e3 800533 2200893 73 440413 3c00493
  //   fc9416e3 a00893 73 413 140413 800533 2200893 73 240413 800533 2200893 73 340413 800533 2200893 73
  //   440413 800533 2200893 73 540413 800533 2200893 73 640413 800533 2200893 73 740413 800533 2200893 73
  //   840413 800533 2200893 2200893 73 8067
  //   流水调试日志用
  //   暂停节拍，不能为0
  //   戳工具置1进入计数暂停模式，ctrl+k时钟自动运行到对应节拍暂停
  //   ctrl+k关闭时钟连续运行，将控制位置零，进入单步调试模式调试
  //   阻塞的时候需要取消使能
  //   第二个寄存器两种情况都要清空
  //   可计数暂停的时钟源
  //   指令字
  //   b型
  //   j型
  //   清空
  //   JALR
  //   URET
  //   Beq
  //   Bne
  //   MemToReg
  //   MemWrite
  //   AluOP
  //   AluSrcB
  //   RegWrite
  //   为方便自动评测，需要输出流水线各段保存的PC值，注意是PC不是PC+4，另外ID段寄存器写入信息，Mem段内存写入信息也要输出
  //   阻塞
  //   R2
  //   aluop
  //   rd
  //   JAL
  //   JALR
  //   PC_4
  //   Aluout
  //   MemtoReg
  //   is_lb
  //   MemWrite
  //   处理sw
  //   数据存储器
  //   R地址
  //   Rdata
  //   写回寄存器有四种情况，R型，jalrjal，lb
  //   Aluout
  //   写回data
endmodule

module \重定向流水线  (
  output RegWrite,
  output MemWrite,
  output [31:0] IF_PC,
  output [31:0] ID_PC,
  output [31:0] EX_PC,
  output [31:0] M_PC,
  output [31:0] WB_PC,
  output [31:0] RDin,
  output [31:0] MDin,
  output [31:0] LedData
);

  wire alu_1_equal, alu_1_out_4, and_1_out, and_3_out, and_4_out, and_5_out, and_6_out, and_7_out, bgue, CLK,
       clock_1_out, comparator_1_eq, comparator_1_lt, comparator_2_eq, comparator_3_eq, d_ff_1_q, ecall, Go,
       halt, IR1, IR2, IR3, is_lb, JAL, JALR, less, loadused, multiplexer_2_out, nand_1_out, not_1_out,
       not_2_out, not_3_out, not_4_out, not_5_out, not_6_out, or_1_out, or_2_out, or_3_out, or_4_out,
       or_5_out, register_2_q, RST, S_type, W1, W2, W3, \单周期硬布线控制器_1_alu_src , \单周期硬布线控制器_1_beq ,
       \单周期硬布线控制器_1_bne , \单周期硬布线控制器_1_memtoreg , \单周期硬布线控制器_1_memwrite , \单周期硬布线控制器_1_regwrite ,
       \单周期硬布线控制器_1_rs1_used , \单周期硬布线控制器_1_rs2_used , \单周期硬布线控制器_1_uret , \流水器器件_1_valid_2 ,
       \流水器器件_2_alusrcb_2 , \流水器器件_2_begue_2 , \流水器器件_2_beq_2 , \流水器器件_2_bne_2 , \流水器器件_2_ecall_2 ,
       \流水器器件_2_is_lb_2 , \流水器器件_2_jal_2 , \流水器器件_2_jalr_2 , \流水器器件_2_memtoreg_2 , \流水器器件_2_memwrite_2 ,
       \流水器器件_2_regwrite_2 , \流水器器件_2_valid_2 , \流水器器件_3_halt_3 , \流水器器件_3_is_lb_2 , \流水器器件_3_jal_2 ,
       \流水器器件_3_jalr_2 , \流水器器件_3_memtoreg_2 , \流水器器件_3_regwrite_2 , \流水器器件_3_valid_2 , \流水器器件_4_halt_3 ;
  wire [1:0] foward_1_rs1_foward_2, foward_1_rs2_foward_2, priority_encoder_1_out, priority_encoder_2_out,
       \重定向_1_r1foward , \重定向_1_r2forward ;
  wire [3:0] \单周期硬布线控制器_1_alu_op , \流水器器件_2_aluop_2 ;
  wire [4:0] multiplexer_3_out, multiplexer_4_out, \流水器器件_2_rd_2 , \流水器器件_3_rd_2 , \流水器器件_4_rd_2 ;
  wire [7:0] multiplexer_10_out;
  wire [11:0] multiplexer_5_out;
  wire [12:0] CNT_num;
  wire [15:0] \LoadUse次数 , \总周期数 , \插入气泡数 , \无条件分支数 , \条件分支成功数 ;
  wire [31:0] a, ab, adder_1_out, alu_1_result, Alu_out, Alu_out2, and_2_out, bit_extender_1_out,
       bit_extender_2_out, bit_extender_3_out, bit_extender_4_out, bout, c, cd, EX_IR, ID_IR, IF_IR, IR,
       jout, MEM_IR, multiplexer_1_out, multiplexer_6_out, multiplexer_9_out, multiplexer_11_out, PC_4id, R1,
       ram_1_data, regifile_1_r2, rom_1_data, shifter_1_out, shifter_2_out, WB_IR, \流水器器件_2_imm_b_2 ,
       \流水器器件_2_imm_j_2 , \流水器器件_2_imm_si_2 , \流水器器件_2_pc_4_2 , \流水器器件_3_pc_4_2 ;

  Button \u_总复位  (.out(RST));
  Button _1 (.out(IR1));
  Button _2 (.out(IR2));
  Button _3 (.out(IR3));
  // Probe on \总周期数 
  // Probe on \总周期数 
  Button \u_继续运行  (.out(Go));
  LED #(.active("true")) led_1 (.in(W1));
  LED #(.active("true")) led_2 (.in(W2));
  LED #(.active("true")) led_3 (.in(W3));
  Hex_Digit_Display hex_digit_display_1 (.value(LedData[31:28]));  // open: dp
  // Probe on IF_PC[19:0]
  // RiscV_Probe riscv_probe_1: pin names not known; wires that end beside it: IF_IR
  Hex_Digit_Display hex_digit_display_2 (.value(LedData[23:20]));  // open: dp
  Hex_Digit_Display hex_digit_display_3 (.value(LedData[27:24]));  // open: dp
  // Probe on ID_PC[19:0]
  // RiscV_Probe riscv_probe_2: pin names not known; wires that end beside it: ID_IR
  Hex_Digit_Display hex_digit_display_4 (.value(LedData[15:12]));  // open: dp
  Hex_Digit_Display hex_digit_display_5 (.value(LedData[19:16]));  // open: dp
  Hex_Digit_Display hex_digit_display_6 (.value(LedData[11:8]));  // open: dp
  Hex_Digit_Display hex_digit_display_7 (.value(LedData[7:4]));  // open: dp
  // Probe on EX_PC[19:0]
  // RiscV_Probe riscv_probe_3: pin names not known; wires that end beside it: EX_IR
  and and_1 (and_1_out, alu_1_out_4, \流水器器件_2_begue_2 );
  assign and_2_out = 32'hfffffffe & alu_1_result;  // AND_Gate and_2, 32 bits wide
  Hex_Digit_Display hex_digit_display_8 (.value(LedData[3:0]));  // open: dp
  not not_1 (not_1_out, alu_1_equal);
  and and_3 (and_3_out, not_1_out, \流水器器件_2_bne_2 );
  and and_4 (and_4_out, \流水器器件_2_beq_2 , alu_1_equal);
  or or_1 (or_1_out, and_1_out, and_4_out, and_3_out);
  Priority_Encoder #(.select(2), .disabled("Z")) priority_encoder_1 (
    .in0(1'b1), .in1(or_1_out), .in2(\流水器器件_2_jal_2 ), .in3(\流水器器件_2_jalr_2 ), .out(priority_encoder_1_out));  // open: gs, en_out, en_in
  Multiplexer #(.select(2), .width(32), .disabled("Z"), .enable("false")) multiplexer_1 (
    .in0(adder_1_out), .in1(\流水器器件_2_imm_b_2 ), .in2(\流水器器件_2_imm_j_2 ), .in3(and_2_out),
    .out(multiplexer_1_out), .sel(priority_encoder_1_out));
  // Probe on \总周期数 
  // Probe on M_PC[19:0]
  // RiscV_Probe riscv_probe_4: pin names not known; wires that end beside it: MEM_IR
  Register #(.width(32), .trigger("rising"), .Select("low")) PC (
    .D(multiplexer_1_out), .en(not_2_out), .Q(IF_PC), .clk(CLK), .clr(RST));
  not not_2 (not_2_out, or_2_out);
  or or_2 (or_2_out, loadused, halt);
  // Probe on \总周期数 
  // Probe on \无条件分支数 
  // Probe on \条件分支成功数 
  // Probe on \插入气泡数 
  // Probe on \LoadUse次数 
  // Probe on IF_PC[11:0]
  // Probe on WB_PC[19:0]
  // RiscV_Probe riscv_probe_5: pin names not known; wires that end beside it: WB_IR
  Adder #(.width(32)) adder_1 (.a(IF_PC), .b(32'h4), .out(adder_1_out));  // open: cin, cout
  // Probe on EX_PC[11:0]
  // Probe on ID_PC[11:0]
  Multiplexer #(.select(1), .width(1), .disabled("Z"), .enable("false")) multiplexer_2 (
    .in0(1'b1), .in1(1'b0), .out(multiplexer_2_out), .sel(halt));
  ROM #(.addrWidth(10), .dataWidth(32), .Select("high")) rom_1 (.addr(IF_PC[11:2]), .data(rom_1_data));
  // Probe on M_PC[11:0]
  D_Flip_Flop #(.trigger("high"), .Pre_Clr_Positions("LEGACY"), .NegatePresetClear("false"), .enable("true"), .NewFFLayout("false")) d_ff_1 (.Q(d_ff_1_q));  // open: clk, D, Qn, preset, en, reset
  // Probe on 13'h334
  // RiscV_Probe riscv_probe_6: pin names not known; wires that end beside it: rom_1_data
  // Probe on WB_PC[11:0]
  Comparator #(.width(13), .mode("twosComplement")) comparator_1 (
    .a(CNT_num), .b(13'h334), .eq(comparator_1_eq), .lt(comparator_1_lt));  // open: gt
  Clock #(.highDuration(1), .lowDuration(1)) clock_1 (.out(clock_1_out));
  \流水器器件  \u_流水器器件_1  (
    .PC(IF_PC), .PC_4(adder_1_out), .IR(rom_1_data), .PC_2(ID_PC), .PC_4_2(PC_4id), .IR_2(IR), .reset(1'b0),
    .refresh(or_3_out), .Halt_2(loadused), .clk(CLK), .valid(multiplexer_2_out), .valid_2(\流水器器件_1_valid_2 ));  // open: JAL, JALR, is_lb, begue, Beq, Bne, MemToReg, MemWrite, AluSrcB, RegWrite, S_type, ecall, halt, AluOp, rd, R1, R2, imm_si, imm_b, imm_j, JAL_2, JALR_2, is_lb_2, begue_2, Beq_2, Bne_2, MemToReg_2, MemWrite_2, AluSrcB_2, RegWrite_2, S_type_2, ecall_2, halt_3, Aluop_2, rd_2, R1_2, R2_2, imm_si_2, imm_b_2, imm_j_2, predict, predict_2
  nand nand_1 (nand_1_out, d_ff_1_q, comparator_1_eq);
  Counter #(.width(13), .max('h1fff), .ongoal("stay"), .trigger("rising"), .behavior("old")) counter_1 (
    .count(comparator_1_lt), .Q(CNT_num), .clk(clock_1_out));  // open: load, D, carry, clr, preset
  assign CLK = nand_1_out ? clock_1_out : 1'bz;  // Controlled_Buffer controlled_buffer_1
  Pull_Resistor #(.pull(1)) pull_resistor_1 (.node(CLK));
  Multiplexer #(.select(1), .width(5), .disabled("Z"), .enable("false")) multiplexer_3 (
    .in0(IR[19:15]), .in1(5'b10001), .out(multiplexer_3_out), .sel(ecall));
  Multiplexer #(.select(1), .width(5), .disabled("Z"), .enable("false")) multiplexer_4 (
    .in0(IR[24:20]), .in1(5'b01010), .out(multiplexer_4_out), .sel(ecall));
  \单周期硬布线控制器  \u_单周期硬布线控制器_1  (
    .Funct({IR[30], IR[25], IR[14:12]}), .OP(IR[6:2]), .ALU_OP(\单周期硬布线控制器_1_alu_op ),
    .MemToReg(\单周期硬布线控制器_1_memtoreg ), .MemWrite(\单周期硬布线控制器_1_memwrite ), .ALU_SRC(\单周期硬布线控制器_1_alu_src ),
    .RegWrite(\单周期硬布线控制器_1_regwrite ), .ecall(ecall), .S_type(S_type), .Jalr(JALR), .Beq(\单周期硬布线控制器_1_beq ),
    .JAL(JAL), .Bne(\单周期硬布线控制器_1_bne ), .in_3(IR[21]), .uret(\单周期硬布线控制器_1_uret ), .is_lb(is_lb), .bgue(bgue),
    .rs1_used(\单周期硬布线控制器_1_rs1_used ), .rs2_used(\单周期硬布线控制器_1_rs2_used ));
  Multiplexer #(.select(1), .width(12), .disabled("Z"), .enable("false")) multiplexer_5 (
    .in0(IR[31:20]), .in1({IR[31:25], IR[11:7]}), .out(multiplexer_5_out), .sel(S_type));
  assign bit_extender_1_out = {{20{IR[31]}}, {IR[31], IR[7], IR[30:25], IR[11:8]}};  // Bit_Extender bit_extender_1
  assign bit_extender_2_out = {{12{IR[31]}}, {IR[31], IR[19:12], IR[20], IR[30:21]}};  // Bit_Extender bit_extender_2
  assign bit_extender_3_out = {{20{multiplexer_5_out[11]}}, multiplexer_5_out};  // Bit_Extender bit_extender_3
  Shifter #(.width(32), .shift("ll")) shifter_1 (.in(bit_extender_1_out), .\dist (5'b00001), .out(shifter_1_out));
  not not_3 (not_3_out, CLK);
  Regifile regifile_1 (
    .Din(RDin), .Clk(not_3_out), .R1(R1), .R2(regifile_1_r2), .WE(RegWrite), .W_num(\流水器器件_4_rd_2 ),
    .R1_num(multiplexer_3_out), .R2_num(multiplexer_4_out));
  Shifter #(.width(32), .shift("ll")) shifter_2 (.in(bit_extender_2_out), .\dist (5'b00001), .out(shifter_2_out));
  Adder #(.width(32)) adder_2 (.a(shifter_1_out), .b(ID_PC), .out(bout));  // open: cin, cout
  Adder #(.width(32)) adder_3 (.a(shifter_2_out), .b(ID_PC), .out(jout));  // open: cin, cout
  or or_3 (or_3_out, priority_encoder_1_out[0], priority_encoder_1_out[1]);
  not not_4 (not_4_out, \流水器器件_1_valid_2 );
  \重定向  \u_重定向_1  (
    .rs1_used(\单周期硬布线控制器_1_rs1_used ), .ex_memtoReg(\流水器器件_2_memtoreg_2 ),
    .ex_RegWrite(\流水器器件_2_regwrite_2 ), .rs2_used(\单周期硬布线控制器_1_rs2_used ), .ex_WriteReg(\流水器器件_2_rd_2 ),
    .rs1(multiplexer_3_out), .Mem_RegWrite(\流水器器件_3_regwrite_2 ), .rs2(multiplexer_4_out),
    .Mem_WriteReg(\流水器器件_3_rd_2 ), .LoadUse(loadused), .r1Foward(\重定向_1_r1foward ),
    .r2Forward(\重定向_1_r2forward ));
  or or_4 (or_4_out, not_4_out, loadused);
  \流水器器件  \u_流水器器件_2  (
    .JAL(JAL), .JALR(JALR), .is_lb(is_lb), .begue(bgue), .Beq(\单周期硬布线控制器_1_beq ), .Bne(\单周期硬布线控制器_1_bne ),
    .MemToReg(\单周期硬布线控制器_1_memtoreg ), .MemWrite(\单周期硬布线控制器_1_memwrite ), .AluSrcB(\单周期硬布线控制器_1_alu_src ),
    .RegWrite(\单周期硬布线控制器_1_regwrite ), .S_type(S_type), .ecall(ecall), .AluOp(\单周期硬布线控制器_1_alu_op ),
    .rd(IR[11:7]), .R1(R1), .R2(regifile_1_r2), .PC(ID_PC), .PC_4(PC_4id), .imm_si(bit_extender_3_out),
    .imm_b(bout), .imm_j(jout), .JAL_2(\流水器器件_2_jal_2 ), .JALR_2(\流水器器件_2_jalr_2 ),
    .is_lb_2(\流水器器件_2_is_lb_2 ), .begue_2(\流水器器件_2_begue_2 ), .Beq_2(\流水器器件_2_beq_2 ),
    .Bne_2(\流水器器件_2_bne_2 ), .MemToReg_2(\流水器器件_2_memtoreg_2 ), .MemWrite_2(\流水器器件_2_memwrite_2 ),
    .AluSrcB_2(\流水器器件_2_alusrcb_2 ), .RegWrite_2(\流水器器件_2_regwrite_2 ), .ecall_2(\流水器器件_2_ecall_2 ),
    .Aluop_2(\流水器器件_2_aluop_2 ), .rd_2(\流水器器件_2_rd_2 ), .R1_2(a), .R2_2(c), .PC_2(EX_PC),
    .PC_4_2(\流水器器件_2_pc_4_2 ), .imm_si_2(\流水器器件_2_imm_si_2 ), .imm_b_2(\流水器器件_2_imm_b_2 ),
    .imm_j_2(\流水器器件_2_imm_j_2 ), .reset(or_4_out), .refresh(or_3_out), .Halt_2(halt), .clk(CLK),
    .valid(\流水器器件_1_valid_2 ), .valid_2(\流水器器件_2_valid_2 ));  // open: halt, IR, S_type_2, halt_3, IR_2, predict, predict_2
  Multiplexer #(.select(1), .width(32), .disabled("Z"), .enable("false")) multiplexer_6 (
    .in0(cd), .in1(\流水器器件_2_imm_si_2 ), .out(multiplexer_6_out), .sel(\流水器器件_2_alusrcb_2 ));
  Comparator #(.width(32), .mode("twosComplement")) comparator_2 (
    .a(ab), .b(32'h22), .eq(comparator_2_eq));  // open: gt, lt
  Comparator #(.width(32), .mode("twosComplement")) comparator_3 (
    .a(32'h22), .b(ab), .eq(comparator_3_eq));  // open: gt, lt
  and and_5 (and_5_out, ~comparator_3_eq, \流水器器件_2_ecall_2 );  // AND_Gate
  foward foward_1 (
    .rs1_foward(\重定向_1_r1foward ), .rs2_foward(\重定向_1_r2forward ), .paopao(loadused), .clk(CLK),
    .rs1_foward_2(foward_1_rs1_foward_2), .rs2_foward_2(foward_1_rs2_foward_2));
  ALU alu_1 (
    .X(ab), .Y(multiplexer_6_out), .AluOP(\流水器器件_2_aluop_2 ), .Equal(alu_1_equal), .Result(alu_1_result),
    .Result_2(Alu_out2), .out_4(alu_1_out_4), .out_6(less));
  and and_6 (and_6_out, \流水器器件_2_ecall_2 , comparator_2_eq);
  Register #(.width(32), .trigger("rising"), .Select("low")) register_1 (
    .D(cd), .en(and_6_out), .Q(LedData), .clk(CLK));  // open: clr
  not not_5 (not_5_out, \流水器器件_2_valid_2 );
  \流水器器件  \u_流水器器件_3  (
    .JAL(\流水器器件_2_jal_2 ), .JALR(\流水器器件_2_jalr_2 ), .is_lb(\流水器器件_2_is_lb_2 ),
    .MemToReg(\流水器器件_2_memtoreg_2 ), .MemWrite(\流水器器件_2_memwrite_2 ), .RegWrite(\流水器器件_2_regwrite_2 ),
    .halt(and_5_out), .rd(\流水器器件_2_rd_2 ), .R2(cd), .PC(EX_PC), .PC_4(\流水器器件_2_pc_4_2 ),
    .imm_si(alu_1_result), .JAL_2(\流水器器件_3_jal_2 ), .JALR_2(\流水器器件_3_jalr_2 ), .is_lb_2(\流水器器件_3_is_lb_2 ),
    .MemToReg_2(\流水器器件_3_memtoreg_2 ), .MemWrite_2(MemWrite), .RegWrite_2(\流水器器件_3_regwrite_2 ),
    .halt_3(\流水器器件_3_halt_3 ), .rd_2(\流水器器件_3_rd_2 ), .R2_2(MDin), .PC_2(M_PC), .PC_4_2(\流水器器件_3_pc_4_2 ),
    .imm_si_2(Alu_out), .reset(not_5_out), .refresh(1'b0), .Halt_2(halt), .clk(CLK),
    .valid(\流水器器件_2_valid_2 ), .valid_2(\流水器器件_3_valid_2 ));  // open: begue, Beq, Bne, AluSrcB, S_type, ecall, AluOp, R1, imm_b, imm_j, IR, begue_2, Beq_2, Bne_2, AluSrcB_2, S_type_2, ecall_2, Aluop_2, R1_2, imm_b_2, imm_j_2, IR_2, predict, predict_2
  Multiplexer #(.select(2), .width(32), .disabled("Z"), .enable("false")) multiplexer_7 (
    .in0(a), .in1(RDin), .in2(Alu_out), .out(ab), .sel(foward_1_rs1_foward_2));  // open: in3
  or or_5 (or_5_out, \流水器器件_3_jal_2 , \流水器器件_3_jalr_2 );
  Multiplexer #(.select(2), .width(32), .disabled("Z"), .enable("false")) multiplexer_8 (
    .in0(c), .in1(RDin), .in2(Alu_out), .out(cd), .sel(foward_1_rs2_foward_2));  // open: in3
  Priority_Encoder #(.select(2), .disabled("Z")) priority_encoder_2 (
    .in0(1'b1), .in1(or_5_out), .in2(\流水器器件_3_memtoreg_2 ), .in3(1'b0), .out(priority_encoder_2_out));  // open: gs, en_out, en_in
  RAM #(.addrWidth(10), .dataWidth(32), .bus("separate"), .Select("high")) ram_1 (
    .addr(Alu_out[11:2]), .din(MDin), .data(ram_1_data), .str(MemWrite), .sel(1'b1), .clk(CLK),
    .ld(\流水器器件_3_memtoreg_2 ), .clr(1'b0));
  Multiplexer #(.select(1), .width(32), .disabled("Z"), .enable("false")) multiplexer_9 (
    .in0(ram_1_data), .in1(bit_extender_4_out), .out(multiplexer_9_out), .sel(\流水器器件_3_is_lb_2 ));
  assign bit_extender_4_out = {{24{multiplexer_10_out[7]}}, multiplexer_10_out};  // Bit_Extender bit_extender_4
  Multiplexer #(.select(2), .width(8), .disabled("Z"), .enable("false")) multiplexer_10 (
    .in0(ram_1_data[7:0]), .in1(ram_1_data[15:8]), .in2(ram_1_data[23:16]), .in3(ram_1_data[31:24]),
    .out(multiplexer_10_out), .sel(Alu_out[1:0]));
  Multiplexer #(.select(2), .width(32), .disabled("Z"), .enable("false")) multiplexer_11 (
    .in0(Alu_out), .in1(\流水器器件_3_pc_4_2 ), .in2(multiplexer_9_out), .out(multiplexer_11_out),
    .sel(priority_encoder_2_out));  // open: in3
  not not_6 (not_6_out, \流水器器件_3_valid_2 );
  \流水器器件  \u_流水器器件_4  (
    .RegWrite(\流水器器件_3_regwrite_2 ), .halt(\流水器器件_3_halt_3 ), .rd(\流水器器件_3_rd_2 ), .PC(M_PC),
    .imm_si(Alu_out), .IR(multiplexer_11_out), .RegWrite_2(RegWrite), .halt_3(\流水器器件_4_halt_3 ),
    .rd_2(\流水器器件_4_rd_2 ), .PC_2(WB_PC), .IR_2(RDin), .reset(not_6_out), .refresh(1'b0), .Halt_2(halt),
    .clk(CLK), .valid(\流水器器件_3_valid_2 ));  // open: JAL, JALR, is_lb, begue, Beq, Bne, MemToReg, MemWrite, AluSrcB, S_type, ecall, AluOp, R1, R2, PC_4, imm_b, imm_j, JAL_2, JALR_2, is_lb_2, begue_2, Beq_2, Bne_2, MemToReg_2, MemWrite_2, AluSrcB_2, S_type_2, ecall_2, Aluop_2, R1_2, R2_2, PC_4_2, imm_si_2, imm_b_2, imm_j_2, valid_2, predict, predict_2
  Register #(.width(1), .trigger("falling"), .Select("low")) register_2 (
    .D(1'b0), .Q(register_2_q), .clk(\流水器器件_4_halt_3 ), .preset(Go));  // open: en, clr, cs
  and and_7 (and_7_out, ~register_2_q, \流水器器件_4_halt_3 );  // AND_Gate
  Register #(.width(1), .trigger("falling"), .Select("low")) register_3 (
    .D(and_7_out), .Q(halt), .clk(CLK));  // open: en, clr

  // Other names for the same wires on the sheet: rd[4:0] = IR[11:7]; MEM_PC[31:0] = M_PC; PC[31:0] = IF_PC;
  //   PCid[31:0] = ID_PC

  // Notes on the sheet:
  //   中断源
  //   时空图监测，可删除
  //   中断等待指示
  //   数码管输出
  //   指令存储器
  //   控制位
  //   指令探针
  //   contents of rom_1 (hex, n*v repeats v):
  //   100493 100006f 100493 200913 300993 100006f 100493 200913 300993 100006f 100493 200913 300993
  //   100006f 100493 200913 300993 29c000ef 100413 100493 1f49493 900533 2200893 73 24d493 48463 fedff06f
  //   900533 2200893 73 100493 249493 900533 2200893 73 48463 fedff06f 100493 1f49493 900533 2200893 73
  //   4034d493 900533 2200893 73 4044d493 900533 2200893 73 4044d493 900533 2200893 73 4044d493 900533
  //   2200893 73 4044d493 900533 2200893 73 4044d493 900533 2200893 73 4044d493 900533 2200893 73 4044d493
  //   900533 2200893 73 100413 1f41993 41f9d993 433 c00913 300b13 140413 f47413 800293 100313 499993
  //   89e9b3 1300533 2200893 73 406282b3 fe0294e3 140413 f00f93 1f47433 1c41413 800293 100313 49d993
  //   89e9b3 1300533 2200893 73 406282b3 fe0294e3 1c45413 406b0b33 b0463 f95ff06f 2b3 fff2c293 829293
  //   ff2e293 500533 2200893 73 fff00413 493 84a023 140413 448493 84a023 140413 448493 84a023 140413
  //   448493 84a023 140413 448493 84a023 140413 448493 84a023 140413 448493 84a023 140413 448493 84a023
  //   140413 448493 84a023 140413 448493 84a023 140413 448493 84a023 140413 448493 84a023 140413 448493
  //   84a023 140413 448493 84a023 140413 448493 84a023 140413 448493 84a023 140413 448493 140413 433
  //   3c00493 42983 4aa03 149a2b3 28663 134a023 1442023 ffc48493 fe9412e3 800533 2200893 73 440413 3c00493
  //   fc9416e3 a00893 73 413 140413 800533 2200893 73 240413 800533 2200893 73 340413 800533 2200893 73
  //   440413 800533 2200893 73 540413 800533 2200893 73 640413 800533 2200893 73 740413 800533 2200893 73
  //   840413 800533 2200893 2200893 73 8067
  //   流水调试日志用
  //   暂停节拍，不能为0
  //   戳工具置1进入计数暂停模式，ctrl+k时钟自动运行到对应节拍暂停
  //   ctrl+k关闭时钟连续运行，将控制位置零，进入单步调试模式调试
  //   正常情况下，我们需要的值都在后面两个寄存器，但是我们如果是lb或者lw，我们的写回数据在寄存器中，如何区分呢，通过memtoreg
  //   可计数暂停的时钟源
  //   指令字
  //   b型
  //   j型
  //   JALR
  //   URET
  //   Beq
  //   Bne
  //   MemToReg
  //   MemWrite
  //   AluOP
  //   AluSrcB
  //   RegWrite
  //   为方便自动评测，需要输出流水线各段保存的PC值，注意是PC不是PC+4，另外ID段寄存器写入信息，Mem段内存写入信息也要输出
  //   R2
  //   aluop
  //   rd
  //   rs1_foward
  //   rs2_foward
  //   发现这个填0也是能过的
  //   JAL
  //   JALR
  //   PC_4
  //   Aluout
  //   MemtoReg
  //   is_lb
  //   MemWrite
  //   处理sw
  //   数据存储器
  //   写回寄存器有四种情况，R型，jalrjal，lb
  //   R地址
  //   Rdata
  //   Aluout
  //   写回data
endmodule

module \中断按键参考电路  (
  input  \同步清零信号 ,
  output \与中断屏蔽位与 
);

  wire \_1号中断_out , and_1_out, clock_1_out, d_ff_1_q, or_1_out, or_2_out;

  Clock #(.highDuration(1), .lowDuration(1)) clock_1 (.out(clock_1_out));
  Button \_1号中断  (.out(\_1号中断_out ));
  LED #(.active("true")) \_1号中断等待指示灯  (.in(or_1_out));
  or or_1 (or_1_out, \与中断屏蔽位与 , d_ff_1_q);
  D_Flip_Flop #(.trigger("rising"), .Pre_Clr_Positions("LEGACY"), .NegatePresetClear("false"), .enable("true"), .NewFFLayout("false")) d_ff_1 (
    .clk(\_1号中断_out ), .D(1'b1), .Q(d_ff_1_q), .reset(\与中断屏蔽位与 ));  // open: Qn, preset, en
  or or_2 (or_2_out, d_ff_1_q, \与中断屏蔽位与 );
  and and_1 (and_1_out, or_2_out, ~\同步清零信号 );  // AND_Gate
  D_Flip_Flop #(.trigger("rising"), .Pre_Clr_Positions("LEGACY"), .NegatePresetClear("false"), .enable("true"), .NewFFLayout("false")) IR1 (
    .clk(clock_1_out), .D(and_1_out), .Q(\与中断屏蔽位与 ));  // open: Qn, preset, en, reset

  // Notes on the sheet:
  //   中断信号采样参考电路
  //   Reset 
endmodule

module \单周期_多级中断  (
  input  IR1,
  input  IR2,
  input  IR3,
  output RegWrite,
  output MemWrite,
  output [31:0] PC,
  output [31:0] IR,
  output [31:0] RDin,
  output [31:0] MDin,
  output [31:0] LedData
);

  wire and_1_out, and_2_out, and_3_out, and_7_out, and_8_out, and_9_out, and_10_out, and_11_out, and_12_out,
       and_13_out, and_14_out, and_15_out, and_17_out, and_19_out, Beq, bgue, Bne, CLK, clock_1_out,
       comparator_1_eq, comparator_2_eq, comparator_3_eq, comparator_4_eq, comparator_5_eq, comparator_6_lt,
       comparator_7_eq, comparator_8_eq, comparator_9_eq, comparator_10_eq, comparator_12_eq,
       comparator_12_lt, comparator_13_eq, comparator_14_eq, csrr, csrrci, csrrsi, d_ff_1_q, d_ff_2_q,
       d_ff_3_q, d_ff_4_q, decoder_1_out1, decoder_1_out2, decoder_1_out3, decoder_2_out1, decoder_2_out2,
       decoder_2_out3, demultiplexer_1_out0, demultiplexer_1_out1, demultiplexer_1_out2,
       demultiplexer_1_out3, ecall, equal, gequal, Go, halt, ie, in, intr, intrrequest, IR1_2_q, IR1_3_q,
       IR1_q, IR1_t, IR2_t, IR3_t, IRA, IRB, IRC, is_lb, JAL, JALR, keep, less, MemToReg, nand_1_out,
       not_1_out, not_2_out, not_3_out, not_4_out, not_5_out, or_4_out, or_5_out, or_6_out, or_7_out,
       or_8_out, or_9_out, or_10_out, or_11_out, or_16_out, or_17_out, or_18_out, register_9_q, RST, S_type,
       uret, W1, W2, W3, \单周期硬布线控制器_1_alu_src ;
  wire [1:0] adder_1_out, count, cur_itrnum, irnum, multiplexer_2_out, priority_encoder_2_out,
       priority_encoder_3_out, Qnum, register_2_q, register_3_q, register_4_q;
  wire [3:0] \单周期硬布线控制器_1_alu_op ;
  wire [4:0] multiplexer_8_out, multiplexer_9_out;
  wire [11:0] multiplexer_10_out;
  wire [12:0] CNT_num;
  wire [15:0] counter_1_q, \总周期数 ;
  wire [31:0] Alu_out, Alu_out2, and_16_out, bit_extender_1_out, bit_extender_2_out, bit_extender_3_out,
       bit_extender_4_out, bout, intr_pc, jout, load, Mout, multiplexer_6_out, multiplexer_7_out,
       multiplexer_11_out, now_pc, PC_4, R1, register_6_q, register_7_q, register_8_q, return_pc,
       shifter_1_out, shifter_2_out;

  Button \u_继续运行  (.out(Go));
  Button _1 ();  // open: out
  Button _2 ();  // open: out
  Button _3 ();  // open: out
  LED #(.active("true")) led_1 (.in(W1));
  LED #(.active("true")) led_2 (.in(W2));
  LED #(.active("true")) led_3 (.in(W3));
  Hex_Digit_Display hex_digit_display_1 (.value(LedData[31:28]));  // open: dp
  Comparator #(.width(16), .mode("twosComplement")) comparator_1 (
    .a(\总周期数 ), .b(16'h7), .eq(comparator_1_eq));  // open: gt, lt
  Comparator #(.width(16), .mode("twosComplement")) comparator_2 (
    .a(\总周期数 ), .b(16'h241), .eq(comparator_2_eq));  // open: gt, lt
  Counter #(.width(16), .max('hffff), .ongoal("wrap"), .trigger("rising"), .behavior("old")) counter_1 (
    .Q(counter_1_q), .clk(CLK));  // open: load, D, count, carry, clr, preset
  or or_1 (W1, IR1_q, d_ff_1_q);
  or or_2 (W2, IR1_2_q, d_ff_2_q);
  or or_3 (W3, IR1_3_q, d_ff_3_q);
  Hex_Digit_Display hex_digit_display_2 (.value(LedData[23:20]));  // open: dp
  Hex_Digit_Display hex_digit_display_3 (.value(LedData[27:24]));  // open: dp
  Comparator #(.width(16), .mode("twosComplement")) comparator_3 (
    .a(16'h258), .b(\总周期数 ), .eq(comparator_3_eq));  // open: gt, lt
  or or_4 (or_4_out, comparator_3_eq, comparator_4_eq);
  Comparator #(.width(16), .mode("twosComplement")) comparator_4 (
    .a(\总周期数 ), .b(16'h1), .eq(comparator_4_eq));  // open: gt, lt
  Comparator #(.width(16), .mode("twosComplement")) comparator_5 (
    .a(\总周期数 ), .b(16'h4), .eq(comparator_5_eq));  // open: gt, lt
  or or_5 (or_5_out, comparator_1_eq, comparator_2_eq);
  or or_6 (or_6_out, csrrsi, csrrci);
  D_Flip_Flop #(.trigger("rising"), .Pre_Clr_Positions("LEGACY"), .NegatePresetClear("false"), .enable("true"), .NewFFLayout("false")) d_ff_1 (
    .clk(IRA), .D(1'b1), .Q(d_ff_1_q), .reset(IR1_q));  // open: Qn, preset, en
  D_Flip_Flop #(.trigger("rising"), .Pre_Clr_Positions("LEGACY"), .NegatePresetClear("false"), .enable("true"), .NewFFLayout("false")) d_ff_2 (
    .clk(IRB), .D(1'b1), .Q(d_ff_2_q), .reset(IR1_2_q));  // open: Qn, preset, en
  D_Flip_Flop #(.trigger("rising"), .Pre_Clr_Positions("LEGACY"), .NegatePresetClear("false"), .enable("true"), .NewFFLayout("false")) d_ff_3 (
    .clk(IRC), .D(1'b1), .Q(d_ff_3_q), .reset(IR1_3_q));  // open: Qn, preset, en
  Hex_Digit_Display hex_digit_display_4 (.value(LedData[15:12]));  // open: dp
  Hex_Digit_Display hex_digit_display_5 (.value(LedData[19:16]));  // open: dp
  Pull_Resistor #(.pull(0)) pull_resistor_1 (.node(IRA));
  assign IRA = or_4_out ? ~CLK : 1'bz;  // Controlled_Inverter controlled_inverter_1
  Pull_Resistor #(.pull(0)) pull_resistor_2 (.node(IRB));
  assign IRB = comparator_5_eq ? ~CLK : 1'bz;  // Controlled_Inverter controlled_inverter_2
  Pull_Resistor #(.pull(0)) pull_resistor_3 (.node(IRC));
  assign IRC = or_5_out ? ~CLK : 1'bz;  // Controlled_Inverter controlled_inverter_3
  not not_1 (not_1_out, or_7_out);
  or or_7 (or_7_out, intr, csrrci);
  or or_8 (or_8_out, or_6_out, comparator_6_lt, intr, uret);
  Comparator #(.width(16), .mode("unsigned")) comparator_6 (
    .a(counter_1_q), .b(16'h2), .lt(comparator_6_lt));  // open: gt, eq
  or or_9 (or_9_out, d_ff_1_q, IR1_q);
  or or_10 (or_10_out, d_ff_2_q, IR1_2_q);
  or or_11 (or_11_out, d_ff_3_q, IR1_3_q);
  Hex_Digit_Display hex_digit_display_6 (.value(LedData[7:4]));  // open: dp
  Hex_Digit_Display hex_digit_display_7 (.value(LedData[11:8]));  // open: dp
  // Probe on \总周期数 
  not not_2 (not_2_out, halt);
  Counter #(.width(16), .max('hffff), .ongoal("wrap"), .trigger("rising"), .behavior("old")) counter_2 (
    .Q(\总周期数 ), .clk(CLK));  // open: load, D, count, carry, clr, preset
  Register #(.width(1), .trigger("rising"), .Select("low")) register_1 (
    .D(not_1_out), .en(or_8_out), .Q(ie), .clk(CLK));  // open: clr
  and and_1 (and_1_out, or_9_out, ~demultiplexer_1_out1);  // AND_Gate
  and and_2 (and_2_out, or_10_out, ~demultiplexer_1_out2);  // AND_Gate
  and and_3 (and_3_out, or_11_out, ~demultiplexer_1_out3);  // AND_Gate
  Hex_Digit_Display hex_digit_display_8 (.value(LedData[3:0]));  // open: dp
  D_Flip_Flop #(.trigger("rising"), .Pre_Clr_Positions("LEGACY"), .NegatePresetClear("false"), .enable("true"), .NewFFLayout("false")) u_IR1 (
    .clk(CLK), .D(and_1_out), .Q(IR1_q));  // open: Qn, preset, en, reset
  D_Flip_Flop #(.trigger("rising"), .Pre_Clr_Positions("LEGACY"), .NegatePresetClear("false"), .enable("true"), .NewFFLayout("false")) IR1_2 (
    .clk(CLK), .D(and_2_out), .Q(IR1_2_q));  // open: Qn, preset, en, reset
  D_Flip_Flop #(.trigger("rising"), .Pre_Clr_Positions("LEGACY"), .NegatePresetClear("false"), .enable("true"), .NewFFLayout("false")) IR1_3 (
    .clk(CLK), .D(and_3_out), .Q(IR1_3_q));  // open: Qn, preset, en, reset
  and and_4 (intr, ie, intrrequest, in);
  or or_12 (IR1_t, IR1, IRA);
  Comparator #(.width(5), .mode("twosComplement")) comparator_7 (
    .a(5'b11100), .b(IR[6:2]), .eq(comparator_7_eq));  // open: gt, lt
  Comparator #(.width(5), .mode("twosComplement")) comparator_8 (
    .a(IR[6:2]), .b(5'b11100), .eq(comparator_8_eq));  // open: gt, lt
  Priority_Encoder #(.select(2), .disabled("Z")) priority_encoder_1 (
    .in0(1'b1), .in1(IR1_q), .in2(IR1_2_q), .in3(IR1_3_q), .out(irnum), .gs(intrrequest));  // open: en_out, en_in
  or or_13 (IR2_t, IR2, IRB);
  Comparator #(.width(3), .mode("twosComplement")) comparator_9 (
    .a(3'b110), .b(IR[14:12]), .eq(comparator_9_eq));  // open: gt, lt
  Comparator #(.width(3), .mode("twosComplement")) comparator_10 (
    .a(IR[14:12]), .b(3'b111), .eq(comparator_10_eq));  // open: gt, lt
  and and_5 (csrrsi, comparator_7_eq, comparator_9_eq);
  or or_14 (csrr, csrrsi, csrrci);
  and and_6 (csrrci, comparator_10_eq, comparator_8_eq);
  Multiplexer #(.select(2), .width(32), .disabled("Z"), .enable("false")) multiplexer_1 (
    .in0(now_pc), .in1(32'h30ac), .in2(32'h3158), .in3(32'h3204), .out(intr_pc), .sel(irnum));
  Decoder #(.select(2), .tristate("false"), .disabled("Z"), .enable("false")) decoder_1 (
    .out1(decoder_1_out1), .out2(decoder_1_out2), .out3(decoder_1_out3), .sel(Qnum));  // open: out0
  Demultiplexer #(.select(2), .width(1), .tristate("false"), .disabled("Z"), .enable("false")) demultiplexer_1 (
    .out0(demultiplexer_1_out0), .out1(demultiplexer_1_out1), .out2(demultiplexer_1_out2),
    .out3(demultiplexer_1_out3), .in(uret), .sel(irnum));
  or or_15 (IR3_t, IR3, IRC);
  Multiplexer #(.select(1), .width(2), .disabled("Z"), .enable("false")) multiplexer_2 (
    .in0(2'b11), .in1(2'b01), .out(multiplexer_2_out), .sel(intr));
  Decoder #(.select(2), .tristate("false"), .disabled("Z"), .enable("false")) decoder_2 (
    .out1(decoder_2_out1), .out2(decoder_2_out2), .out3(decoder_2_out3), .sel(irnum));  // open: out0
  and and_7 (and_7_out, decoder_1_out1, intr);
  and and_8 (and_8_out, decoder_1_out2, intr);
  and and_9 (and_9_out, decoder_1_out3, intr);
  Adder #(.width(2)) adder_1 (.a(count), .b(multiplexer_2_out), .out(adder_1_out));  // open: cin, cout
  // Probe on irnum
  and and_10 (and_10_out, decoder_2_out1, intr);
  and and_11 (and_11_out, decoder_2_out2, intr);
  and and_12 (and_12_out, decoder_2_out3, intr);
  Register #(.width(2), .trigger("rising"), .Select("low")) register_2 (
    .D(irnum), .en(and_7_out), .Q(register_2_q), .clk(CLK));  // open: clr
  Register #(.width(2), .trigger("rising"), .Select("low")) register_3 (
    .D(irnum), .en(and_8_out), .Q(register_3_q), .clk(CLK));  // open: clr
  Register #(.width(2), .trigger("rising"), .Select("low")) register_4 (
    .D(irnum), .en(and_9_out), .Q(register_4_q), .clk(CLK));  // open: clr
  or or_16 (or_16_out, intr, uret);
  // Probe on count
  // Probe on count
  Register #(.width(2), .trigger("rising"), .Select("low")) register_5 (
    .D(adder_1_out), .en(or_16_out), .Q(count), .clk(CLK));  // open: clr
  and and_13 (and_13_out, gequal, bgue);
  Multiplexer #(.select(2), .width(2), .disabled("Z"), .enable("false")) multiplexer_3 (
    .in0(2'b00), .in1(register_2_q), .in2(register_3_q), .in3(register_4_q), .out(cur_itrnum), .sel(count));
  Adder #(.width(2)) adder_2 (.a(count), .b(2'b01), .out(Qnum));  // open: cin, cout
  not not_3 (not_3_out, equal);
  and and_14 (and_14_out, Beq, equal);
  or or_17 (or_17_out, and_13_out, and_14_out, and_15_out);
  Priority_Encoder #(.select(2), .disabled("Z")) priority_encoder_2 (
    .in0(1'b1), .in1(or_17_out), .in2(JAL), .in3(JALR), .out(priority_encoder_2_out));  // open: gs, en_out, en_in
  Register #(.width(32), .trigger("rising"), .Select("low")) register_6 (
    .D(now_pc), .en(and_10_out), .Q(register_6_q), .clk(CLK));  // open: clr
  Register #(.width(32), .trigger("rising"), .Select("low")) register_7 (
    .D(now_pc), .en(and_11_out), .Q(register_7_q), .clk(CLK));  // open: clr
  Register #(.width(32), .trigger("rising"), .Select("low")) register_8 (
    .D(now_pc), .en(and_12_out), .Q(register_8_q), .clk(CLK));  // open: clr
  // Probe on cur_itrnum
  // Probe on irnum
  and and_15 (and_15_out, not_3_out, Bne);
  Comparator #(.width(2), .mode("unsigned")) comparator_11 (.a(cur_itrnum), .b(irnum), .lt(in));  // open: gt, eq
  assign and_16_out = Alu_out & 32'hfffffffe;  // AND_Gate and_16, 32 bits wide
  Multiplexer #(.select(2), .width(32), .disabled("Z"), .enable("false")) multiplexer_4 (
    .in1(register_6_q), .in2(register_7_q), .in3(register_8_q), .out(return_pc), .sel(cur_itrnum));  // open: in0
  Multiplexer #(.select(2), .width(32), .disabled("Z"), .enable("false")) multiplexer_5 (
    .in0(PC_4), .in1(bout), .in2(jout), .in3(and_16_out), .out(now_pc), .sel(priority_encoder_2_out));
  Multiplexer #(.select(1), .width(32), .disabled("Z"), .enable("false")) multiplexer_6 (
    .in0(now_pc), .in1(return_pc), .out(multiplexer_6_out), .sel(uret));
  D_Flip_Flop #(.trigger("high"), .Pre_Clr_Positions("LEGACY"), .NegatePresetClear("false"), .enable("true"), .NewFFLayout("false")) d_ff_4 (.Q(d_ff_4_q));  // open: clk, D, Qn, preset, en, reset
  // Probe on 13'haa
  Multiplexer #(.select(1), .width(32), .disabled("Z"), .enable("false")) multiplexer_7 (
    .in0(multiplexer_6_out), .in1(intr_pc), .out(multiplexer_7_out), .sel(intr));
  Comparator #(.width(13), .mode("twosComplement")) comparator_12 (
    .a(CNT_num), .b(13'haa), .eq(comparator_12_eq), .lt(comparator_12_lt));  // open: gt
  Clock #(.highDuration(1), .lowDuration(1)) clock_1 (.out(clock_1_out));
  Counter #(.width(13), .max('h1fff), .ongoal("stay"), .trigger("rising"), .behavior("old")) counter_3 (
    .count(comparator_12_lt), .Q(CNT_num), .clk(clock_1_out));  // open: load, D, carry, clr, preset
  Register #(.width(32), .trigger("rising"), .Select("low")) u_PC (
    .D(multiplexer_7_out), .en(not_4_out), .Q(PC), .clk(CLK), .clr(RST));
  not not_4 (not_4_out, halt);
  nand nand_1 (nand_1_out, d_ff_4_q, comparator_12_eq);
  assign CLK = nand_1_out ? clock_1_out : 1'bz;  // Controlled_Buffer controlled_buffer_1
  Pull_Resistor #(.pull(1)) pull_resistor_4 (.node(CLK));
  Adder #(.width(32)) adder_3 (.a(PC), .b(32'h4), .out(PC_4));  // open: cin, cout
  // RiscV_Probe riscv_probe_1: pin names not known; wires that end beside it: IR
  ROM #(.addrWidth(10), .dataWidth(32), .Select("high")) rom_1 (.addr(PC[11:2]), .data(IR));
  Comparator #(.width(32), .mode("twosComplement")) comparator_13 (
    .a(R1), .b(32'h22), .eq(comparator_13_eq));  // open: gt, lt
  and and_17 (and_17_out, ecall, comparator_13_eq);
  not not_5 (not_5_out, comparator_14_eq);
  Comparator #(.width(32), .mode("twosComplement")) comparator_14 (
    .a(R1), .b(32'h22), .eq(comparator_14_eq));  // open: gt, lt
  Register #(.width(1), .trigger("falling"), .Select("low")) register_9 (
    .D(1'b0), .Q(register_9_q), .clk(keep), .preset(Go));  // open: en, clr, cs
  \单周期硬布线控制器  \u_单周期硬布线控制器_1  (
    .Funct({IR[30], IR[25], IR[14:12]}), .OP(IR[6:2]), .ALU_OP(\单周期硬布线控制器_1_alu_op ), .MemToReg(MemToReg),
    .MemWrite(MemWrite), .ALU_SRC(\单周期硬布线控制器_1_alu_src ), .RegWrite(RegWrite), .ecall(ecall),
    .S_type(S_type), .Jalr(JALR), .Beq(Beq), .JAL(JAL), .Bne(Bne), .in_3(IR[21]), .uret(uret), .is_lb(is_lb),
    .bgue(bgue));  // open: rs1_used, rs2_used
  Multiplexer #(.select(1), .width(5), .disabled("Z"), .enable("false")) multiplexer_8 (
    .in0(IR[19:15]), .in1(5'b10001), .out(multiplexer_8_out), .sel(ecall));
  Multiplexer #(.select(1), .width(5), .disabled("Z"), .enable("false")) multiplexer_9 (
    .in0(IR[24:20]), .in1(5'b01010), .out(multiplexer_9_out), .sel(ecall));
  Multiplexer #(.select(1), .width(12), .disabled("Z"), .enable("false")) multiplexer_10 (
    .in0(IR[31:20]), .in1({IR[31:25], IR[11:7]}), .out(multiplexer_10_out), .sel(S_type));
  assign bit_extender_1_out = {{20{IR[31]}}, {IR[31], IR[7], IR[30:25], IR[11:8]}};  // Bit_Extender bit_extender_1
  assign bit_extender_2_out = {{12{IR[31]}}, {IR[31], IR[19:12], IR[20], IR[30:21]}};  // Bit_Extender bit_extender_2
  Register #(.width(32), .trigger("rising"), .Select("low")) register_10 (
    .D(MDin), .en(and_17_out), .Q(LedData), .clk(CLK));  // open: clr
  and and_18 (keep, ecall, not_5_out);
  and and_19 (and_19_out, ~register_9_q, keep);  // AND_Gate
  Register #(.width(1), .trigger("falling"), .Select("low")) register_11 (
    .D(and_19_out), .Q(halt), .clk(CLK));  // open: en, clr
  assign bit_extender_3_out = {{20{multiplexer_10_out[11]}}, multiplexer_10_out};  // Bit_Extender bit_extender_3
  Regifile regifile_1 (
    .Din(RDin), .Clk(CLK), .R1(R1), .R2(MDin), .WE(RegWrite), .W_num(IR[11:7]), .R1_num(multiplexer_8_out),
    .R2_num(multiplexer_9_out));
  Shifter #(.width(32), .shift("ll")) shifter_1 (.in(bit_extender_1_out), .\dist (5'b00001), .out(shifter_1_out));
  Shifter #(.width(32), .shift("ll")) shifter_2 (.in(bit_extender_2_out), .\dist (5'b00001), .out(shifter_2_out));
  Multiplexer #(.select(1), .width(32), .disabled("Z"), .enable("false")) multiplexer_11 (
    .in0(MDin), .in1(bit_extender_3_out), .out(multiplexer_11_out), .sel(\单周期硬布线控制器_1_alu_src ));
  Adder #(.width(32)) adder_4 (.a(shifter_1_out), .b(PC), .out(bout));  // open: cin, cout
  Adder #(.width(32)) adder_5 (.a(shifter_2_out), .b(PC), .out(jout));  // open: cin, cout
  ALU alu_1 (
    .X(R1), .Y(multiplexer_11_out), .AluOP(\单周期硬布线控制器_1_alu_op ), .Equal(equal), .Result(Alu_out),
    .Result_2(Alu_out2), .out_4(gequal), .out_6(less));
  or or_18 (or_18_out, JAL, JALR);
  Priority_Encoder #(.select(2), .disabled("Z")) priority_encoder_3 (
    .in0(1'b1), .in1(or_18_out), .in2(MemToReg), .in3(1'b0), .out(priority_encoder_3_out));  // open: gs, en_out, en_in
  assign bit_extender_4_out = {{24{Mout[7]}}, Mout[7:0]};  // Bit_Extender bit_extender_4
  Multiplexer #(.select(1), .width(32), .disabled("Z"), .enable("false")) multiplexer_12 (
    .in0(Mout), .in1(bit_extender_4_out), .out(load), .sel(is_lb));
  RAM #(.addrWidth(10), .dataWidth(32), .bus("separate"), .Select("high")) ram_1 (
    .addr(Alu_out[11:2]), .din(MDin), .data(Mout), .str(MemWrite), .sel(1'b1), .clk(CLK), .ld(MemToReg),
    .clr(1'b0));
  Multiplexer #(.select(2), .width(32), .disabled("Z"), .enable("false")) multiplexer_13 (
    .in0(Alu_out), .in1(PC_4), .in2(load), .out(RDin), .sel(priority_encoder_3_out));  // open: in3
  // also tied to GND on the sheet: demultiplexer_1_out0

  // Other names for the same wires on the sheet: fun3[2:0] = IR[14:12]; opcode[4:0] = IR[6:2]; R2[31:0] = MDin

  // Notes on the sheet:
  //   中断源
  //   中断等待指示
  //   总复位信号应将除ROM以外所有存储组件全部清零
  //   多级中断测试信号模拟器
  //   设置关中断
  //   数码管输出
  //   数码管输出应该用寄存器锁存，否则显示数据只能一闪而过
  //   Reset 
  //   Reset 
  //   Reset 
  //   in表示我们堆栈里面还有没有处理完的堆栈
  //   如何保存多级中断的断点呢？epc，
  //   为方便自动评测，需要输出PC，IR，寄存器堆写如数据RDin
  //   RAM写使能MemWrite、RAM写入数据MDin等信号
  //   因为我们最多只有三个中断，我们只要分别保存对应的epc即可
  //   当前存储中断的的存储器编号
  //   这个表示下一位有空的存储器编号
  //   暂停节拍，不能为0
  //   处理完中断返回的地址
  //   控制位
  //   戳工具置1进入计数暂停模式，ctrl+k时钟自动运行到对应节拍暂停
  //   ctrl+k关闭时钟连续运行，将控制位置零，进入单步调试模式调试
  //   可计数暂停的时钟源
  //   指令探针
  //   指令存储器
  //   指令字
  //   contents of rom_1 (hex, n*v repeats v):
  //   7d000113 100413 1f41993 41f9d993 433 c00913 800b13 140413 f47413 800293 100313 499993 89e9b3 1300533
  //   2200893 73 406282b3 fe0294e3 140413 f00f93 1f47433 1c41413 800293 100313 49d993 89e9b3 1300533
  //   2200893 73 406282b3 fe0294e3 1c45413 406b0b33 b0463 f95ff06f 2b3 fff2c293 1029293 fff2e293 500533
  //   2200893 73 f5dff06f 1112023 410113 a12023 410113 812023 410113 1312023 410113 1412023 410113 1512023
  //   410113 1612023 410113 40e073 100b13 300a13 100a93 1600433 441413 14469b3 1300533 2200893 73 fe0416e3
  //   415a0a33 fe0a10e3 40f073 ffc10113 12b03 ffc10113 12a83 ffc10113 12a03 ffc10113 12983 ffc10113 12403
  //   ffc10113 12503 ffc10113 12883 200073 1112023 410113 a12023 410113 812023 410113 1312023 410113
  //   1412023 410113 1512023 410113 1612023 410113 40e073 200b13 300a13 100a93 1600433 441413 14469b3
  //   1300533 2200893 73 fe0416e3 415a0a33 fe0a10e3 40f073 ffc10113 12b03 ffc10113 12a83 ffc10113 12a03
  //   ffc10113 12983 ffc10113 12403 ffc10113 12503 ffc10113 12883 200073 1112023 410113 a12023 410113
  //   812023 410113 1312023 410113 1412023 410113 1512023 410113 1612023 410113 40e073 300b13 300a13
  //   100a93 1600433 441413 14469b3 1300533 2200893 73 fe0416e3 415a0a33 fe0a10e3 40f073 ffc10113 12b03
  //   ffc10113 12a83 ffc10113 12a03 ffc10113 12983 ffc10113 12403 ffc10113 12503 ffc10113 12883 200073
  //   keep信号为1表示暂停
  //   由于会出现毛刺问题，我们需要用寄存器以及
  //   JAL
  //   JALR
  //   URET
  //   b型
  //   j型
  //   Led显示，注意我们需要锁存，且我们在a7！=34的时候要暂停
  //   Beq
  //   Bne
  //   MemToReg
  //   MemWrite
  //   AluOP
  //   AluSrcB
  //   RegWrite
  //   0是正常1是暂停（因为我们后面有一个非门）
  //   jal和jalr传给pc的值不一样
  //   处理sw，写入Mdatain
  //   区分lb和lw，写入寄存器
  //   数据存储器
  //   rdin分三种情况，正常r型指令要aluout，j型要pc4，最后是lw和lb
endmodule

module \单周期_单级中断  (
  input  IR1,
  input  IR2,
  input  IR3,
  output RegWrite,
  output MemWrite,
  output [31:0] PC,
  output [31:0] IR,
  output [31:0] RDin,
  output [31:0] MDin,
  output [31:0] LedData
);

  wire and_1_out, and_2_out, and_3_out, and_5_out, and_6_out, and_7_out, and_9_out, and_11_out, Beq, bgue,
       Bne, CLK, clock_1_out, clock_2_out, clock_3_out, clock_4_out, comparator_1_eq, comparator_2_eq,
       comparator_3_eq, comparator_4_eq, comparator_5_eq, comparator_6_eq, comparator_7_eq, comparator_7_lt,
       d_ff_1_q, d_ff_2_q, d_ff_3_q, d_ff_4_q, demultiplexer_1_out0, demultiplexer_1_out1,
       demultiplexer_1_out2, ecall, equal, gequal, Go, halt, intr, IR1_2_q, IR1_3_q, IR1_q, IR1_t, IR2_t,
       IR3_t, IRA, IRB, IRC, is_lb, JAL, JALR, keep, less, MemToReg, nand_1_out, not_1_out, not_2_out,
       not_3_out, not_4_out, or_4_out, or_5_out, or_6_out, or_7_out, or_8_out, or_9_out, or_12_out,
       or_14_out, register_4_q, RST, S_type, uret, W1, W2, W3, \关中断 , \单周期硬布线控制器_1_alu_src ;
  wire [1:0] priority_encoder_1_out, priority_encoder_2_out, priority_encoder_3_out, priority_encoder_4_out,
       register_2_q;
  wire [3:0] \单周期硬布线控制器_1_alu_op ;
  wire [4:0] multiplexer_4_out, multiplexer_5_out;
  wire [11:0] multiplexer_6_out;
  wire [12:0] CNT_num;
  wire [15:0] \总周期数 ;
  wire [31:0] Alu_out, Alu_out2, and_8_out, bit_extender_1_out, bit_extender_2_out, bit_extender_3_out,
       bit_extender_4_out, bout, jout, load, Mout, multiplexer_1_out, multiplexer_2_out, multiplexer_3_out,
       multiplexer_7_out, PC_4, R1, register_3_q, shifter_1_out, shifter_2_out;

  Button \u_继续运行  (.out(Go));
  Button _1 ();  // open: out
  Button _2 ();  // open: out
  Button _3 ();  // open: out
  Clock #(.highDuration(1), .lowDuration(1)) clock_1 (.out(clock_1_out));
  Clock #(.highDuration(1), .lowDuration(1)) clock_2 (.out(clock_2_out));
  Clock #(.highDuration(1), .lowDuration(1)) clock_3 (.out(clock_3_out));
  LED #(.active("true")) led_1 (.in(W1));
  LED #(.active("true")) led_2 (.in(W2));
  LED #(.active("true")) led_3 (.in(W3));
  or or_1 (W1, IR1_q, d_ff_1_q);
  or or_2 (W2, IR1_2_q, d_ff_2_q);
  or or_3 (W3, IR1_3_q, d_ff_3_q);
  Hex_Digit_Display hex_digit_display_1 (.value(LedData[31:28]));  // open: dp
  Comparator #(.width(16), .mode("twosComplement")) comparator_1 (
    .a(16'h23b), .b(\总周期数 ), .eq(comparator_1_eq));  // open: gt, lt
  Comparator #(.width(16), .mode("twosComplement")) comparator_2 (
    .a(\总周期数 ), .b(16'h1), .eq(comparator_2_eq));  // open: gt, lt
  Comparator #(.width(16), .mode("twosComplement")) comparator_3 (
    .a(\总周期数 ), .b(16'h4), .eq(comparator_3_eq));  // open: gt, lt
  Comparator #(.width(16), .mode("twosComplement")) comparator_4 (
    .a(\总周期数 ), .b(16'h7), .eq(comparator_4_eq));  // open: gt, lt
  D_Flip_Flop #(.trigger("rising"), .Pre_Clr_Positions("LEGACY"), .NegatePresetClear("false"), .enable("true"), .NewFFLayout("false")) d_ff_1 (
    .clk(IRA), .D(1'b1), .Q(d_ff_1_q), .reset(IR1_q));  // open: Qn, preset, en
  D_Flip_Flop #(.trigger("rising"), .Pre_Clr_Positions("LEGACY"), .NegatePresetClear("false"), .enable("true"), .NewFFLayout("false")) d_ff_2 (
    .clk(IRB), .D(1'b1), .Q(d_ff_2_q), .reset(IR1_2_q));  // open: Qn, preset, en
  D_Flip_Flop #(.trigger("rising"), .Pre_Clr_Positions("LEGACY"), .NegatePresetClear("false"), .enable("true"), .NewFFLayout("false")) d_ff_3 (
    .clk(IRC), .D(1'b1), .Q(d_ff_3_q), .reset(IR1_3_q));  // open: Qn, preset, en
  Hex_Digit_Display hex_digit_display_2 (.value(LedData[23:20]));  // open: dp
  Hex_Digit_Display hex_digit_display_3 (.value(LedData[27:24]));  // open: dp
  or or_4 (or_4_out, comparator_1_eq, comparator_2_eq);
  assign IRA = or_4_out ? ~CLK : 1'bz;  // Controlled_Inverter controlled_inverter_1
  assign IRB = comparator_3_eq ? ~CLK : 1'bz;  // Controlled_Inverter controlled_inverter_2
  assign IRC = comparator_4_eq ? ~CLK : 1'bz;  // Controlled_Inverter controlled_inverter_3
  or or_5 (or_5_out, d_ff_1_q, IR1_q);
  or or_6 (or_6_out, d_ff_2_q, IR1_2_q);
  or or_7 (or_7_out, d_ff_3_q, IR1_3_q);
  Hex_Digit_Display hex_digit_display_4 (.value(LedData[15:12]));  // open: dp
  Hex_Digit_Display hex_digit_display_5 (.value(LedData[19:16]));  // open: dp
  Pull_Resistor #(.pull(0)) pull_resistor_1 (.node(IRA));
  Pull_Resistor #(.pull(0)) pull_resistor_2 (.node(IRB));
  Pull_Resistor #(.pull(0)) pull_resistor_3 (.node(IRC));
  and and_1 (and_1_out, or_5_out, ~demultiplexer_1_out0);  // AND_Gate
  and and_2 (and_2_out, or_6_out, ~demultiplexer_1_out1);  // AND_Gate
  and and_3 (and_3_out, or_7_out, ~demultiplexer_1_out2);  // AND_Gate
  Hex_Digit_Display hex_digit_display_6 (.value(LedData[7:4]));  // open: dp
  Hex_Digit_Display hex_digit_display_7 (.value(LedData[11:8]));  // open: dp
  // Probe on \总周期数 
  not not_1 (not_1_out, halt);
  D_Flip_Flop #(.trigger("rising"), .Pre_Clr_Positions("LEGACY"), .NegatePresetClear("false"), .enable("true"), .NewFFLayout("false")) u_IR1 (
    .clk(clock_1_out), .D(and_1_out), .Q(IR1_q));  // open: Qn, preset, en, reset
  D_Flip_Flop #(.trigger("rising"), .Pre_Clr_Positions("LEGACY"), .NegatePresetClear("false"), .enable("true"), .NewFFLayout("false")) IR1_2 (
    .clk(clock_2_out), .D(and_2_out), .Q(IR1_2_q));  // open: Qn, preset, en, reset
  D_Flip_Flop #(.trigger("rising"), .Pre_Clr_Positions("LEGACY"), .NegatePresetClear("false"), .enable("true"), .NewFFLayout("false")) IR1_3 (
    .clk(clock_3_out), .D(and_3_out), .Q(IR1_3_q));  // open: Qn, preset, en, reset
  Hex_Digit_Display hex_digit_display_8 (.value(LedData[3:0]));  // open: dp
  Counter #(.width(16), .max('hffff), .ongoal("wrap"), .trigger("rising"), .behavior("old")) counter_1 (
    .Q(\总周期数 ), .clk(CLK));  // open: load, D, count, carry, clr, preset
  or or_8 (or_8_out, uret, ~or_9_out);  // OR_Gate
  or or_9 (or_9_out, IR1_q, IR1_2_q, IR1_3_q);
  Register #(.width(1), .trigger("rising"), .Select("low")) register_1 (
    .D(or_8_out), .Q(\关中断 ), .clk(CLK));  // open: en, clr
  Priority_Encoder #(.select(2), .disabled("Z")) priority_encoder_1 (
    .in0(IR1_q), .in1(IR1_2_q), .in2(IR1_3_q), .in3(1'b0), .out(priority_encoder_1_out));  // open: gs, en_out, en_in
  Multiplexer #(.select(2), .width(32), .disabled("Z"), .enable("false")) multiplexer_1 (
    .in0(32'h30ac), .in1(32'h3150), .in2(32'h31f4), .out(multiplexer_1_out), .sel(priority_encoder_1_out));  // open: in3
  or or_10 (IR1_t, IR1, IRA);
  and and_4 (intr, \关中断 , or_9_out);
  Register #(.width(2), .trigger("rising"), .Select("low")) register_2 (
    .D(priority_encoder_1_out), .en(intr), .Q(register_2_q), .clk(CLK));  // open: clr
  or or_11 (IR2_t, IR2, IRB);
  and and_5 (and_5_out, gequal, bgue);
  Demultiplexer #(.select(2), .width(1), .tristate("false"), .disabled("Z"), .enable("false")) demultiplexer_1 (
    .out0(demultiplexer_1_out0), .out1(demultiplexer_1_out1), .out2(demultiplexer_1_out2), .in(uret),
    .sel(register_2_q));  // open: out3
  not not_2 (not_2_out, equal);
  and and_6 (and_6_out, not_2_out, Bne);
  and and_7 (and_7_out, Beq, equal);
  or or_12 (or_12_out, and_5_out, and_7_out, and_6_out);
  Priority_Encoder #(.select(2), .disabled("Z")) priority_encoder_2 (
    .in0(1'b1), .in1(or_12_out), .in2(JAL), .in3(JALR), .out(priority_encoder_2_out));  // open: gs, en_out, en_in
  assign and_8_out = Alu_out & 32'hfffffffe;  // AND_Gate and_8, 32 bits wide
  Multiplexer #(.select(2), .width(32), .disabled("Z"), .enable("false")) multiplexer_2 (
    .in0(multiplexer_3_out), .in1(multiplexer_1_out), .in2(register_3_q), .out(multiplexer_2_out),
    .sel(priority_encoder_3_out));  // open: in3
  or or_13 (IR3_t, IR3, IRC);
  Multiplexer #(.select(2), .width(32), .disabled("Z"), .enable("false")) multiplexer_3 (
    .in0(PC_4), .in1(bout), .in2(jout), .in3(and_8_out), .out(multiplexer_3_out), .sel(priority_encoder_2_out));
  Register #(.width(32), .trigger("rising"), .Select("low")) register_3 (
    .D(multiplexer_3_out), .en(intr), .Q(register_3_q), .clk(CLK));  // open: clr
  Priority_Encoder #(.select(2), .disabled("Z")) priority_encoder_3 (
    .in0(1'b1), .in1(intr), .in2(uret), .out(priority_encoder_3_out));  // open: in3, gs, en_out, en_in
  not not_3 (not_3_out, halt);
  Register #(.width(32), .trigger("rising"), .Select("low")) u_PC (
    .D(multiplexer_2_out), .en(not_3_out), .Q(PC), .clk(CLK), .clr(RST));
  Adder #(.width(32)) adder_1 (.a(PC), .b(32'h4), .out(PC_4));  // open: cin, cout
  // RiscV_Probe riscv_probe_1: pin names not known; wires that end beside it: IR
  ROM #(.addrWidth(10), .dataWidth(32), .Select("high")) rom_1 (.addr(PC[11:2]), .data(IR));
  D_Flip_Flop #(.trigger("high"), .Pre_Clr_Positions("LEGACY"), .NegatePresetClear("false"), .enable("true"), .NewFFLayout("false")) d_ff_4 (.Q(d_ff_4_q));  // open: clk, D, Qn, preset, en, reset
  // Probe on 13'hc
  Comparator #(.width(32), .mode("twosComplement")) comparator_5 (
    .a(R1), .b(32'h22), .eq(comparator_5_eq));  // open: gt, lt
  Comparator #(.width(32), .mode("twosComplement")) comparator_6 (
    .a(R1), .b(32'h22), .eq(comparator_6_eq));  // open: gt, lt
  Register #(.width(1), .trigger("falling"), .Select("low")) register_4 (
    .D(1'b0), .Q(register_4_q), .clk(keep), .preset(Go));  // open: en, clr, cs
  Comparator #(.width(13), .mode("twosComplement")) comparator_7 (
    .a(CNT_num), .b(13'hc), .eq(comparator_7_eq), .lt(comparator_7_lt));  // open: gt
  Clock #(.highDuration(1), .lowDuration(1)) clock_4 (.out(clock_4_out));
  \单周期硬布线控制器  \u_单周期硬布线控制器_1  (
    .Funct({IR[30], IR[25], IR[14:12]}), .OP(IR[6:2]), .ALU_OP(\单周期硬布线控制器_1_alu_op ), .MemToReg(MemToReg),
    .MemWrite(MemWrite), .ALU_SRC(\单周期硬布线控制器_1_alu_src ), .RegWrite(RegWrite), .ecall(ecall),
    .S_type(S_type), .Jalr(JALR), .Beq(Beq), .JAL(JAL), .Bne(Bne), .in_3(IR[21]), .uret(uret), .is_lb(is_lb),
    .bgue(bgue));  // open: rs1_used, rs2_used
  Multiplexer #(.select(1), .width(5), .disabled("Z"), .enable("false")) multiplexer_4 (
    .in0(IR[19:15]), .in1(5'b10001), .out(multiplexer_4_out), .sel(ecall));
  Multiplexer #(.select(1), .width(5), .disabled("Z"), .enable("false")) multiplexer_5 (
    .in0(IR[24:20]), .in1(5'b01010), .out(multiplexer_5_out), .sel(ecall));
  Multiplexer #(.select(1), .width(12), .disabled("Z"), .enable("false")) multiplexer_6 (
    .in0(IR[31:20]), .in1({IR[31:25], IR[11:7]}), .out(multiplexer_6_out), .sel(S_type));
  and and_9 (and_9_out, ecall, comparator_5_eq);
  and and_10 (keep, ecall, not_4_out);
  not not_4 (not_4_out, comparator_6_eq);
  and and_11 (and_11_out, ~register_4_q, keep);  // AND_Gate
  Counter #(.width(13), .max('h1fff), .ongoal("stay"), .trigger("rising"), .behavior("old")) counter_2 (
    .count(comparator_7_lt), .Q(CNT_num), .clk(clock_4_out));  // open: load, D, carry, clr, preset
  assign bit_extender_1_out = {{20{IR[31]}}, {IR[31], IR[7], IR[30:25], IR[11:8]}};  // Bit_Extender bit_extender_1
  assign bit_extender_2_out = {{12{IR[31]}}, {IR[31], IR[19:12], IR[20], IR[30:21]}};  // Bit_Extender bit_extender_2
  Register #(.width(32), .trigger("rising"), .Select("low")) register_5 (
    .D(MDin), .en(and_9_out), .Q(LedData), .clk(CLK));  // open: clr
  Register #(.width(1), .trigger("falling"), .Select("low")) register_6 (
    .D(and_11_out), .Q(halt), .clk(CLK));  // open: en, clr
  nand nand_1 (nand_1_out, d_ff_4_q, comparator_7_eq);
  assign bit_extender_3_out = {{20{multiplexer_6_out[11]}}, multiplexer_6_out};  // Bit_Extender bit_extender_3
  Shifter #(.width(32), .shift("ll")) shifter_1 (.in(bit_extender_1_out), .\dist (5'b00001), .out(shifter_1_out));
  Shifter #(.width(32), .shift("ll")) shifter_2 (.in(bit_extender_2_out), .\dist (5'b00001), .out(shifter_2_out));
  assign CLK = nand_1_out ? clock_4_out : 1'bz;  // Controlled_Buffer controlled_buffer_1
  Pull_Resistor #(.pull(1)) pull_resistor_4 (.node(CLK));
  Regifile regifile_1 (
    .Din(RDin), .Clk(CLK), .R1(R1), .R2(MDin), .WE(RegWrite), .W_num(IR[11:7]), .R1_num(multiplexer_4_out),
    .R2_num(multiplexer_5_out));
  Adder #(.width(32)) adder_2 (.a(shifter_1_out), .b(PC), .out(bout));  // open: cin, cout
  Adder #(.width(32)) adder_3 (.a(shifter_2_out), .b(PC), .out(jout));  // open: cin, cout
  Multiplexer #(.select(1), .width(32), .disabled("Z"), .enable("false")) multiplexer_7 (
    .in0(MDin), .in1(bit_extender_3_out), .out(multiplexer_7_out), .sel(\单周期硬布线控制器_1_alu_src ));
  ALU alu_1 (
    .X(R1), .Y(multiplexer_7_out), .AluOP(\单周期硬布线控制器_1_alu_op ), .Equal(equal), .Result(Alu_out),
    .Result_2(Alu_out2), .out_4(gequal), .out_6(less));
  or or_14 (or_14_out, JAL, JALR);
  Priority_Encoder #(.select(2), .disabled("Z")) priority_encoder_4 (
    .in0(1'b1), .in1(or_14_out), .in2(MemToReg), .in3(1'b0), .out(priority_encoder_4_out));  // open: gs, en_out, en_in
  assign bit_extender_4_out = {{24{Mout[7]}}, Mout[7:0]};  // Bit_Extender bit_extender_4
  RAM #(.addrWidth(10), .dataWidth(32), .bus("separate"), .Select("high")) ram_1 (
    .addr(Alu_out[11:2]), .din(MDin), .data(Mout), .str(MemWrite), .sel(1'b1), .clk(CLK), .ld(MemToReg),
    .clr(1'b0));
  Multiplexer #(.select(1), .width(32), .disabled("Z"), .enable("false")) multiplexer_8 (
    .in0(Mout), .in1(bit_extender_4_out), .out(load), .sel(is_lb));
  Multiplexer #(.select(2), .width(32), .disabled("Z"), .enable("false")) multiplexer_9 (
    .in0(Alu_out), .in1(PC_4), .in2(load), .out(RDin), .sel(priority_encoder_4_out));  // open: in3

  // Other names for the same wires on the sheet: R2[31:0] = MDin

  // Notes on the sheet:
  //   中断源
  //   中断等待指示
  //   总复位信号应将除ROM以外所有存储组件全部清零
  //   单级中断测试信号模拟器
  //   数码管输出
  //   Reset 
  //   Reset 
  //   Reset 
  //   数码管输出应该用寄存器锁存，否则显示数据只能一闪而过
  //   1为开
  //   为方便自动评测，需要输出PC，IR，寄存器堆写如数据RDin
  //   RAM写使能MemWrite、RAM写入数据MDin等信号
  //   指令探针
  //   指令存储器
  //   指令字
  //   contents of rom_1 (hex, n*v repeats v):
  //   7d000113 100413 1f41993 41f9d993 433 c00913 800b13 140413 f47413 800293 100313 499993 89e9b3 1300533
  //   2200893 73 406282b3 fe0294e3 140413 f00f93 1f47433 1c41413 800293 100313 49d993 89e9b3 1300533
  //   2200893 73 406282b3 fe0294e3 1c45413 406b0b33 b0463 f95ff06f 2b3 fff2c293 1029293 fff2e293 500533
  //   2200893 73 f5dff06f 1112023 410113 a12023 410113 812023 410113 1312023 410113 1412023 410113 1512023
  //   410113 1612023 410113 100b13 300a13 100a93 1600433 441413 14469b3 1300533 2200893 73 fe0416e3
  //   415a0a33 fe0a10e3 ffc10113 12b03 ffc10113 12a83 ffc10113 12a03 ffc10113 12983 ffc10113 12403
  //   ffc10113 12503 ffc10113 12883 200073 1112023 410113 a12023 410113 812023 410113 1312023 410113
  //   1412023 410113 1512023 410113 1612023 410113 200b13 300a13 100a93 1600433 441413 14469b3 1300533
  //   2200893 73 fe0416e3 415a0a33 fe0a10e3 ffc10113 12b03 ffc10113 12a83 ffc10113 12a03 ffc10113 12983
  //   ffc10113 12403 ffc10113 12503 ffc10113 12883 200073 1112023 410113 a12023 410113 812023 410113
  //   1312023 410113 1412023 410113 1512023 410113 1612023 410113 300b13 300a13 100a93 1600433 441413
  //   14469b3 1300533 2200893 73 fe0416e3 415a0a33 fe0a10e3 ffc10113 12b03 ffc10113 12a83 ffc10113 12a03
  //   ffc10113 12983 ffc10113 12403 ffc10113 12503 ffc10113 12883 200073
  //   keep信号为1表示暂停
  //   控制位
  //   暂停节拍，不能为0
  //   JAL
  //   JALR
  //   URET
  //   b型
  //   j型
  //   Led显示，注意我们需要锁存，且我们在a7！=34的时候要暂停
  //   由于会出现毛刺问题，我们需要用寄存器以及
  //   戳工具置1进入计数暂停模式，ctrl+k时钟自动运行到对应节拍暂停
  //   ctrl+k关闭时钟连续运行，将控制位置零，进入单步调试模式调试
  //   Beq
  //   Bne
  //   AluOP
  //   AluSrcB
  //   RegWrite
  //   MemToReg
  //   MemWrite
  //   0是正常1是暂停（因为我们后面有一个非门）
  //   可计数暂停的时钟源
  //   jal和jalr传给pc的值不一样
  //   处理sw，写入Mdatain
  //   区分lb和lw，写入寄存器
  //   数据存储器
  //   rdin分三种情况，正常r型指令要aluout，j型要pc4，最后是lw和lb
endmodule

module \封装正确性测试  (
);

  wire IR1, IR2, IR3, MemW, RegW;
  wire [31:0] EX_PC, ID_PC, IF_PC, IR, LED, MDin, MDinr, MEM_PC, PC, RDin, RDinr, WB_PC;

  \单周期RISC_V  \u_单周期risc_v_1  (
    .IR1(IR1), .IR2(IR2), .IR3(IR3), .RegWrite(RegW), .MemWrite(MemW), .PC(PC), .IR(IR), .RDin(RDin),
    .MDin(MDin), .LedData(LED));
  \气泡流水线  \u_气泡流水线_1  (
    .RegWrite(RegW), .MemWrite(MemW), .IF_PC(IF_PC), .ID_PC(ID_PC), .EX_PC(EX_PC), .M_PC(MEM_PC),
    .WB_PC(WB_PC), .RDin(RDinr), .MDin(MDinr), .LedData(LED));
  \单周期_单级中断  \u_单周期_单级中断_1  (
    .IR1(IR1), .IR2(IR2), .IR3(IR3), .RegWrite(RegW), .MemWrite(MemW), .PC(PC), .IR(IR), .RDin(RDin),
    .MDin(MDin), .LedData(LED));
  \理想流水线  \u_理想流水线_1  (
    .RegWrite(RegW), .MemWrite(MemW), .IF_PC(IF_PC), .ID_PC(ID_PC), .EX_PC(EX_PC), .M_PC(MEM_PC),
    .WB_PC(WB_PC), .RDin(RDinr), .MDin(MDinr), .LedData(LED));
  \重定向流水线  \u_重定向流水线_1  (
    .RegWrite(RegW), .MemWrite(MemW), .IF_PC(IF_PC), .ID_PC(ID_PC), .EX_PC(EX_PC), .M_PC(MEM_PC),
    .WB_PC(WB_PC), .RDin(RDinr), .MDin(MDinr), .LedData(LED));
  \单周期_多级中断  \u_单周期_多级中断_1  (
    .IR1(IR1), .IR2(IR2), .IR3(IR3), .RegWrite(RegW), .MemWrite(MemW), .PC(PC), .IR(IR), .RDin(RDin),
    .MDin(MDin), .LedData(LED));

  // Notes on the sheet:
  //   单周期封装测试
  //   气泡流水封装测试
  //   单周期+单级中断封装测试
  //   请检查上面封装有无位宽不匹配，引脚标签是否和连接的标签相对应，否则无法在educoder平台上正确测试
  //   理想流水封装测试
  //   重定向流水封装测试
  //   单周期+多级中断封装测试
endmodule

module \流水器器件  (
  input  JAL,
  input  JALR,
  input  is_lb,
  input  begue,
  input  Beq,
  input  Bne,
  input  MemToReg,
  input  MemWrite,
  input  AluSrcB,
  input  RegWrite,
  input  S_type,
  input  ecall,
  input  halt,
  input  [3:0] AluOp,
  input  [4:0] rd,
  input  [31:0] R1,
  input  [31:0] R2,
  input  [31:0] PC,
  input  [31:0] PC_4,
  input  [31:0] imm_si,
  input  [31:0] imm_b,
  input  [31:0] imm_j,
  input  predict,
  input  [31:0] IR,
  input  valid,
  input  reset,
  input  refresh,
  input  Halt_2,
  input  clk,
  output JAL_2,
  output JALR_2,
  output is_lb_2,
  output begue_2,
  output Beq_2,
  output Bne_2,
  output MemToReg_2,
  output MemWrite_2,
  output AluSrcB_2,
  output RegWrite_2,
  output S_type_2,
  output ecall_2,
  output halt_3,
  output [3:0] Aluop_2,
  output [4:0] rd_2,
  output [31:0] R1_2,
  output [31:0] R2_2,
  output [31:0] PC_2,
  output [31:0] PC_4_2,
  output [31:0] imm_si_2,
  output [31:0] imm_b_2,
  output [31:0] imm_j_2,
  output predict_2,
  output [31:0] IR_2,
  output valid_2
);

  wire multiplexer_1_out, multiplexer_2_out, multiplexer_3_out, multiplexer_4_out, multiplexer_5_out,
       multiplexer_6_out, multiplexer_7_out, multiplexer_8_out, multiplexer_9_out, multiplexer_10_out,
       multiplexer_11_out, multiplexer_12_out, multiplexer_13_out, multiplexer_23_out, multiplexer_25_out,
       not_1_out, or_1_out;
  wire [3:0] multiplexer_14_out;
  wire [4:0] multiplexer_15_out;
  wire [31:0] multiplexer_16_out, multiplexer_17_out, multiplexer_18_out, multiplexer_19_out,
       multiplexer_20_out, multiplexer_21_out, multiplexer_22_out, multiplexer_24_out;

  Multiplexer #(.select(1), .width(1), .disabled("Z"), .enable("false")) multiplexer_1 (
    .in0(JAL), .in1(1'b0), .out(multiplexer_1_out), .sel(or_1_out));
  Multiplexer #(.select(1), .width(1), .disabled("Z"), .enable("false")) multiplexer_2 (
    .in0(JALR), .in1(1'b0), .out(multiplexer_2_out), .sel(or_1_out));
  Multiplexer #(.select(1), .width(1), .disabled("Z"), .enable("false")) multiplexer_3 (
    .in0(is_lb), .in1(1'b0), .out(multiplexer_3_out), .sel(or_1_out));
  Multiplexer #(.select(1), .width(1), .disabled("Z"), .enable("false")) multiplexer_4 (
    .in0(begue), .in1(1'b0), .out(multiplexer_4_out), .sel(or_1_out));
  Multiplexer #(.select(1), .width(1), .disabled("Z"), .enable("false")) multiplexer_5 (
    .in0(Beq), .in1(1'b0), .out(multiplexer_5_out), .sel(or_1_out));
  Multiplexer #(.select(1), .width(1), .disabled("Z"), .enable("false")) multiplexer_6 (
    .in0(Bne), .in1(1'b0), .out(multiplexer_6_out), .sel(or_1_out));
  Multiplexer #(.select(1), .width(1), .disabled("Z"), .enable("false")) multiplexer_7 (
    .in0(MemToReg), .in1(1'b0), .out(multiplexer_7_out), .sel(or_1_out));
  Multiplexer #(.select(1), .width(1), .disabled("Z"), .enable("false")) multiplexer_8 (
    .in0(MemWrite), .in1(1'b0), .out(multiplexer_8_out), .sel(or_1_out));
  Multiplexer #(.select(1), .width(1), .disabled("Z"), .enable("false")) multiplexer_9 (
    .in0(AluSrcB), .in1(1'b0), .out(multiplexer_9_out), .sel(or_1_out));
  Multiplexer #(.select(1), .width(1), .disabled("Z"), .enable("false")) multiplexer_10 (
    .in0(RegWrite), .in1(1'b0), .out(multiplexer_10_out), .sel(or_1_out));
  Multiplexer #(.select(1), .width(1), .disabled("Z"), .enable("false")) multiplexer_11 (
    .in0(S_type), .in1(1'b0), .out(multiplexer_11_out), .sel(or_1_out));
  Multiplexer #(.select(1), .width(1), .disabled("Z"), .enable("false")) multiplexer_12 (
    .in0(ecall), .in1(1'b0), .out(multiplexer_12_out), .sel(or_1_out));
  Multiplexer #(.select(1), .width(1), .disabled("Z"), .enable("false")) multiplexer_13 (
    .in0(halt), .in1(1'b0), .out(multiplexer_13_out), .sel(or_1_out));
  Multiplexer #(.select(1), .width(4), .disabled("Z"), .enable("false")) multiplexer_14 (
    .in0(AluOp), .in1(4'b0000), .out(multiplexer_14_out), .sel(or_1_out));
  Multiplexer #(.select(1), .width(5), .disabled("Z"), .enable("false")) multiplexer_15 (
    .in0(rd), .in1({5{1'b0}}), .out(multiplexer_15_out), .sel(or_1_out));
  Multiplexer #(.select(1), .width(32), .disabled("Z"), .enable("false")) multiplexer_16 (
    .in0(R1), .in1({32{1'b0}}), .out(multiplexer_16_out), .sel(or_1_out));
  Multiplexer #(.select(1), .width(32), .disabled("Z"), .enable("false")) multiplexer_17 (
    .in0(R2), .in1({32{1'b0}}), .out(multiplexer_17_out), .sel(or_1_out));
  Multiplexer #(.select(1), .width(32), .disabled("Z"), .enable("false")) multiplexer_18 (
    .in0(PC), .in1({32{1'b0}}), .out(multiplexer_18_out), .sel(or_1_out));
  Multiplexer #(.select(1), .width(32), .disabled("Z"), .enable("false")) multiplexer_19 (
    .in0(PC_4), .in1({32{1'b0}}), .out(multiplexer_19_out), .sel(or_1_out));
  Multiplexer #(.select(1), .width(32), .disabled("Z"), .enable("false")) multiplexer_20 (
    .in0(imm_si), .in1({32{1'b0}}), .out(multiplexer_20_out), .sel(or_1_out));
  Multiplexer #(.select(1), .width(32), .disabled("Z"), .enable("false")) multiplexer_21 (
    .in0(imm_b), .in1({32{1'b0}}), .out(multiplexer_21_out), .sel(or_1_out));
  Multiplexer #(.select(1), .width(32), .disabled("Z"), .enable("false")) multiplexer_22 (
    .in0(imm_j), .in1({32{1'b0}}), .out(multiplexer_22_out), .sel(or_1_out));
  Multiplexer #(.select(1), .width(1), .disabled("Z"), .enable("false")) multiplexer_23 (
    .in0(predict), .in1(1'b0), .out(multiplexer_23_out), .sel(or_1_out));
  Multiplexer #(.select(1), .width(32), .disabled("Z"), .enable("false")) multiplexer_24 (
    .in0(IR), .in1({32{1'b0}}), .out(multiplexer_24_out), .sel(or_1_out));
  Multiplexer #(.select(1), .width(1), .disabled("Z"), .enable("false")) multiplexer_25 (
    .in0(valid), .in1(1'b0), .out(multiplexer_25_out), .sel(or_1_out));
  or or_1 (or_1_out, reset, refresh);
  Register #(.width(1), .trigger("rising"), .Select("low")) register_1 (
    .D(multiplexer_1_out), .en(not_1_out), .Q(JAL_2), .clk(clk));  // open: clr
  Register #(.width(1), .trigger("rising"), .Select("low")) register_2 (
    .D(multiplexer_2_out), .en(not_1_out), .Q(JALR_2), .clk(clk));  // open: clr
  Register #(.width(1), .trigger("rising"), .Select("low")) register_3 (
    .D(multiplexer_3_out), .en(not_1_out), .Q(is_lb_2), .clk(clk));  // open: clr
  Register #(.width(1), .trigger("rising"), .Select("low")) register_4 (
    .D(multiplexer_4_out), .en(not_1_out), .Q(begue_2), .clk(clk));  // open: clr
  Register #(.width(1), .trigger("rising"), .Select("low")) register_5 (
    .D(multiplexer_5_out), .en(not_1_out), .Q(Beq_2), .clk(clk));  // open: clr
  Register #(.width(1), .trigger("rising"), .Select("low")) register_6 (
    .D(multiplexer_6_out), .en(not_1_out), .Q(Bne_2), .clk(clk));  // open: clr
  Register #(.width(1), .trigger("rising"), .Select("low")) register_7 (
    .D(multiplexer_7_out), .en(not_1_out), .Q(MemToReg_2), .clk(clk));  // open: clr
  Register #(.width(1), .trigger("rising"), .Select("low")) register_8 (
    .D(multiplexer_8_out), .en(not_1_out), .Q(MemWrite_2), .clk(clk));  // open: clr
  Register #(.width(1), .trigger("rising"), .Select("low")) register_9 (
    .D(multiplexer_9_out), .en(not_1_out), .Q(AluSrcB_2), .clk(clk));  // open: clr
  Register #(.width(1), .trigger("rising"), .Select("low")) register_10 (
    .D(multiplexer_10_out), .en(not_1_out), .Q(RegWrite_2), .clk(clk));  // open: clr
  Register #(.width(1), .trigger("rising"), .Select("low")) register_11 (
    .D(multiplexer_11_out), .en(not_1_out), .Q(S_type_2), .clk(clk));  // open: clr
  Register #(.width(1), .trigger("rising"), .Select("low")) register_12 (
    .D(multiplexer_12_out), .en(not_1_out), .Q(ecall_2), .clk(clk));  // open: clr
  Register #(.width(1), .trigger("rising"), .Select("low")) register_13 (
    .D(multiplexer_13_out), .en(not_1_out), .Q(halt_3), .clk(clk));  // open: clr
  Register #(.width(4), .trigger("rising"), .Select("low")) register_14 (
    .D(multiplexer_14_out), .en(not_1_out), .Q(Aluop_2), .clk(clk));  // open: clr
  Register #(.width(5), .trigger("rising"), .Select("low")) register_15 (
    .D(multiplexer_15_out), .en(not_1_out), .Q(rd_2), .clk(clk));  // open: clr
  Register #(.width(32), .trigger("rising"), .Select("low")) register_16 (
    .D(multiplexer_16_out), .en(not_1_out), .Q(R1_2), .clk(clk));  // open: clr
  Register #(.width(32), .trigger("rising"), .Select("low")) register_17 (
    .D(multiplexer_17_out), .en(not_1_out), .Q(R2_2), .clk(clk));  // open: clr
  Register #(.width(32), .trigger("rising"), .Select("low")) register_18 (
    .D(multiplexer_18_out), .en(not_1_out), .Q(PC_2), .clk(clk));  // open: clr
  Register #(.width(32), .trigger("rising"), .Select("low")) register_19 (
    .D(multiplexer_19_out), .en(not_1_out), .Q(PC_4_2), .clk(clk));  // open: clr
  Register #(.width(32), .trigger("rising"), .Select("low")) register_20 (
    .D(multiplexer_20_out), .en(not_1_out), .Q(imm_si_2), .clk(clk));  // open: clr
  Register #(.width(32), .trigger("rising"), .Select("low")) register_21 (
    .D(multiplexer_21_out), .en(not_1_out), .Q(imm_b_2), .clk(clk));  // open: clr
  Register #(.width(32), .trigger("rising"), .Select("low")) register_22 (
    .D(multiplexer_22_out), .en(not_1_out), .Q(imm_j_2), .clk(clk));  // open: clr
  Register #(.width(1), .trigger("rising"), .Select("low")) register_23 (
    .D(multiplexer_23_out), .en(not_1_out), .Q(predict_2), .clk(clk));  // open: clr
  Register #(.width(32), .trigger("rising"), .Select("low")) register_24 (
    .D(multiplexer_24_out), .en(not_1_out), .Q(IR_2), .clk(clk));  // open: clr
  not not_1 (not_1_out, Halt_2);
  Register #(.width(1), .trigger("rising"), .Select("low")) register_25 (
    .D(multiplexer_25_out), .en(not_1_out), .Q(valid_2), .clk(clk));  // open: clr
endmodule

module \气泡器件  (
  input  [4:0] rs1,
  input  BranchTaken,
  input  [4:0] rs2,
  input  rs1_used,
  input  rs2_used,
  input  [4:0] ex_WriteReg,
  input  ex_RegWrite,
  input  [4:0] Mem_WriteReg,
  input  Mem_RegWrite,
  output \清空 ,
  output \阻塞 
);

  wire and_1_out, and_2_out, and_3_out, and_4_out, comparator_1_eq, comparator_2_eq, comparator_3_eq,
       comparator_4_eq, comparator_5_eq, comparator_6_eq, not_1_out, not_2_out;

  Comparator #(.width(5), .mode("twosComplement")) comparator_1 (
    .a(rs1), .b({5{1'b0}}), .eq(comparator_1_eq));  // open: gt, lt
  Comparator #(.width(5), .mode("twosComplement")) comparator_2 (
    .a(rs2), .b({5{1'b0}}), .eq(comparator_2_eq));  // open: gt, lt
  not not_1 (not_1_out, comparator_1_eq);
  not not_2 (not_2_out, comparator_2_eq);
  Comparator #(.width(5), .mode("twosComplement")) comparator_3 (
    .a(rs1), .b(ex_WriteReg), .eq(comparator_3_eq));  // open: gt, lt
  Comparator #(.width(5), .mode("twosComplement")) comparator_4 (
    .a(rs1), .b(Mem_WriteReg), .eq(comparator_4_eq));  // open: gt, lt
  Comparator #(.width(5), .mode("twosComplement")) comparator_5 (
    .a(rs2), .b(ex_WriteReg), .eq(comparator_5_eq));  // open: gt, lt
  Comparator #(.width(5), .mode("twosComplement")) comparator_6 (
    .a(rs2), .b(Mem_WriteReg), .eq(comparator_6_eq));  // open: gt, lt
  and and_1 (and_1_out, not_1_out, comparator_3_eq, ex_RegWrite, rs1_used);
  and and_2 (and_2_out, rs1_used, comparator_4_eq, Mem_RegWrite, not_1_out);
  and and_3 (and_3_out, rs2_used, comparator_5_eq, ex_RegWrite, not_2_out);
  and and_4 (and_4_out, rs2_used, comparator_6_eq, Mem_RegWrite, not_2_out);
  or or_1 (\阻塞 , and_1_out, and_2_out, and_3_out, and_4_out);

  assign \清空  = BranchTaken;

  // Notes on the sheet:
  //   我是sb，没有考虑ecall的情况，其实在excel表里面增加ecall的rs1used和rs2就行
  //   清空是遇到分支的时候需要清空
  //   阻塞是因为我们的数据冲突了
endmodule

module \重定向  (
  input  rs1_used,
  input  ex_memtoReg,
  input  ex_RegWrite,
  input  rs2_used,
  input  [4:0] ex_WriteReg,
  input  [4:0] rs1,
  input  Mem_RegWrite,
  input  [4:0] rs2,
  input  [4:0] Mem_WriteReg,
  output LoadUse,
  output [1:0] r1Foward,
  output [1:0] r2Forward
);

  wire and_1_out, and_2_out, and_3_out, and_4_out, and_5_out, and_6_out, comparator_1_eq, comparator_2_eq,
       comparator_3_eq, comparator_4_eq, comparator_5_eq, comparator_6_eq, comparator_7_eq, comparator_8_eq,
       comparator_9_eq, comparator_10_eq, comparator_11_eq, comparator_12_eq, not_1_out, not_2_out,
       not_3_out, not_4_out, not_5_out, not_6_out;

  not not_1 (not_1_out, comparator_1_eq);
  Comparator #(.width(5), .mode("twosComplement")) comparator_1 (
    .a(rs1), .b({5{1'b0}}), .eq(comparator_1_eq));  // open: gt, lt
  Comparator #(.width(5), .mode("twosComplement")) comparator_2 (
    .a(rs1), .b(ex_WriteReg), .eq(comparator_2_eq));  // open: gt, lt
  Comparator #(.width(5), .mode("twosComplement")) comparator_3 (
    .a(rs2), .b({5{1'b0}}), .eq(comparator_3_eq));  // open: gt, lt
  not not_2 (not_2_out, comparator_3_eq);
  Comparator #(.width(5), .mode("twosComplement")) comparator_4 (
    .a(rs2), .b(ex_WriteReg), .eq(comparator_4_eq));  // open: gt, lt
  and and_1 (and_1_out, rs1_used, not_1_out, comparator_2_eq, ex_memtoReg);
  and and_2 (and_2_out, rs2_used, not_2_out, comparator_4_eq, ex_memtoReg);
  or or_1 (LoadUse, and_1_out, and_2_out);
  not not_3 (not_3_out, comparator_5_eq);
  Comparator #(.width(5), .mode("twosComplement")) comparator_5 (
    .a(rs1), .b({5{1'b0}}), .eq(comparator_5_eq));  // open: gt, lt
  Comparator #(.width(5), .mode("twosComplement")) comparator_6 (
    .a(rs1), .b(Mem_WriteReg), .eq(comparator_6_eq));  // open: gt, lt
  not not_4 (not_4_out, comparator_7_eq);
  Comparator #(.width(5), .mode("twosComplement")) comparator_7 (
    .a(rs1), .b({5{1'b0}}), .eq(comparator_7_eq));  // open: gt, lt
  Comparator #(.width(5), .mode("twosComplement")) comparator_8 (
    .a(rs1), .b(ex_WriteReg), .eq(comparator_8_eq));  // open: gt, lt
  not not_5 (not_5_out, comparator_9_eq);
  Comparator #(.width(5), .mode("twosComplement")) comparator_9 (
    .a(rs2), .b({5{1'b0}}), .eq(comparator_9_eq));  // open: gt, lt
  Comparator #(.width(5), .mode("twosComplement")) comparator_10 (
    .a(rs2), .b(Mem_WriteReg), .eq(comparator_10_eq));  // open: gt, lt
  not not_6 (not_6_out, comparator_11_eq);
  Comparator #(.width(5), .mode("twosComplement")) comparator_11 (
    .a(rs2), .b({5{1'b0}}), .eq(comparator_11_eq));  // open: gt, lt
  Comparator #(.width(5), .mode("twosComplement")) comparator_12 (
    .a(rs2), .b(ex_WriteReg), .eq(comparator_12_eq));  // open: gt, lt
  and and_3 (and_3_out, rs1_used, not_3_out, comparator_6_eq, Mem_RegWrite);
  and and_4 (and_4_out, rs1_used, not_4_out, comparator_8_eq, ex_RegWrite);
  and and_5 (and_5_out, rs2_used, not_5_out, comparator_10_eq, Mem_RegWrite);
  and and_6 (and_6_out, rs2_used, not_6_out, comparator_12_eq, ex_RegWrite);
  Priority_Encoder #(.select(2), .disabled("Z")) priority_encoder_1 (
    .in0(1'b1), .in1(and_3_out), .in2(and_4_out), .in3(1'b0), .out(r1Foward));  // open: gs, en_out, en_in
  Priority_Encoder #(.select(2), .disabled("Z")) priority_encoder_2 (
    .in0(1'b1), .in1(and_5_out), .in2(and_6_out), .in3(1'b0), .out(r2Forward));  // open: gs, en_out, en_in

  // Notes on the sheet:
  //   只用处理和ex的关系
endmodule

module foward (
  input  [1:0] rs1_foward,
  input  [1:0] rs2_foward,
  input  paopao,
  input  clk,
  output [1:0] rs1_foward_2,
  output [1:0] rs2_foward_2
);

  wire [1:0] multiplexer_1_out, multiplexer_2_out;

  Multiplexer #(.select(1), .width(2), .disabled("Z"), .enable("false")) multiplexer_1 (
    .in0(rs1_foward), .in1(2'b00), .out(multiplexer_1_out), .sel(paopao));
  Multiplexer #(.select(1), .width(2), .disabled("Z"), .enable("false")) multiplexer_2 (
    .in0(rs2_foward), .in1(2'b00), .out(multiplexer_2_out), .sel(paopao));
  Register #(.width(2), .trigger("rising"), .Select("low")) register_1 (
    .D(multiplexer_1_out), .Q(rs1_foward_2), .clk(clk));  // open: en, clr
  Register #(.width(2), .trigger("rising"), .Select("low")) register_2 (
    .D(multiplexer_2_out), .Q(rs2_foward_2), .clk(clk));  // open: en, clr
endmodule
module \动态分支预测  (
  output RegWrite,
  output MemWrite,
  output [31:0] IF_PC,
  output [31:0] ID_PC,
  output [31:0] EX_PC,
  output [31:0] M_PC,
  output [31:0] WB_PC,
  output [31:0] RDin,
  output [31:0] MDin,
  output [31:0] LedData
);

  wire alu_1_equal, alu_1_out_4, and_2_out, and_3_out, and_4_out, and_5_out, and_6_out, and_7_out, bgue, CLK,
       clock_1_out, comparator_1_eq, comparator_1_lt, comparator_2_gt, comparator_3_eq, comparator_4_eq,
       comparator_5_eq, d_ff_1_q, ecall, ex_predict_jump, Go, halt, id_predict, IR1, IR2, IR3, is_jump,
       is_lb, JAL, JALR, less, loadused, multiplexer_3_out, nand_1_out, not_2_out, not_3_out, not_4_out,
       not_5_out, not_7_out, not_8_out, or_2_out, or_3_out, or_4_out, or_5_out, Predict_jump, predictErrpr,
       register_2_q, riscv_probe_3_p2, RST, S_type, W1, W2, W3, \单周期硬布线控制器_1_alu_src , \单周期硬布线控制器_1_beq ,
       \单周期硬布线控制器_1_bne , \单周期硬布线控制器_1_memtoreg , \单周期硬布线控制器_1_memwrite , \单周期硬布线控制器_1_regwrite ,
       \单周期硬布线控制器_1_rs1_used , \单周期硬布线控制器_1_rs2_used , \单周期硬布线控制器_1_uret , \流水器器件_1_valid_2 ,
       \流水器器件_2_alusrcb_2 , \流水器器件_2_begue_2 , \流水器器件_2_beq_2 , \流水器器件_2_bne_2 , \流水器器件_2_ecall_2 ,
       \流水器器件_2_is_lb_2 , \流水器器件_2_jal_2 , \流水器器件_2_jalr_2 , \流水器器件_2_memtoreg_2 , \流水器器件_2_memwrite_2 ,
       \流水器器件_2_regwrite_2 , \流水器器件_2_valid_2 , \流水器器件_3_halt_3 , \流水器器件_3_is_lb_2 , \流水器器件_3_jal_2 ,
       \流水器器件_3_jalr_2 , \流水器器件_3_memtoreg_2 , \流水器器件_3_regwrite_2 , \流水器器件_3_valid_2 , \流水器器件_4_halt_3 ;
  wire [1:0] foward_1_rs1_foward_2, foward_1_rs2_foward_2, jump, priority_encoder_2_out, \重定向_1_r1foward ,
       \重定向_1_r2forward ;
  wire [3:0] \单周期硬布线控制器_1_alu_op , \流水器器件_2_aluop_2 ;
  wire [4:0] multiplexer_4_out, multiplexer_5_out, \流水器器件_2_rd_2 , \流水器器件_3_rd_2 , \流水器器件_4_rd_2 ;
  wire [7:0] multiplexer_12_out;
  wire [11:0] multiplexer_6_out;
  wire [12:0] CNT_num;
  wire [15:0] \LoadUse次数 , \总周期数 , \插入气泡数 , \无条件分支数 , \条件分支成功数 ;
  wire [31:0] a, ab, add_PC, adder_1_out, alu_1_result, Alu_out, Alu_out2, and_1_out, bit_extender_1_out,
       bit_extender_2_out, bit_extender_3_out, bit_extender_4_out, bout, btb_1_btb_jumpaddr, c, cd, EX_IR,
       expc_4, ID_IR, IF_IR, jout, MEM_IR, multiplexer_2_out, multiplexer_7_out, multiplexer_11_out,
       multiplexer_13_out, PC_4id, Predict_jumpaddr, R1, ram_1_data, regifile_1_r2, shifter_1_out,
       shifter_2_out, WB_IR, \流水器器件_2_imm_b_2 , \流水器器件_2_imm_j_2 , \流水器器件_2_imm_si_2 , \流水器器件_3_pc_4_2 ;

  Button \u_总复位  (.out(RST));
  Button _1 (.out(IR1));
  Button _2 (.out(IR2));
  Button _3 (.out(IR3));
  // Probe on \总周期数 
  // Probe on \总周期数 
  Button \u_继续运行  (.out(Go));
  LED #(.active("true")) led_1 (.in(W1));
  LED #(.active("true")) led_2 (.in(W2));
  LED #(.active("true")) led_3 (.in(W3));
  Hex_Digit_Display hex_digit_display_1 (.value(LedData[31:28]));  // open: dp
  // Probe on IF_PC[19:0]
  // RiscV_Probe riscv_probe_1: pin names not known; wires that end beside it: IF_IR
  assign and_1_out = 32'hfffffffe & alu_1_result;  // AND_Gate and_1, 32 bits wide
  Hex_Digit_Display hex_digit_display_2 (.value(LedData[27:24]));  // open: dp
  Hex_Digit_Display hex_digit_display_3 (.value(LedData[23:20]));  // open: dp
  // Probe on ID_PC[19:0]
  // RiscV_Probe riscv_probe_2: pin names not known; wires that end beside it: ID_IR
  or or_1 (is_jump, \流水器器件_2_begue_2 , \流水器器件_2_beq_2 , \流水器器件_2_bne_2 , \流水器器件_2_jal_2 , \流水器器件_2_jalr_2 );
  Multiplexer #(.select(2), .width(32), .disabled("Z"), .enable("false")) multiplexer_1 (
    .in0(expc_4), .in1(\流水器器件_2_imm_b_2 ), .in2(\流水器器件_2_imm_j_2 ), .in3(and_1_out), .out(add_PC), .sel(jump));
  Hex_Digit_Display hex_digit_display_4 (.value(LedData[19:16]));  // open: dp
  Hex_Digit_Display hex_digit_display_5 (.value(LedData[15:12]));  // open: dp
  Hex_Digit_Display hex_digit_display_6 (.value(LedData[7:4]));  // open: dp
  Hex_Digit_Display hex_digit_display_7 (.value(LedData[11:8]));  // open: dp
  // Probe on EX_PC[19:0]
  // RiscV_Probe riscv_probe_3: pin names not known; wires that end beside it: EX_IR, riscv_probe_3_p2
  not not_1 (riscv_probe_3_p2, halt);
  Counter #(.width(16), .max('hffff), .ongoal("wrap"), .trigger("rising"), .behavior("old")) counter_1 (
    .Q(\总周期数 ), .clk(CLK));  // open: load, D, count, carry, clr, preset
  and and_2 (and_2_out, alu_1_out_4, \流水器器件_2_begue_2 );
  Multiplexer #(.select(1), .width(32), .disabled("Z"), .enable("false")) multiplexer_2 (
    .in0(Predict_jumpaddr), .in1(add_PC), .out(multiplexer_2_out), .sel(predictErrpr));
  Hex_Digit_Display hex_digit_display_8 (.value(LedData[3:0]));  // open: dp
  not not_2 (not_2_out, alu_1_equal);
  and and_3 (and_3_out, \流水器器件_2_beq_2 , alu_1_equal);
  and and_4 (and_4_out, not_2_out, \流水器器件_2_bne_2 );
  or or_2 (or_2_out, and_2_out, and_3_out, and_4_out);
  Priority_Encoder #(.select(2), .disabled("Z")) priority_encoder_1 (
    .in0(1'b1), .in1(or_2_out), .in2(\流水器器件_2_jal_2 ), .in3(\流水器器件_2_jalr_2 ), .out(jump));  // open: gs, en_out, en_in
  // Probe on \总周期数 
  // Probe on M_PC[19:0]
  // RiscV_Probe riscv_probe_4: pin names not known; wires that end beside it: MEM_IR
  Register #(.width(32), .trigger("rising"), .Select("low")) PC (
    .D(multiplexer_2_out), .en(not_3_out), .Q(IF_PC), .clk(CLK), .clr(RST));
  not not_3 (not_3_out, or_3_out);
  or or_3 (or_3_out, loadused, halt);
  // Probe on \总周期数 
  // Probe on \无条件分支数 
  // Probe on \条件分支成功数 
  // Probe on \插入气泡数 
  // Probe on \LoadUse次数 
  // Probe on IF_PC[11:0]
  // Probe on WB_PC[19:0]
  // RiscV_Probe riscv_probe_5: pin names not known; wires that end beside it: WB_IR
  Adder #(.width(32)) adder_1 (.a(IF_PC), .b(32'h4), .out(adder_1_out));  // open: cin, cout
  // Probe on EX_PC[11:0]
  // Probe on ID_PC[11:0]
  Multiplexer #(.select(1), .width(1), .disabled("Z"), .enable("false")) multiplexer_3 (
    .in0(1'b1), .in1(1'b0), .out(multiplexer_3_out), .sel(halt));
  ROM #(.addrWidth(10), .dataWidth(32), .Select("high")) rom_1 (.addr(IF_PC[11:2]), .data(IF_IR));
  // Probe on M_PC[11:0]
  D_Flip_Flop #(.trigger("high"), .Pre_Clr_Positions("LEGACY"), .NegatePresetClear("false"), .enable("true"), .NewFFLayout("false")) d_ff_1 (.Q(d_ff_1_q));  // open: clk, D, Qn, preset, en, reset
  // Probe on 13'h178
  // RiscV_Probe riscv_probe_6: pin names not known; wires that end beside it: IF_IR
  // Probe on WB_PC[11:0]
  Comparator #(.width(13), .mode("twosComplement")) comparator_1 (
    .a(CNT_num), .b(13'h178), .eq(comparator_1_eq), .lt(comparator_1_lt));  // open: gt
  Clock #(.highDuration(1), .lowDuration(1)) clock_1 (.out(clock_1_out));
  \流水器器件  \u_流水器器件_1  (
    .PC(IF_PC), .PC_4(adder_1_out), .IR(IF_IR), .PC_2(ID_PC), .PC_4_2(PC_4id), .IR_2(ID_IR), .reset(1'b0),
    .refresh(predictErrpr), .Halt_2(loadused), .clk(CLK), .valid(multiplexer_3_out),
    .valid_2(\流水器器件_1_valid_2 ), .predict(Predict_jump), .predict_2(id_predict));  // open: JAL, JALR, is_lb, begue, Beq, Bne, MemToReg, MemWrite, AluSrcB, RegWrite, S_type, ecall, halt, AluOp, rd, R1, R2, imm_si, imm_b, imm_j, JAL_2, JALR_2, is_lb_2, begue_2, Beq_2, Bne_2, MemToReg_2, MemWrite_2, AluSrcB_2, RegWrite_2, S_type_2, ecall_2, halt_3, Aluop_2, rd_2, R1_2, R2_2, imm_si_2, imm_b_2, imm_j_2
  nand nand_1 (nand_1_out, d_ff_1_q, comparator_1_eq);
  Counter #(.width(13), .max('h1fff), .ongoal("stay"), .trigger("rising"), .behavior("old")) counter_2 (
    .count(comparator_1_lt), .Q(CNT_num), .clk(clock_1_out));  // open: load, D, carry, clr, preset
  assign CLK = nand_1_out ? clock_1_out : 1'bz;  // Controlled_Buffer controlled_buffer_1
  Pull_Resistor #(.pull(1)) pull_resistor_1 (.node(CLK));
  Multiplexer #(.select(1), .width(5), .disabled("Z"), .enable("false")) multiplexer_4 (
    .in0(ID_IR[19:15]), .in1(5'b10001), .out(multiplexer_4_out), .sel(ecall));
  Multiplexer #(.select(1), .width(5), .disabled("Z"), .enable("false")) multiplexer_5 (
    .in0(ID_IR[24:20]), .in1(5'b01010), .out(multiplexer_5_out), .sel(ecall));
  Comparator #(.width(2), .mode("unsigned")) comparator_2 (.a(jump), .b(2'b00), .gt(comparator_2_gt));  // open: eq, lt
  \单周期硬布线控制器  \u_单周期硬布线控制器_1  (
    .Funct({ID_IR[30], ID_IR[25], ID_IR[14:12]}), .OP(ID_IR[6:2]), .ALU_OP(\单周期硬布线控制器_1_alu_op ),
    .MemToReg(\单周期硬布线控制器_1_memtoreg ), .MemWrite(\单周期硬布线控制器_1_memwrite ), .ALU_SRC(\单周期硬布线控制器_1_alu_src ),
    .RegWrite(\单周期硬布线控制器_1_regwrite ), .ecall(ecall), .S_type(S_type), .Jalr(JALR), .Beq(\单周期硬布线控制器_1_beq ),
    .JAL(JAL), .Bne(\单周期硬布线控制器_1_bne ), .in_3(ID_IR[21]), .uret(\单周期硬布线控制器_1_uret ), .is_lb(is_lb),
    .bgue(bgue), .rs1_used(\单周期硬布线控制器_1_rs1_used ), .rs2_used(\单周期硬布线控制器_1_rs2_used ));
  Multiplexer #(.select(1), .width(12), .disabled("Z"), .enable("false")) multiplexer_6 (
    .in0(ID_IR[31:20]), .in1({ID_IR[31:25], ID_IR[11:7]}), .out(multiplexer_6_out), .sel(S_type));
  assign bit_extender_1_out = {{20{ID_IR[31]}}, {ID_IR[31], ID_IR[7], ID_IR[30:25], ID_IR[11:8]}};  // Bit_Extender bit_extender_1
  assign bit_extender_2_out = {{12{ID_IR[31]}}, {ID_IR[31], ID_IR[19:12], ID_IR[20], ID_IR[30:21]}};  // Bit_Extender bit_extender_2
  assign bit_extender_3_out = {{20{multiplexer_6_out[11]}}, multiplexer_6_out};  // Bit_Extender bit_extender_3
  Shifter #(.width(32), .shift("ll")) shifter_1 (.in(bit_extender_1_out), .\dist (5'b00001), .out(shifter_1_out));
  not not_4 (not_4_out, CLK);
  Regifile regifile_1 (
    .Din(RDin), .Clk(not_4_out), .R1(R1), .R2(regifile_1_r2), .WE(RegWrite), .W_num(\流水器器件_4_rd_2 ),
    .R1_num(multiplexer_4_out), .R2_num(multiplexer_5_out));
  Shifter #(.width(32), .shift("ll")) shifter_2 (.in(bit_extender_2_out), .\dist (5'b00001), .out(shifter_2_out));
  Adder #(.width(32)) adder_2 (.a(shifter_1_out), .b(ID_PC), .out(bout));  // open: cin, cout
  Adder #(.width(32)) adder_3 (.a(shifter_2_out), .b(ID_PC), .out(jout));  // open: cin, cout
  not not_5 (not_5_out, \流水器器件_1_valid_2 );
  BTB btb_1 (
    .PC(IF_PC), .EX_PC(EX_PC), .EX_BranchAddr(add_PC), .EX_Branch(is_jump), .EX_Branched(comparator_2_gt),
    .in_6(CLK), .IF_PredictJump(Predict_jump), .BTB_JumpAddr(btb_1_btb_jumpaddr));
  \重定向  \u_重定向_1  (
    .rs1_used(\单周期硬布线控制器_1_rs1_used ), .ex_memtoReg(\流水器器件_2_memtoreg_2 ),
    .ex_RegWrite(\流水器器件_2_regwrite_2 ), .rs2_used(\单周期硬布线控制器_1_rs2_used ), .ex_WriteReg(\流水器器件_2_rd_2 ),
    .rs1(multiplexer_4_out), .Mem_RegWrite(\流水器器件_3_regwrite_2 ), .rs2(multiplexer_5_out),
    .Mem_WriteReg(\流水器器件_3_rd_2 ), .LoadUse(loadused), .r1Foward(\重定向_1_r1foward ),
    .r2Forward(\重定向_1_r2forward ));
  or or_4 (or_4_out, not_5_out, loadused);
  \流水器器件  \u_流水器器件_2  (
    .JAL(JAL), .JALR(JALR), .is_lb(is_lb), .begue(bgue), .Beq(\单周期硬布线控制器_1_beq ), .Bne(\单周期硬布线控制器_1_bne ),
    .MemToReg(\单周期硬布线控制器_1_memtoreg ), .MemWrite(\单周期硬布线控制器_1_memwrite ), .AluSrcB(\单周期硬布线控制器_1_alu_src ),
    .RegWrite(\单周期硬布线控制器_1_regwrite ), .S_type(S_type), .ecall(ecall), .AluOp(\单周期硬布线控制器_1_alu_op ),
    .rd(ID_IR[11:7]), .R1(R1), .R2(regifile_1_r2), .PC(ID_PC), .PC_4(PC_4id), .imm_si(bit_extender_3_out),
    .imm_b(bout), .imm_j(jout), .JAL_2(\流水器器件_2_jal_2 ), .JALR_2(\流水器器件_2_jalr_2 ),
    .is_lb_2(\流水器器件_2_is_lb_2 ), .begue_2(\流水器器件_2_begue_2 ), .Beq_2(\流水器器件_2_beq_2 ),
    .Bne_2(\流水器器件_2_bne_2 ), .MemToReg_2(\流水器器件_2_memtoreg_2 ), .MemWrite_2(\流水器器件_2_memwrite_2 ),
    .AluSrcB_2(\流水器器件_2_alusrcb_2 ), .RegWrite_2(\流水器器件_2_regwrite_2 ), .ecall_2(\流水器器件_2_ecall_2 ),
    .Aluop_2(\流水器器件_2_aluop_2 ), .rd_2(\流水器器件_2_rd_2 ), .R1_2(a), .R2_2(c), .PC_2(EX_PC), .PC_4_2(expc_4),
    .imm_si_2(\流水器器件_2_imm_si_2 ), .imm_b_2(\流水器器件_2_imm_b_2 ), .imm_j_2(\流水器器件_2_imm_j_2 ),
    .reset(or_4_out), .refresh(predictErrpr), .Halt_2(halt), .clk(CLK), .valid(\流水器器件_1_valid_2 ),
    .valid_2(\流水器器件_2_valid_2 ), .predict(id_predict), .predict_2(ex_predict_jump));  // open: halt, IR, S_type_2, halt_3, IR_2
  Multiplexer #(.select(1), .width(32), .disabled("Z"), .enable("false")) multiplexer_7 (
    .in0(cd), .in1(\流水器器件_2_imm_si_2 ), .out(multiplexer_7_out), .sel(\流水器器件_2_alusrcb_2 ));
  Comparator #(.width(32), .mode("twosComplement")) comparator_3 (
    .a(ab), .b(32'h22), .eq(comparator_3_eq));  // open: gt, lt
  Comparator #(.width(32), .mode("twosComplement")) comparator_4 (
    .a(32'h22), .b(ab), .eq(comparator_4_eq));  // open: gt, lt
  and and_5 (and_5_out, ~comparator_4_eq, \流水器器件_2_ecall_2 );  // AND_Gate
  Multiplexer #(.select(1), .width(32), .disabled("Z"), .enable("false")) multiplexer_8 (
    .in0(adder_1_out), .in1(btb_1_btb_jumpaddr), .out(Predict_jumpaddr), .sel(Predict_jump));
  foward foward_1 (
    .rs1_foward(\重定向_1_r1foward ), .rs2_foward(\重定向_1_r2forward ), .paopao(loadused), .clk(CLK),
    .rs1_foward_2(foward_1_rs1_foward_2), .rs2_foward_2(foward_1_rs2_foward_2));
  ALU alu_1 (
    .X(ab), .Y(multiplexer_7_out), .AluOP(\流水器器件_2_aluop_2 ), .Equal(alu_1_equal), .Result(alu_1_result),
    .Result_2(Alu_out2), .out_4(alu_1_out_4), .out_6(less));
  and and_6 (and_6_out, \流水器器件_2_ecall_2 , comparator_3_eq);
  Comparator #(.width(1), .mode("unsigned")) comparator_5 (
    .a(ex_predict_jump), .b(comparator_2_gt), .eq(comparator_5_eq));  // open: gt, lt
  not not_6 (predictErrpr, comparator_5_eq);
  Register #(.width(32), .trigger("rising"), .Select("low")) register_1 (
    .D(cd), .en(and_6_out), .Q(LedData), .clk(CLK));  // open: clr
  not not_7 (not_7_out, \流水器器件_2_valid_2 );
  \流水器器件  \u_流水器器件_3  (
    .JAL(\流水器器件_2_jal_2 ), .JALR(\流水器器件_2_jalr_2 ), .is_lb(\流水器器件_2_is_lb_2 ),
    .MemToReg(\流水器器件_2_memtoreg_2 ), .MemWrite(\流水器器件_2_memwrite_2 ), .RegWrite(\流水器器件_2_regwrite_2 ),
    .halt(and_5_out), .rd(\流水器器件_2_rd_2 ), .R2(cd), .PC(EX_PC), .PC_4(expc_4), .imm_si(alu_1_result),
    .JAL_2(\流水器器件_3_jal_2 ), .JALR_2(\流水器器件_3_jalr_2 ), .is_lb_2(\流水器器件_3_is_lb_2 ),
    .MemToReg_2(\流水器器件_3_memtoreg_2 ), .MemWrite_2(MemWrite), .RegWrite_2(\流水器器件_3_regwrite_2 ),
    .halt_3(\流水器器件_3_halt_3 ), .rd_2(\流水器器件_3_rd_2 ), .R2_2(MDin), .PC_2(M_PC), .PC_4_2(\流水器器件_3_pc_4_2 ),
    .imm_si_2(Alu_out), .reset(not_7_out), .refresh(1'b0), .Halt_2(halt), .clk(CLK),
    .valid(\流水器器件_2_valid_2 ), .valid_2(\流水器器件_3_valid_2 ));  // open: begue, Beq, Bne, AluSrcB, S_type, ecall, AluOp, R1, imm_b, imm_j, IR, begue_2, Beq_2, Bne_2, AluSrcB_2, S_type_2, ecall_2, Aluop_2, R1_2, imm_b_2, imm_j_2, IR_2, predict, predict_2
  Multiplexer #(.select(2), .width(32), .disabled("Z"), .enable("false")) multiplexer_9 (
    .in0(a), .in1(RDin), .in2(Alu_out), .out(ab), .sel(foward_1_rs1_foward_2));  // open: in3
  or or_5 (or_5_out, \流水器器件_3_jal_2 , \流水器器件_3_jalr_2 );
  Multiplexer #(.select(2), .width(32), .disabled("Z"), .enable("false")) multiplexer_10 (
    .in0(c), .in1(RDin), .in2(Alu_out), .out(cd), .sel(foward_1_rs2_foward_2));  // open: in3
  Priority_Encoder #(.select(2), .disabled("Z")) priority_encoder_2 (
    .in0(1'b1), .in1(or_5_out), .in2(\流水器器件_3_memtoreg_2 ), .in3(1'b0), .out(priority_encoder_2_out));  // open: gs, en_out, en_in
  RAM #(.addrWidth(10), .dataWidth(32), .bus("separate"), .Select("high")) ram_1 (
    .addr(Alu_out[11:2]), .din(MDin), .data(ram_1_data), .str(MemWrite), .sel(1'b1), .clk(CLK),
    .ld(\流水器器件_3_memtoreg_2 ), .clr(1'b0));
  Multiplexer #(.select(1), .width(32), .disabled("Z"), .enable("false")) multiplexer_11 (
    .in0(ram_1_data), .in1(bit_extender_4_out), .out(multiplexer_11_out), .sel(\流水器器件_3_is_lb_2 ));
  Multiplexer #(.select(2), .width(8), .disabled("Z"), .enable("false")) multiplexer_12 (
    .in0(ram_1_data[7:0]), .in1(ram_1_data[15:8]), .in2(ram_1_data[23:16]), .in3(ram_1_data[31:24]),
    .out(multiplexer_12_out), .sel(Alu_out[1:0]));
  assign bit_extender_4_out = {{24{multiplexer_12_out[7]}}, multiplexer_12_out};  // Bit_Extender bit_extender_4
  Multiplexer #(.select(2), .width(32), .disabled("Z"), .enable("false")) multiplexer_13 (
    .in0(Alu_out), .in1(\流水器器件_3_pc_4_2 ), .in2(multiplexer_11_out), .out(multiplexer_13_out),
    .sel(priority_encoder_2_out));  // open: in3
  not not_8 (not_8_out, \流水器器件_3_valid_2 );
  \流水器器件  \u_流水器器件_4  (
    .RegWrite(\流水器器件_3_regwrite_2 ), .halt(\流水器器件_3_halt_3 ), .rd(\流水器器件_3_rd_2 ), .PC(M_PC),
    .imm_si(Alu_out), .IR(multiplexer_13_out), .RegWrite_2(RegWrite), .halt_3(\流水器器件_4_halt_3 ),
    .rd_2(\流水器器件_4_rd_2 ), .PC_2(WB_PC), .IR_2(RDin), .reset(not_8_out), .refresh(1'b0), .Halt_2(halt),
    .clk(CLK), .valid(\流水器器件_3_valid_2 ));  // open: JAL, JALR, is_lb, begue, Beq, Bne, MemToReg, MemWrite, AluSrcB, S_type, ecall, AluOp, R1, R2, PC_4, imm_b, imm_j, JAL_2, JALR_2, is_lb_2, begue_2, Beq_2, Bne_2, MemToReg_2, MemWrite_2, AluSrcB_2, S_type_2, ecall_2, Aluop_2, R1_2, R2_2, PC_4_2, imm_si_2, imm_b_2, imm_j_2, valid_2, predict, predict_2
  Register #(.width(1), .trigger("falling"), .Select("low")) register_2 (
    .D(1'b0), .Q(register_2_q), .clk(\流水器器件_4_halt_3 ), .preset(Go));  // open: en, clr, cs
  and and_7 (and_7_out, ~register_2_q, \流水器器件_4_halt_3 );  // AND_Gate
  Register #(.width(1), .trigger("falling"), .Select("low")) register_3 (
    .D(and_7_out), .Q(halt), .clk(CLK));  // open: en, clr

  // Other names for the same wires on the sheet: IR[31:0] = ID_IR; rd[4:0] = ID_IR[11:7]; MEM_PC[31:0] = M_PC;
  //   PC[31:0] = IF_PC; PCid[31:0] = ID_PC

  // Notes on the sheet:
  //   中断源
  //   时空图监测，可删除
  //   中断等待指示
  //   易错点，我们传过去的可能是错误的指令，我们这里应该是ex的pc，就是当时的pc
  //   数码管输出
  //   只有出错才会用到这个
  //   指令存储器
  //   控制位
  //   指令探针
  //   contents of rom_1 (hex, n*v repeats v):
  //   100493 100006f 100493 200913 300993 100006f 100493 200913 300993 100006f 100493 200913 300993
  //   100006f 100493 200913 300993 29c000ef 100413 100493 1f49493 900533 2200893 73 24d493 48463 fedff06f
  //   900533 2200893 73 100493 249493 900533 2200893 73 48463 fedff06f 100493 1f49493 900533 2200893 73
  //   4034d493 900533 2200893 73 4044d493 900533 2200893 73 4044d493 900533 2200893 73 4044d493 900533
  //   2200893 73 4044d493 900533 2200893 73 4044d493 900533 2200893 73 4044d493 900533 2200893 73 4044d493
  //   900533 2200893 73 100413 1f41993 41f9d993 433 c00913 300b13 140413 f47413 800293 100313 499993
  //   89e9b3 1300533 2200893 73 406282b3 fe0294e3 140413 f00f93 1f47433 1c41413 800293 100313 49d993
  //   89e9b3 1300533 2200893 73 406282b3 fe0294e3 1c45413 406b0b33 b0463 f95ff06f 2b3 fff2c293 829293
  //   ff2e293 500533 2200893 73 fff00413 493 84a023 140413 448493 84a023 140413 448493 84a023 140413
  //   448493 84a023 140413 448493 84a023 140413 448493 84a023 140413 448493 84a023 140413 448493 84a023
  //   140413 448493 84a023 140413 448493 84a023 140413 448493 84a023 140413 448493 84a023 140413 448493
  //   84a023 140413 448493 84a023 140413 448493 84a023 140413 448493 84a023 140413 448493 140413 433
  //   3c00493 42983 4aa03 149a2b3 28663 134a023 1442023 ffc48493 fe9412e3 800533 2200893 73 440413 3c00493
  //   fc9416e3 a00893 73 413 140413 800533 2200893 73 240413 800533 2200893 73 340413 800533 2200893 73
  //   440413 800533 2200893 73 540413 800533 2200893 73 640413 800533 2200893 73 740413 800533 2200893 73
  //   840413 800533 2200893 2200893 73 8067
  //   流水调试日志用
  //   暂停节拍，不能为0
  //   戳工具置1进入计数暂停模式，ctrl+k时钟自动运行到对应节拍暂停
  //   ctrl+k关闭时钟连续运行，将控制位置零，进入单步调试模式调试
  //   正常情况下，我们需要的值都在后面两个寄存器，但是我们如果是lb或者lw，我们的写回数据在寄存器中，如何区分呢，通过memtoreg
  //   判断是否要跳转
  //   可计数暂停的时钟源
  //   ex段的跳转地址
  //   指令字
  //   b型
  //   j型
  //   JALR
  //   URET
  //   Beq
  //   Bne
  //   MemToReg
  //   MemWrite
  //   AluOP
  //   AluSrcB
  //   RegWrite
  //   为方便自动评测，需要输出流水线各段保存的PC值，注意是PC不是PC+4，另外ID段寄存器写入信息，Mem段内存写入信息也要输出
  //   R2
  //   aluop
  //   rd
  //   rs1_foward
  //   rs2_foward
  //   发现这个填0也是能过的
  //   JAL
  //   JALR
  //   PC_4
  //   Aluout
  //   MemtoReg
  //   is_lb
  //   MemWrite
  //   处理sw
  //   数据存储器
  //   写回寄存器有四种情况，R型，jalrjal，lb
  //   R地址
  //   Rdata
  //   Aluout
  //   写回data
endmodule

module BTB (
  input  [31:0] PC,
  input  [31:0] EX_PC,
  input  [31:0] EX_BranchAddr,
  input  EX_Branch,
  input  EX_Branched,
  input  in_6,
  output IF_PredictJump,
  output [31:0] BTB_JumpAddr
);

  wire and_17_out, and_26_out, and_27_out, and_28_out, and_29_out, and_30_out, and_31_out, and_32_out,
       and_33_out, comparator_1_eq, comparator_2_eq, comparator_3_eq, comparator_4_eq, comparator_5_eq,
       comparator_6_eq, comparator_7_eq, comparator_8_eq, comparator_9_eq, comparator_10_eq,
       comparator_11_eq, comparator_12_eq, comparator_13_eq, comparator_14_eq, comparator_15_eq,
       comparator_16_eq, d_ff_1_q, d_ff_2_q, d_ff_3_q, d_ff_4_q, d_ff_5_q, d_ff_6_q, d_ff_7_q, d_ff_8_q,
       decoder_1_out0, decoder_1_out1, decoder_1_out2, decoder_1_out3, decoder_1_out4, decoder_1_out5,
       decoder_1_out6, decoder_1_out7, decoder_2_out0, decoder_2_out1, decoder_2_out2, decoder_2_out3,
       decoder_2_out4, decoder_2_out5, decoder_2_out6, decoder_2_out7, EX_Hit, EX_Miss, L0, L1, L2, L3, L4,
       L5, L6, L7, M0, M1, M2, M3, M4, M5, M6, M7, not_1_out, not_2_out, not_3_out, not_4_out, not_5_out,
       not_6_out, not_7_out, not_8_out, or_1_out, or_2_out, or_3_out, or_4_out, or_5_out, or_6_out, or_7_out,
       or_8_out, or_10_out, or_11_out, or_12_out, or_13_out, or_14_out, or_15_out, or_16_out, or_17_out,
       priority_encoder_1_gs, v0, v1, v2, v3, v4, v5, v6, v7, write0, write1, write2, write3, write4, write5,
       write6, write7;
  wire [0:0] controlled_buffer_9_out, controlled_buffer_10_out, controlled_buffer_11_out,
       controlled_buffer_12_out, controlled_buffer_13_out, controlled_buffer_14_out,
       controlled_buffer_15_out, controlled_buffer_16_out;
  wire [1:0] fsm_1_nextlow, fsm_2_nextlow, fsm_3_nextlow, fsm_4_nextlow, fsm_5_nextlow, fsm_6_nextlow,
       fsm_7_nextlow, fsm_8_nextlow, predict0, predict1, predict2, predict3, predict4, predict5, predict6,
       predict7;
  wire [2:0] max_1_max_num, max_2_max_num, max_3_max_num, max_4_max_num, max_5_max_num, max_6_max_num,
       max_7_max_num, priority_encoder_1_out;
  wire [15:0] c0, c1, c2, c3, c4, c5, c6, c7, max_1_max, max_2_max, max_3_max, max_4_max, max_5_max,
       max_6_max;
  wire [31:0] register_17_q, register_18_q, register_19_q, register_20_q, register_21_q, register_22_q,
       register_23_q, register_24_q, tag0, tag1, tag2, tag3, tag4, tag5, tag6, tag7;

  LED #(.active("true")) led_1 (.in(v0));
  Register #(.width(1), .trigger("rising"), .Select("low")) register_1 (
    .D(1'b1), .en(write0), .Q(v0), .clk(in_6));  // open: clr
  LED #(.active("true")) led_2 (.in(v1));
  Register #(.width(1), .trigger("rising"), .Select("low")) register_2 (
    .D(1'b1), .en(write1), .Q(v1), .clk(in_6));  // open: clr
  LED #(.active("true")) led_3 (.in(v2));
  Register #(.width(1), .trigger("rising"), .Select("low")) register_3 (
    .D(1'b1), .en(write2), .Q(v2), .clk(in_6));  // open: clr
  LED #(.active("true")) led_4 (.in(v3));
  Register #(.width(1), .trigger("rising"), .Select("low")) register_4 (
    .D(1'b1), .en(write3), .Q(v3), .clk(in_6));  // open: clr
  LED #(.active("true")) led_5 (.in(v4));
  Register #(.width(1), .trigger("rising"), .Select("low")) register_5 (
    .D(1'b1), .en(write4), .Q(v4), .clk(in_6));  // open: clr
  LED #(.active("true")) led_6 (.in(v5));
  Register #(.width(1), .trigger("rising"), .Select("low")) register_6 (
    .D(1'b1), .en(write5), .Q(v5), .clk(in_6));  // open: clr
  LED #(.active("true")) led_7 (.in(v6));
  Register #(.width(1), .trigger("rising"), .Select("low")) register_7 (
    .D(1'b1), .en(write6), .Q(v6), .clk(in_6));  // open: clr
  Register #(.width(1), .trigger("rising"), .Select("low")) register_8 (
    .D(1'b1), .en(write7), .Q(v7), .clk(in_6));  // open: clr
  LED #(.active("true")) led_8 (.in(v7));
  // Probe on tag0
  Register #(.width(32), .trigger("rising"), .Select("low")) register_9 (
    .D(EX_PC), .en(write0), .Q(tag0), .clk(in_6));  // open: clr
  // Probe on tag1
  Register #(.width(32), .trigger("rising"), .Select("low")) register_10 (
    .D(EX_PC), .en(write1), .Q(tag1), .clk(in_6));  // open: clr
  // Probe on tag2
  Register #(.width(32), .trigger("rising"), .Select("low")) register_11 (
    .D(EX_PC), .en(write2), .Q(tag2), .clk(in_6));  // open: clr
  // Probe on tag3
  Register #(.width(32), .trigger("rising"), .Select("low")) register_12 (
    .D(EX_PC), .en(write3), .Q(tag3), .clk(in_6));  // open: clr
  // Probe on tag4
  Register #(.width(32), .trigger("rising"), .Select("low")) register_13 (
    .D(EX_PC), .en(write4), .Q(tag4), .clk(in_6));  // open: clr
  // Probe on tag5
  Register #(.width(32), .trigger("rising"), .Select("low")) register_14 (
    .D(EX_PC), .en(write5), .Q(tag5), .clk(in_6));  // open: clr
  Register #(.width(32), .trigger("rising"), .Select("low")) register_15 (
    .D(EX_PC), .en(write6), .Q(tag6), .clk(in_6));  // open: clr
  // Probe on tag7
  Register #(.width(32), .trigger("rising"), .Select("low")) register_16 (
    .D(EX_PC), .en(write7), .Q(tag7), .clk(in_6));  // open: clr
  // Probe on tag6
  Counter #(.width(16), .max('hffff), .ongoal("wrap"), .trigger("rising"), .behavior("old")) counter_1 (
    .Q(c0), .clk(in_6), .clr(d_ff_3_q));  // open: load, D, count, carry, preset
  or or_1 (or_1_out, write0, L0);
  Counter #(.width(16), .max('hffff), .ongoal("wrap"), .trigger("rising"), .behavior("old")) counter_2 (
    .Q(c1), .clk(in_6), .clr(d_ff_4_q));  // open: load, D, count, carry, preset
  or or_2 (or_2_out, write1, L1);
  Counter #(.width(16), .max('hffff), .ongoal("wrap"), .trigger("rising"), .behavior("old")) counter_3 (
    .Q(c2), .clk(in_6), .clr(d_ff_5_q));  // open: load, D, count, carry, preset
  or or_3 (or_3_out, write2, L2);
  Counter #(.width(16), .max('hffff), .ongoal("wrap"), .trigger("rising"), .behavior("old")) counter_4 (
    .Q(c3), .clk(in_6), .clr(d_ff_6_q));  // open: load, D, count, carry, preset
  or or_4 (or_4_out, write3, L3);
  Counter #(.width(16), .max('hffff), .ongoal("wrap"), .trigger("rising"), .behavior("old")) counter_5 (
    .Q(c4), .clk(in_6), .clr(d_ff_1_q));  // open: load, D, count, carry, preset
  D_Flip_Flop #(.trigger("rising"), .Pre_Clr_Positions("LEGACY"), .NegatePresetClear("false"), .enable("true"), .NewFFLayout("false")) d_ff_1 (
    .clk(in_6), .D(or_5_out), .Q(d_ff_1_q));  // open: Qn, preset, en, reset
  or or_5 (or_5_out, write4, L4);
  Counter #(.width(16), .max('hffff), .ongoal("wrap"), .trigger("rising"), .behavior("old")) counter_6 (
    .Q(c5), .clk(in_6), .clr(d_ff_7_q));  // open: load, D, count, carry, preset
  or or_6 (or_6_out, write5, L5);
  Counter #(.width(16), .max('hffff), .ongoal("wrap"), .trigger("rising"), .behavior("old")) counter_7 (
    .Q(c6), .clk(in_6), .clr(d_ff_8_q));  // open: load, D, count, carry, preset
  or or_7 (or_7_out, write6, L6);
  Counter #(.width(16), .max('hffff), .ongoal("wrap"), .trigger("rising"), .behavior("old")) counter_8 (
    .Q(c7), .clk(in_6), .clr(d_ff_2_q));  // open: load, D, count, carry, preset
  D_Flip_Flop #(.trigger("rising"), .Pre_Clr_Positions("LEGACY"), .NegatePresetClear("false"), .enable("true"), .NewFFLayout("false")) d_ff_2 (
    .clk(in_6), .D(or_8_out), .Q(d_ff_2_q));  // open: Qn, preset, en, reset
  or or_8 (or_8_out, write7, L7);
  D_Flip_Flop #(.trigger("rising"), .Pre_Clr_Positions("LEGACY"), .NegatePresetClear("false"), .enable("true"), .NewFFLayout("false")) d_ff_3 (
    .clk(in_6), .D(or_1_out), .Q(d_ff_3_q));  // open: Qn, preset, en, reset
  D_Flip_Flop #(.trigger("rising"), .Pre_Clr_Positions("LEGACY"), .NegatePresetClear("false"), .enable("true"), .NewFFLayout("false")) d_ff_4 (
    .clk(in_6), .D(or_2_out), .Q(d_ff_4_q));  // open: Qn, preset, en, reset
  D_Flip_Flop #(.trigger("rising"), .Pre_Clr_Positions("LEGACY"), .NegatePresetClear("false"), .enable("true"), .NewFFLayout("false")) d_ff_5 (
    .clk(in_6), .D(or_3_out), .Q(d_ff_5_q));  // open: Qn, preset, en, reset
  D_Flip_Flop #(.trigger("rising"), .Pre_Clr_Positions("LEGACY"), .NegatePresetClear("false"), .enable("true"), .NewFFLayout("false")) d_ff_6 (
    .clk(in_6), .D(or_4_out), .Q(d_ff_6_q));  // open: Qn, preset, en, reset
  D_Flip_Flop #(.trigger("rising"), .Pre_Clr_Positions("LEGACY"), .NegatePresetClear("false"), .enable("true"), .NewFFLayout("false")) d_ff_7 (
    .clk(in_6), .D(or_6_out), .Q(d_ff_7_q));  // open: Qn, preset, en, reset
  D_Flip_Flop #(.trigger("rising"), .Pre_Clr_Positions("LEGACY"), .NegatePresetClear("false"), .enable("true"), .NewFFLayout("false")) d_ff_8 (
    .clk(in_6), .D(or_7_out), .Q(d_ff_8_q));  // open: Qn, preset, en, reset
  Register #(.width(32), .trigger("rising"), .Select("low")) register_17 (
    .D(EX_BranchAddr), .en(write0), .Q(register_17_q), .clk(in_6));  // open: clr
  Register #(.width(32), .trigger("rising"), .Select("low")) register_18 (
    .D(EX_BranchAddr), .en(write1), .Q(register_18_q), .clk(in_6));  // open: clr
  Register #(.width(32), .trigger("rising"), .Select("low")) register_19 (
    .D(EX_BranchAddr), .en(write2), .Q(register_19_q), .clk(in_6));  // open: clr
  Register #(.width(32), .trigger("rising"), .Select("low")) register_20 (
    .D(EX_BranchAddr), .en(write3), .Q(register_20_q), .clk(in_6));  // open: clr
  Register #(.width(32), .trigger("rising"), .Select("low")) register_21 (
    .D(EX_BranchAddr), .en(write4), .Q(register_21_q), .clk(in_6));  // open: clr
  Register #(.width(32), .trigger("rising"), .Select("low")) register_22 (
    .D(EX_BranchAddr), .en(write5), .Q(register_22_q), .clk(in_6));  // open: clr
  Register #(.width(32), .trigger("rising"), .Select("low")) register_23 (
    .D(EX_BranchAddr), .en(write6), .Q(register_23_q), .clk(in_6));  // open: clr
  Register #(.width(32), .trigger("rising"), .Select("low")) register_24 (
    .D(EX_BranchAddr), .en(write7), .Q(register_24_q), .clk(in_6));  // open: clr
  assign BTB_JumpAddr = L0 ? register_17_q : 32'bz;  // Controlled_Buffer controlled_buffer_1
  assign BTB_JumpAddr = L1 ? register_18_q : 32'bz;  // Controlled_Buffer controlled_buffer_2
  assign BTB_JumpAddr = L2 ? register_19_q : 32'bz;  // Controlled_Buffer controlled_buffer_3
  assign BTB_JumpAddr = L3 ? register_20_q : 32'bz;  // Controlled_Buffer controlled_buffer_4
  assign BTB_JumpAddr = L4 ? register_21_q : 32'bz;  // Controlled_Buffer controlled_buffer_5
  assign BTB_JumpAddr = L5 ? register_22_q : 32'bz;  // Controlled_Buffer controlled_buffer_6
  assign BTB_JumpAddr = L6 ? register_23_q : 32'bz;  // Controlled_Buffer controlled_buffer_7
  assign BTB_JumpAddr = L7 ? register_24_q : 32'bz;  // Controlled_Buffer controlled_buffer_8
  Comparator #(.width(32), .mode("twosComplement")) comparator_1 (
    .a(tag0), .b(PC), .eq(comparator_1_eq));  // open: gt, lt
  Comparator #(.width(32), .mode("twosComplement")) comparator_2 (
    .a(tag1), .b(PC), .eq(comparator_2_eq));  // open: gt, lt
  Comparator #(.width(32), .mode("twosComplement")) comparator_3 (
    .a(tag2), .b(PC), .eq(comparator_3_eq));  // open: gt, lt
  Comparator #(.width(32), .mode("twosComplement")) comparator_4 (
    .a(tag3), .b(PC), .eq(comparator_4_eq));  // open: gt, lt
  Comparator #(.width(32), .mode("twosComplement")) comparator_5 (
    .a(tag4), .b(PC), .eq(comparator_5_eq));  // open: gt, lt
  Comparator #(.width(32), .mode("twosComplement")) comparator_6 (
    .a(tag5), .b(PC), .eq(comparator_6_eq));  // open: gt, lt
  Comparator #(.width(32), .mode("twosComplement")) comparator_7 (
    .a(tag6), .b(PC), .eq(comparator_7_eq));  // open: gt, lt
  Comparator #(.width(32), .mode("twosComplement")) comparator_8 (
    .a(tag7), .b(PC), .eq(comparator_8_eq));  // open: gt, lt
  and and_1 (L0, v0, comparator_1_eq);
  and and_2 (L1, v1, comparator_2_eq);
  and and_3 (L2, v2, comparator_3_eq);
  and and_4 (L3, v3, comparator_4_eq);
  and and_5 (L4, v4, comparator_5_eq);
  and and_6 (L5, v5, comparator_6_eq);
  and and_7 (L6, v6, comparator_7_eq);
  and and_8 (L7, v7, comparator_8_eq);
  Comparator #(.width(32), .mode("twosComplement")) comparator_9 (
    .a(tag0), .b(EX_PC), .eq(comparator_9_eq));  // open: gt, lt
  Comparator #(.width(32), .mode("twosComplement")) comparator_10 (
    .a(tag1), .b(EX_PC), .eq(comparator_10_eq));  // open: gt, lt
  Comparator #(.width(32), .mode("twosComplement")) comparator_11 (
    .a(tag2), .b(EX_PC), .eq(comparator_11_eq));  // open: gt, lt
  Comparator #(.width(32), .mode("twosComplement")) comparator_12 (
    .a(tag3), .b(EX_PC), .eq(comparator_12_eq));  // open: gt, lt
  Comparator #(.width(32), .mode("twosComplement")) comparator_13 (
    .a(tag4), .b(EX_PC), .eq(comparator_13_eq));  // open: gt, lt
  Comparator #(.width(32), .mode("twosComplement")) comparator_14 (
    .a(tag5), .b(EX_PC), .eq(comparator_14_eq));  // open: gt, lt
  Comparator #(.width(32), .mode("twosComplement")) comparator_15 (
    .a(tag6), .b(EX_PC), .eq(comparator_15_eq));  // open: gt, lt
  Comparator #(.width(32), .mode("twosComplement")) comparator_16 (
    .a(tag7), .b(EX_PC), .eq(comparator_16_eq));  // open: gt, lt
  and and_9 (M0, v0, comparator_9_eq);
  and and_10 (M1, v1, comparator_10_eq);
  and and_11 (M2, v2, comparator_11_eq);
  and and_12 (M3, v3, comparator_12_eq);
  and and_13 (M4, v4, comparator_13_eq);
  and and_14 (M5, v5, comparator_14_eq);
  and and_15 (M6, v6, comparator_15_eq);
  and and_16 (M7, v7, comparator_16_eq);
  MAX max_1 (.Y(c1), .X(c0), .Y_num(3'b001), .X_num(3'b000), .MAX(max_1_max), .Max_num(max_1_max_num));
  MAX max_2 (.Y(c3), .X(c2), .Y_num(3'b011), .X_num(3'b010), .MAX(max_2_max), .Max_num(max_2_max_num));
  MAX max_3 (.Y(c5), .X(c4), .Y_num(3'b101), .X_num(3'b100), .MAX(max_3_max), .Max_num(max_3_max_num));
  MAX max_4 (.Y(c7), .X(c6), .Y_num(3'b111), .X_num(3'b110), .MAX(max_4_max), .Max_num(max_4_max_num));
  not not_1 (not_1_out, v0);
  not not_2 (not_2_out, v1);
  not not_3 (not_3_out, v2);
  not not_4 (not_4_out, v3);
  not not_5 (not_5_out, v4);
  not not_6 (not_6_out, v5);
  not not_7 (not_7_out, v6);
  not not_8 (not_8_out, v7);
  and and_17 (and_17_out, v0, v1, v2, v3, v4, v5, v6, v7);
  MAX max_5 (
    .Y(max_2_max), .X(max_1_max), .Y_num(max_2_max_num), .X_num(max_1_max_num), .MAX(max_5_max),
    .Max_num(max_5_max_num));
  MAX max_6 (
    .Y(max_4_max), .X(max_3_max), .Y_num(max_4_max_num), .X_num(max_3_max_num), .MAX(max_6_max),
    .Max_num(max_6_max_num));
  or or_9 (EX_Hit, M0, M1, M2, M3, M4, M5, M6, M7);
  not not_9 (EX_Miss, EX_Hit);
  Priority_Encoder #(.select(3), .disabled("Z")) priority_encoder_1 (
    .in0(not_1_out), .in1(not_2_out), .in2(not_3_out), .in3(not_4_out), .in4(not_5_out), .in5(not_6_out),
    .in6(not_7_out), .in7(not_8_out), .out(priority_encoder_1_out), .gs(priority_encoder_1_gs));  // open: en_out, en_in
  MAX max_7 (
    .Y(max_6_max), .X(max_5_max), .Y_num(max_6_max_num), .X_num(max_5_max_num), .Max_num(max_7_max_num));  // open: MAX
  Decoder #(.select(3), .tristate("false"), .disabled(0), .enable("true")) decoder_1 (
    .out0(decoder_1_out0), .out1(decoder_1_out1), .out2(decoder_1_out2), .out3(decoder_1_out3),
    .out4(decoder_1_out4), .out5(decoder_1_out5), .out6(decoder_1_out6), .out7(decoder_1_out7),
    .sel(priority_encoder_1_out), .en(priority_encoder_1_gs));
  Decoder #(.select(3), .tristate("false"), .disabled(0), .enable("true")) decoder_2 (
    .out0(decoder_2_out0), .out1(decoder_2_out1), .out2(decoder_2_out2), .out3(decoder_2_out3),
    .out4(decoder_2_out4), .out5(decoder_2_out5), .out6(decoder_2_out6), .out7(decoder_2_out7),
    .sel(max_7_max_num), .en(and_17_out));
  or or_10 (or_10_out, decoder_1_out0, decoder_2_out0);
  or or_11 (or_11_out, decoder_1_out1, decoder_2_out1);
  or or_12 (or_12_out, decoder_1_out2, decoder_2_out2);
  or or_13 (or_13_out, decoder_1_out3, decoder_2_out3);
  or or_14 (or_14_out, decoder_1_out4, decoder_2_out4);
  or or_15 (or_15_out, decoder_1_out5, decoder_2_out5);
  or or_16 (or_16_out, decoder_1_out6, decoder_2_out6);
  or or_17 (or_17_out, decoder_1_out7, decoder_2_out7);
  and and_18 (write0, or_10_out, EX_Miss, EX_Branch);
  and and_19 (write1, or_11_out, EX_Miss, EX_Branch);
  and and_20 (write2, or_12_out, EX_Miss, EX_Branch);
  and and_21 (write3, or_13_out, EX_Miss, EX_Branch);
  and and_22 (write4, or_14_out, EX_Miss, EX_Branch);
  and and_23 (write5, or_15_out, EX_Miss, EX_Branch);
  and and_24 (write6, or_16_out, EX_Miss, EX_Branch);
  and and_25 (write7, or_17_out, EX_Miss, EX_Branch);
  assign {IF_PredictJump, controlled_buffer_9_out[0]} = L0 ? predict0 : 2'bz;  // Controlled_Buffer controlled_buffer_9
  assign {IF_PredictJump, controlled_buffer_10_out[0]} = L1 ? predict1 : 2'bz;  // Controlled_Buffer controlled_buffer_10
  assign {IF_PredictJump, controlled_buffer_11_out[0]} = L2 ? predict2 : 2'bz;  // Controlled_Buffer controlled_buffer_11
  assign {IF_PredictJump, controlled_buffer_12_out[0]} = L3 ? predict3 : 2'bz;  // Controlled_Buffer controlled_buffer_12
  assign {IF_PredictJump, controlled_buffer_13_out[0]} = L4 ? predict4 : 2'bz;  // Controlled_Buffer controlled_buffer_13
  assign {IF_PredictJump, controlled_buffer_14_out[0]} = L5 ? predict5 : 2'bz;  // Controlled_Buffer controlled_buffer_14
  assign {IF_PredictJump, controlled_buffer_15_out[0]} = L6 ? predict6 : 2'bz;  // Controlled_Buffer controlled_buffer_15
  assign {IF_PredictJump, controlled_buffer_16_out[0]} = L7 ? predict7 : 2'bz;  // Controlled_Buffer controlled_buffer_16
  Pull_Resistor #(.pull(0)) pull_resistor_1 (.node(IF_PredictJump));
  FSM fsm_1 (
    .high(predict0[1]), .low(predict0[0]), .jump(EX_Branched), .NextHigh(fsm_1_nextlow[1]),
    .NextLow(fsm_1_nextlow[0]));
  FSM fsm_2 (
    .high(predict1[1]), .low(predict1[0]), .jump(EX_Branched), .NextHigh(fsm_2_nextlow[1]),
    .NextLow(fsm_2_nextlow[0]));
  FSM fsm_3 (
    .high(predict2[1]), .low(predict2[0]), .jump(EX_Branched), .NextHigh(fsm_3_nextlow[1]),
    .NextLow(fsm_3_nextlow[0]));
  FSM fsm_4 (
    .high(predict3[1]), .low(predict3[0]), .jump(EX_Branched), .NextHigh(fsm_4_nextlow[1]),
    .NextLow(fsm_4_nextlow[0]));
  FSM fsm_5 (
    .high(predict4[1]), .low(predict4[0]), .jump(EX_Branched), .NextHigh(fsm_5_nextlow[1]),
    .NextLow(fsm_5_nextlow[0]));
  FSM fsm_6 (
    .high(predict5[1]), .low(predict5[0]), .jump(EX_Branched), .NextHigh(fsm_6_nextlow[1]),
    .NextLow(fsm_6_nextlow[0]));
  FSM fsm_7 (
    .high(predict6[1]), .low(predict6[0]), .jump(EX_Branched), .NextHigh(fsm_7_nextlow[1]),
    .NextLow(fsm_7_nextlow[0]));
  FSM fsm_8 (
    .high(predict7[1]), .low(predict7[0]), .jump(EX_Branched), .NextHigh(fsm_8_nextlow[1]),
    .NextLow(fsm_8_nextlow[0]));
  and and_26 (and_26_out, EX_Branch, M0);
  Register #(.width(2), .trigger("rising"), .Select("low")) register_25 (
    .D(fsm_1_nextlow), .en(and_26_out), .Q(predict0), .clk(in_6));  // open: clr
  and and_27 (and_27_out, EX_Branch, M1);
  Register #(.width(2), .trigger("rising"), .Select("low")) register_26 (
    .D(fsm_2_nextlow), .en(and_27_out), .Q(predict1), .clk(in_6));  // open: clr
  and and_28 (and_28_out, EX_Branch, M2);
  Register #(.width(2), .trigger("rising"), .Select("low")) register_27 (
    .D(fsm_3_nextlow), .en(and_28_out), .Q(predict2), .clk(in_6));  // open: clr
  and and_29 (and_29_out, EX_Branch, M3);
  Register #(.width(2), .trigger("rising"), .Select("low")) register_28 (
    .D(fsm_4_nextlow), .en(and_29_out), .Q(predict3), .clk(in_6));  // open: clr
  and and_30 (and_30_out, EX_Branch, M4);
  Register #(.width(2), .trigger("rising"), .Select("low")) register_29 (
    .D(fsm_5_nextlow), .en(and_30_out), .Q(predict4), .clk(in_6));  // open: clr
  and and_31 (and_31_out, EX_Branch, M5);
  Register #(.width(2), .trigger("rising"), .Select("low")) register_30 (
    .D(fsm_6_nextlow), .en(and_31_out), .Q(predict5), .clk(in_6));  // open: clr
  and and_32 (and_32_out, EX_Branch, M6);
  Register #(.width(2), .trigger("rising"), .Select("low")) register_31 (
    .D(fsm_7_nextlow), .en(and_32_out), .Q(predict6), .clk(in_6));  // open: clr
  and and_33 (and_33_out, EX_Branch, M7);
  Register #(.width(2), .trigger("rising"), .Select("low")) register_32 (
    .D(fsm_8_nextlow), .en(and_33_out), .Q(predict7), .clk(in_6));  // open: clr

  // Other names for the same wires on the sheet: CLK = in_6; Tag[31:0] = EX_PC

  // Notes on the sheet:
  //   wrote是写使能信号，当我们选中这一行的时候才写入
  //   tag相等并且是有效的时候
  //   EX的pc相等且有效的时候
  //   命中信号
  //   命中且ex段有分支的时候才会更新btb
  //   历史预测位
  //   与PC比较数据命中  选择L而不是M
  //   EX.PC如果数据命中，需要根据EX.Branched的值依据预测位状态机更新分支预测历史位的值
endmodule

module MAX (
  input  [15:0] Y,
  input  [15:0] X,
  input  [2:0] Y_num,
  input  [2:0] X_num,
  output [15:0] MAX,
  output [2:0] Max_num
);

  wire comparator_1_eq, comparator_1_gt, or_1_out;

  Comparator #(.width(16), .mode("unsigned")) comparator_1 (
    .a(X), .b(Y), .gt(comparator_1_gt), .eq(comparator_1_eq));  // open: lt
  Multiplexer #(.select(1), .width(16), .disabled("Z"), .enable("false")) multiplexer_1 (
    .in0(Y), .in1(X), .out(MAX), .sel(or_1_out));
  or or_1 (or_1_out, comparator_1_gt, comparator_1_eq);
  Multiplexer #(.select(1), .width(3), .disabled("Z"), .enable("false")) multiplexer_2 (
    .in0(Y_num), .in1(X_num), .out(Max_num), .sel(or_1_out));

  // Notes on the sheet:
  //   输出两个输入中的较大值，并输出较大值的3位编号
endmodule

module FSM (
  input  high,
  input  low,
  input  jump,
  output NextHigh,
  output NextLow
);

  wire and_1_out, and_2_out, and_3_out, and_4_out, not_1_out, not_2_out, not_3_out, not_4_out, not_5_out;

  not not_1 (not_1_out, low);
  not not_2 (not_2_out, high);
  not not_3 (not_3_out, low);
  not not_4 (not_4_out, low);
  not not_5 (not_5_out, jump);
  and and_1 (and_1_out, low, jump);
  and and_2 (and_2_out, high, not_1_out);
  and and_3 (and_3_out, not_2_out, not_3_out, jump);
  and and_4 (and_4_out, high, not_4_out, not_5_out);
  or or_1 (NextHigh, and_1_out, and_2_out);
  or or_2 (NextLow, and_3_out, and_4_out);
endmodule
